// Logisim project Guia05.circ as structural Verilog: 6 circuits, main circuit Exemplo_0502
module Exemplo_0502 (
  input  a,
  input  a_2,
  input  b,
  input  b_2,
  output \output ,
  output output_2
);

  wire nand_1_out, nand_2_out, not_1_out;

  not not_1 (not_1_out, a);
  and and_1 (\output , not_1_out, b);
  nand nand_1 (nand_1_out, a_2, b_2);
  nand nand_2 (nand_2_out, b_2, b_2);
  nand nand_3 (output_2, nand_1_out, nand_2_out);

  // Notes on the sheet:
  //   Circuito (~a & b)
  //   Mesmo circuito so que com portas NAND
endmodule

module Exemplo_0503 (
  input  a,
  input  a_2,
  input  b,
  input  b_2,
  output \output ,
  output output_2
);

  wire nor_1_out, nor_2_out, nor_3_out, not_out;

  not \not  (not_out, b_2);
  or \or  (\output , a_2, not_out);
  nor nor_1 (nor_1_out, b, b);
  nor nor_2 (nor_2_out, a, nor_1_out);
  nor nor_3 (nor_3_out, nor_1_out, nor_1_out);
  nor nor_4 (output_2, nor_2_out, nor_3_out);

  // Notes on the sheet:
  //   circuito (a | ~b)
  //   mesmo circuito usando portas NOR
endmodule

module Exemplo_0504 (
  input  in_1,
  input  a,
  input  in_3,
  input  b,
  output \output ,
  output output_2
);

  wire not_1_out, not_2_out;

  not not_1 (not_1_out, a);
  not not_2 (not_2_out, b);
  or \or  (output_2, not_1_out, not_2_out);
  nand \nand  (\output , in_1, in_3);

  // Notes on the sheet:
  //   circuito (~a|~b)
  //   mesmo circuito usando porta NAND
endmodule

module Exemplo_0505 (
  input  a,
  input  a_2,
  input  b,
  input  b_2,
  output \output ,
  output output_2
);

  wire nor_2_out, nor_3_out, nor_out, not_1_out, not_2_out;

  not not_1 (not_1_out, a_2);
  not not_2 (not_2_out, b);
  and \and  (\output , not_1_out, not_2_out);
  nor \nor  (nor_out, a, a);
  nor nor_2 (nor_2_out, b_2, b_2);
  nor nor_3 (nor_3_out, nor_out, nor_2_out);
  nor nor_4 (output_2, nor_3_out, nor_3_out);

  // Notes on the sheet:
  //   Circuito (~a & ~b) 
  //   mesmo circuito usando nor
endmodule

module Exemplo_0506 (
  input  a,
  input  a_2,
  input  b,
  input  b_2,
  output \output ,
  output output_2
);

  wire nand_2_out, nand_3_out, nand_4_out, nand_out;

  xnor xnor_1 (\output , a_2, b);
  nand \nand  (nand_out, a, b_2);
  nand nand_2 (nand_2_out, a, a);
  nand nand_3 (nand_3_out, nand_2_out, nand_4_out);
  nand nand_4 (nand_4_out, b_2, b_2);
  nand nand_5 (output_2, nand_out, nand_3_out);

  // Notes on the sheet:
  //   circuito ~(a^b)
endmodule

module Exemplo_0507 (
  input  a,
  input  a_2,
  input  b,
  input  b_2,
  output \output ,
  output output_2
);

  wire nor_1_out, nor_2_out, nor_3_out, nor_4_out;

  xor \xor  (\output , a_2, b_2);
  nor nor_1 (nor_1_out, a, a);
  nor nor_2 (nor_2_out, nor_1_out, nor_3_out);
  nor nor_3 (nor_3_out, b, b);
  nor nor_4 (nor_4_out, b, a);
  nor nor_5 (output_2, nor_2_out, nor_4_out);

  // Notes on the sheet:
  //   circuito (a ^ b)
endmodule
