// Logisim project guia07.circ as structural Verilog: 7 circuits, main circuit guia0701
module guia0701 (
  input  x,
  input  y,
  input  in_3,
  output out_4
);

  wire and_1_out, nand_1_out;

  and and_1 (and_1_out, x, y);
  nand nand_1 (nand_1_out, y, x);
  Multiplexer #(.enable("false")) multiplexer_1 (.in0(and_1_out), .in1(nand_1_out), .out(out_4), .sel(in_3));
endmodule

module teste_decoder (
  input  a,
  input  b,
  output s1,
  output s2,
  output s3,
  output s4
);

  wire not_1_out, not_2_out;

  not not_1 (not_1_out, a);
  not not_2 (not_2_out, b);
  and and_1 (s1, not_2_out, not_1_out);
  and and_2 (s2, b, not_1_out);
  and and_3 (s3, not_2_out, a);
  and and_4 (s4, b, a);

  // Notes on the sheet:
  //   Teste Decoder
endmodule

module my_multiplexer (
  input  x,
  input  y,
  input  e,
  output s
);

  wire and_1_out, and_2_out, not_1_out;

  not not_1 (not_1_out, e);
  and and_1 (and_1_out, x, e);
  and and_2 (and_2_out, y, not_1_out);
  or or_1 (s, and_1_out, and_2_out);
endmodule

module guia0702 (
  input  x,
  input  y,
  input  in_3,
  output out_4,
  output out_5,
  output out_6
);

  or or_1 (out_4, x, y);
  nor nor_1 (out_5, y, x);
  Multiplexer #(.enable("false")) multiplexer_1 (.in0(out_5), .in1(out_4), .out(out_6), .sel(in_3));
endmodule

module guia0703 (
  input  x,
  input  y,
  input  in_3,
  input  in_4,
  input  in_5,
  output out_6
);

  wire and_1_out, multiplexer_1_out, multiplexer_2_out, nand_1_out, nor_1_out, or_1_out;

  and and_1 (and_1_out, x, y);
  nand nand_1 (nand_1_out, y, x);
  or or_1 (or_1_out, x, y);
  nor nor_1 (nor_1_out, y, x);
  Multiplexer #(.enable("false")) multiplexer_1 (
    .in0(and_1_out), .in1(nand_1_out), .out(multiplexer_1_out), .sel(in_3));
  Multiplexer #(.enable("false")) multiplexer_2 (.in0(or_1_out), .in1(nor_1_out), .out(multiplexer_2_out), .sel(in_4));
  Multiplexer #(.enable("false")) multiplexer_3 (
    .in0(multiplexer_1_out), .in1(multiplexer_2_out), .out(out_6), .sel(in_5));
endmodule

module guia0704 (
  input  x,
  input  y,
  input  [1:0] in_3,
  output out_4
);

  wire nor_1_out, or_1_out, xnor_1_out, xor_1_out;

  xor xor_1 (xor_1_out, x, y);
  or or_1 (or_1_out, x, y);
  nor nor_1 (nor_1_out, y, x);
  xnor xnor_1 (xnor_1_out, y, x);
  Multiplexer #(.select(2), .enable("false")) multiplexer_1 (
    .in0(xor_1_out), .in1(xnor_1_out), .in2(or_1_out), .in3(nor_1_out), .out(out_4), .sel(in_3));
endmodule

module guia0705 (
  input  x,
  input  y,
  input  [2:0] in_3,
  output out_4
);

  wire and_1_out, nand_1_out, nor_1_out, not_1_out, not_2_out, or_1_out, xnor_1_out, xor_1_out;

  not not_1 (not_1_out, y);
  not not_2 (not_2_out, x);
  and and_1 (and_1_out, x, y);
  nand nand_1 (nand_1_out, x, y);
  xor xor_1 (xor_1_out, x, y);
  xnor xnor_1 (xnor_1_out, x, y);
  or or_1 (or_1_out, x, y);
  nor nor_1 (nor_1_out, x, y);
  Multiplexer #(.select(3), .enable("false")) multiplexer_1 (
    .in0(not_1_out), .in1(not_2_out), .in2(and_1_out), .in3(nand_1_out), .in4(xor_1_out), .in5(xnor_1_out),
    .in6(or_1_out), .in7(nor_1_out), .out(out_4), .sel(in_3));
endmodule
