// Logisim project Guia08(incompleto).circ as structural Verilog
module Exemplo_0801 (
  input  a,
  input  b,
  input  carry,
  output s0,
  output s1
);

  wire and_1_out, and_2_out, xor_1_out;

  xor xor_1 (xor_1_out, a, b);
  and and_1 (and_1_out, a, b);
  and and_2 (and_2_out, xor_1_out, carry);
  xor xor_2 (s0, xor_1_out, carry);
  or or_1 (s1, and_2_out, and_1_out);
endmodule

module Exemplo_0802 (
  input  [5:0] a,
  input  [5:0] b,
  output [5:0] out_3
);
endmodule

module Exemplo_0804 (
  input  carry,
  input  a,
  input  b,
  output s0,
  output s1
);

  wire and_1_out, and_2_out, not_1_out, not_2_out, xor_1_out;

  not not_1 (not_1_out, a);
  not not_2 (not_2_out, xor_1_out);
  xor xor_1 (xor_1_out, a, b);
  and and_1 (and_1_out, b, not_1_out);
  xor xor_2 (s0, carry, xor_1_out);
  and and_2 (and_2_out, carry, not_2_out);
  and and_3 (s1, and_2_out, and_1_out);
endmodule
