// Logisim project circuitos.circ as structural Verilog: 4 circuits, main circuit 01
module _01 (
  input  in_1,
  input  in_2,
  output out_3
);

  wire and_1_out, clock_1_out, d_ff_1_q, d_ff_2_q, d_ff_3_q, d_ff_4_q, not_1_out;

  Clock clock_1 (.out(clock_1_out));
  D_Flip_Flop d_ff_1 (.clk(clock_1_out), .D(in_1), .Q(d_ff_1_q), .reset(in_2));  // open: Qn, preset
  D_Flip_Flop d_ff_2 (.clk(clock_1_out), .D(d_ff_1_q), .Q(d_ff_2_q), .reset(in_2));  // open: Qn, preset
  D_Flip_Flop d_ff_3 (.clk(clock_1_out), .D(d_ff_2_q), .Q(d_ff_3_q), .reset(in_2));  // open: Qn, preset
  D_Flip_Flop d_ff_4 (.clk(clock_1_out), .D(d_ff_3_q), .Q(d_ff_4_q), .reset(in_2));  // open: Qn, preset
  not not_1 (not_1_out, d_ff_2_q);
  and and_1 (and_1_out, d_ff_4_q, d_ff_3_q, not_1_out, d_ff_1_q);
  D_Flip_Flop d_ff_5 (.clk(clock_1_out), .D(and_1_out), .Q(out_3), .reset(in_2));  // open: Qn, preset
endmodule

module _02 (
  input  in_1,
  input  in_2,
  output out_3
);

  wire and_1_out, clock_1_out, d_ff_1_q, d_ff_2_q, d_ff_3_q, d_ff_4_q, not_1_out;

  Clock clock_1 (.out(clock_1_out));
  D_Flip_Flop d_ff_1 (.clk(clock_1_out), .D(in_1), .Q(d_ff_1_q), .reset(in_2));  // open: Qn, preset
  D_Flip_Flop d_ff_2 (.clk(clock_1_out), .D(d_ff_1_q), .Q(d_ff_2_q), .reset(in_2));  // open: Qn, preset
  D_Flip_Flop d_ff_3 (.clk(clock_1_out), .D(d_ff_2_q), .Q(d_ff_3_q), .reset(in_2));  // open: Qn, preset
  not not_1 (not_1_out, d_ff_2_q);
  D_Flip_Flop d_ff_4 (.clk(clock_1_out), .D(d_ff_3_q), .Q(d_ff_4_q), .reset(in_2));  // open: Qn, preset
  and and_1 (and_1_out, d_ff_4_q, d_ff_3_q, not_1_out, d_ff_1_q);
  D_Flip_Flop d_ff_5 (.clk(clock_1_out), .D(and_1_out), .Q(out_3), .reset(in_2));  // open: Qn, preset
endmodule

module _03 (
  input  in_1,
  input  in_2,
  output \Saída_do_Moore ,
  output out_4
);

  wire clock_1_out, d_ff_1_q, d_ff_2_q, d_ff_3_q, d_ff_4_q, not_1_out;

  Clock clock_1 (.out(clock_1_out));
  D_Flip_Flop d_ff_1 (.clk(clock_1_out), .D(in_1), .Q(d_ff_1_q), .reset(in_2));  // open: Qn, preset
  D_Flip_Flop d_ff_2 (.clk(clock_1_out), .D(d_ff_1_q), .Q(d_ff_2_q), .reset(in_2));  // open: Qn, preset
  D_Flip_Flop d_ff_3 (.clk(clock_1_out), .D(d_ff_2_q), .Q(d_ff_3_q), .reset(in_2));  // open: Qn, preset
  not not_1 (not_1_out, d_ff_2_q);
  D_Flip_Flop d_ff_4 (.clk(clock_1_out), .D(d_ff_3_q), .Q(d_ff_4_q), .reset(in_2));  // open: Qn, preset
  and and_1 (out_4, d_ff_4_q, d_ff_3_q, not_1_out, d_ff_1_q);
  D_Flip_Flop d_ff_5 (.clk(clock_1_out), .D(out_4), .Q(\Saída_do_Moore ), .reset(in_2));  // open: Qn, preset
endmodule

module _04 (
  input  in_1,
  input  in_2,
  output out_3
);

  wire clock_1_out, controlled_buffer_1_out, d_ff_1_q, d_ff_2_q, d_ff_3_q, d_ff_4_q, not_1_out, not_2_out,
       not_3_out;

  Clock clock_1 (.out(clock_1_out));
  assign controlled_buffer_1_out = not_3_out ? clock_1_out : 1'bz;  // Controlled_Buffer controlled_buffer_1
  D_Flip_Flop d_ff_1 (.clk(controlled_buffer_1_out), .D(in_1), .Q(d_ff_1_q), .reset(in_2));  // open: Qn, preset
  D_Flip_Flop d_ff_2 (.clk(controlled_buffer_1_out), .D(d_ff_1_q), .Q(d_ff_2_q), .reset(in_2));  // open: Qn, preset
  D_Flip_Flop d_ff_3 (.clk(controlled_buffer_1_out), .D(d_ff_2_q), .Q(d_ff_3_q), .reset(in_2));  // open: Qn, preset
  not not_1 (not_1_out, d_ff_3_q);
  not not_2 (not_2_out, d_ff_1_q);
  D_Flip_Flop d_ff_4 (.clk(controlled_buffer_1_out), .D(d_ff_3_q), .Q(d_ff_4_q), .reset(in_2));  // open: Qn, preset
  and and_1 (out_3, d_ff_4_q, not_1_out, d_ff_2_q, not_2_out);
  not not_3 (not_3_out, out_3);
endmodule
