// Logisim project c.circ as structural Verilog
module _01 (
  input  Add,
  input  R_W,
  input  CLK,
  input  [3:0] IN,
  input  CLR,
  output [3:0] out_6
);

  _1x2 u_1x2_1 (.Addr(Add), .R_W(R_W), .CLK(CLK), .IN(IN[3:2]), .CLR(CLR), .out_6(out_6[3:2]));
  _1x2 u_1x2_2 (.Addr(Add), .R_W(R_W), .CLK(CLK), .IN(IN[1:0]), .CLR(CLR), .out_6(out_6[1:0]));
endmodule

module ramzinha_1x1 (
  input  Address,
  input  CLK,
  input  R_W,
  input  CLR,
  input  IN,
  output OUT
);

  wire and_1_out, j_k_ff_1_q, not_1_out;

  and and_1 (and_1_out, Address, CLK, R_W);
  not not_1 (not_1_out, IN);
  and and_2 (OUT, Address, j_k_ff_1_q);
  J_K_Flip_Flop j_k_ff_1 (.J(R_W), .clk(and_1_out), .K(not_1_out), .Q(j_k_ff_1_q), .reset(CLR));  // open: Qn, preset
endmodule

module _1x2 (
  input  Addr,
  input  R_W,
  input  CLK,
  input  [1:0] IN,
  input  CLR,
  output [1:0] out_6
);

  ramzinha_1x1 ramzinha_1x1_1 (.Address(Addr), .CLK(R_W), .R_W(CLK), .IN(IN[1]), .CLR(CLR), .OUT(out_6[1]));
  ramzinha_1x1 ramzinha_1x1_2 (.Address(Addr), .CLK(R_W), .R_W(CLK), .IN(IN[0]), .CLR(CLR), .OUT(out_6[0]));
endmodule

module _1x4 (
  input  Addr,
  input  R_W,
  input  CLK,
  input  [3:0] IN,
  input  CLR,
  output [3:0] out_6
);

  _1x2 u_1x2_1 (.Addr(Addr), .R_W(R_W), .CLK(CLK), .IN(IN[3:2]), .CLR(CLR), .out_6(out_6[3:2]));
  _1x2 u_1x2_2 (.Addr(Addr), .R_W(R_W), .CLK(CLK), .IN(IN[1:0]), .CLR(CLR), .out_6(out_6[1:0]));
endmodule

module _02 (
  input  Addr,
  input  R_W,
  input  CLK,
  input  [3:0] IN,
  input  CLR,
  output [3:0] out_6
);

  _1x2 u_1x2_1 (.Addr(Addr), .R_W(R_W), .CLK(CLK), .IN(IN[3:2]), .CLR(CLR), .out_6(out_6[3:2]));
  _1x2 u_1x2_2 (.Addr(Addr), .R_W(R_W), .CLK(CLK), .IN(IN[1:0]), .CLR(CLR), .out_6(out_6[1:0]));
endmodule
