// Logisim project circuitos.circ as structural Verilog: 5 circuits, main circuit 01
module _01 (
  input  In,
  input  clear
);

  wire clock_1_out;
  wire [4:0] j_k_ff_5_qn;

  Clock clock_1 (.out(clock_1_out));
  // Probe on j_k_ff_5_qn[4]
  J_K_Flip_Flop j_k_ff_1 (.J(In), .clk(j_k_ff_5_qn[3]), .K(In), .Qn(j_k_ff_5_qn[4]), .reset(clear));  // open: Q, preset
  // Probe on j_k_ff_5_qn[3]
  J_K_Flip_Flop j_k_ff_2 (.J(In), .clk(j_k_ff_5_qn[2]), .K(In), .Qn(j_k_ff_5_qn[3]), .reset(clear));  // open: Q, preset
  // Probe on j_k_ff_5_qn[2]
  J_K_Flip_Flop j_k_ff_3 (.J(In), .clk(j_k_ff_5_qn[1]), .K(In), .Qn(j_k_ff_5_qn[2]), .reset(clear));  // open: Q, preset
  // Probe on j_k_ff_5_qn[1]
  J_K_Flip_Flop j_k_ff_4 (.J(In), .clk(j_k_ff_5_qn[0]), .K(In), .Qn(j_k_ff_5_qn[1]), .reset(clear));  // open: Q, preset
  // Probe on j_k_ff_5_qn[0]
  J_K_Flip_Flop j_k_ff_5 (.J(In), .clk(clock_1_out), .K(In), .Qn(j_k_ff_5_qn[0]), .reset(clear));  // open: Q, preset
  // Probe on j_k_ff_5_qn
endmodule

module _02 (
  input  In,
  input  clear
);

  wire clock_1_out, j_k_ff_2_q, j_k_ff_3_q, j_k_ff_4_q, j_k_ff_5_q;
  wire [4:0] j_k_ff_5_qn;

  Clock clock_1 (.out(clock_1_out));
  // Probe on j_k_ff_5_qn[4]
  J_K_Flip_Flop j_k_ff_1 (.J(In), .clk(j_k_ff_2_q), .K(In), .Qn(j_k_ff_5_qn[4]), .reset(clear));  // open: Q, preset
  // Probe on j_k_ff_5_qn[3]
  J_K_Flip_Flop j_k_ff_2 (
    .J(In), .clk(j_k_ff_3_q), .K(In), .Q(j_k_ff_2_q), .Qn(j_k_ff_5_qn[3]), .reset(clear));  // open: preset
  // Probe on j_k_ff_5_qn[2]
  J_K_Flip_Flop j_k_ff_3 (
    .J(In), .clk(j_k_ff_4_q), .K(In), .Q(j_k_ff_3_q), .Qn(j_k_ff_5_qn[2]), .reset(clear));  // open: preset
  // Probe on j_k_ff_5_qn[1]
  J_K_Flip_Flop j_k_ff_4 (
    .J(In), .clk(j_k_ff_5_q), .K(In), .Q(j_k_ff_4_q), .Qn(j_k_ff_5_qn[1]), .reset(clear));  // open: preset
  // Probe on j_k_ff_5_qn[0]
  J_K_Flip_Flop j_k_ff_5 (
    .J(In), .clk(clock_1_out), .K(In), .Q(j_k_ff_5_q), .Qn(j_k_ff_5_qn[0]), .reset(clear));  // open: preset
  // Probe on j_k_ff_5_qn
endmodule

module _03 (
  input  in,
  input  clear
);

  wire and_1_out, clock_1_out, j_k_ff_1_q, j_k_ff_1_qn, j_k_ff_2_q, j_k_ff_2_qn, j_k_ff_3_q, j_k_ff_3_qn,
       j_k_ff_4_q, not_1_out, not_2_out, or_1_out;

  Clock clock_1 (.out(clock_1_out));
  or or_1 (or_1_out, clear, and_1_out);
  not not_1 (not_1_out, j_k_ff_1_q);
  and and_1 (and_1_out, not_1_out, j_k_ff_2_q, not_2_out, j_k_ff_4_q);
  not not_2 (not_2_out, j_k_ff_3_q);
  J_K_Flip_Flop j_k_ff_1 (
    .J(in), .clk(clock_1_out), .K(in), .Q(j_k_ff_1_q), .Qn(j_k_ff_1_qn), .reset(or_1_out));  // open: preset
  J_K_Flip_Flop j_k_ff_2 (
    .J(in), .clk(j_k_ff_1_qn), .K(in), .Q(j_k_ff_2_q), .Qn(j_k_ff_2_qn), .reset(or_1_out));  // open: preset
  // Probe on j_k_ff_3_q
  // Probe on j_k_ff_4_q
  J_K_Flip_Flop #(.trigger("falling")) j_k_ff_3 (
    .J(in), .clk(j_k_ff_2_qn), .K(in), .Q(j_k_ff_3_q), .Qn(j_k_ff_3_qn), .reset(or_1_out));  // open: preset
  // Probe on j_k_ff_2_q
  J_K_Flip_Flop j_k_ff_4 (.J(in), .clk(j_k_ff_3_qn), .K(in), .Q(j_k_ff_4_q), .reset(or_1_out));  // open: Qn, preset
  // Probe on j_k_ff_1_q
endmodule

module _04 (
  input  in,
  input  in_2
);

  wire and_1_out, clock_1_out, j_k_ff_1_q, j_k_ff_1_qn, j_k_ff_2_q, j_k_ff_2_qn, j_k_ff_3_q, j_k_ff_3_qn,
       j_k_ff_4_q, j_k_ff_4_qn, not_1_out, not_2_out, or_1_out;

  Clock clock_1 (.out(clock_1_out));
  or or_1 (or_1_out, in_2, and_1_out);
  and and_1 (and_1_out, not_1_out, j_k_ff_2_qn, not_2_out, j_k_ff_4_qn);
  // Probe on j_k_ff_4_q
  J_K_Flip_Flop j_k_ff_1 (
    .J(in), .clk(clock_1_out), .K(in), .Q(j_k_ff_1_q), .Qn(j_k_ff_1_qn), .preset(or_1_out));  // open: reset
  not not_1 (not_1_out, j_k_ff_1_qn);
  not not_2 (not_2_out, j_k_ff_3_qn);
  // Probe on j_k_ff_3_q
  J_K_Flip_Flop j_k_ff_2 (
    .J(in), .clk(j_k_ff_1_q), .K(in), .Q(j_k_ff_2_q), .Qn(j_k_ff_2_qn), .preset(or_1_out));  // open: reset
  // Probe on j_k_ff_2_q
  J_K_Flip_Flop j_k_ff_3 (
    .J(in), .clk(j_k_ff_2_q), .K(in), .Q(j_k_ff_3_q), .Qn(j_k_ff_3_qn), .preset(or_1_out));  // open: reset
  // Probe on j_k_ff_1_q
  J_K_Flip_Flop j_k_ff_4 (
    .J(in), .clk(j_k_ff_3_q), .K(in), .Q(j_k_ff_4_q), .Qn(j_k_ff_4_qn), .preset(or_1_out));  // open: reset
endmodule

module _05 (
  input  in_1,
  output out_2,
  output out_3,
  output out_4
);

  wire and_1_out, and_2_out, and_3_out, and_4_out, and_5_out, clock_1_out, or_1_out, or_2_out, or_3_out,
       t_ff_3_qn;

  Clock clock_1 (.out(clock_1_out));
  T_Flip_Flop #(.Pre_Clr_Positions("LEGACY"), .enable("true"), .NewFFLayout("false")) t_ff_1 (
    .clk(clock_1_out), .T(in_1), .Q(out_2));  // open: Qn, preset, reset, en
  // Probe on out_2
  and and_1 (and_1_out, t_ff_3_qn, out_2);
  and and_2 (and_2_out, out_4, out_3);
  // Probe on out_3
  T_Flip_Flop #(.Pre_Clr_Positions("LEGACY"), .enable("true"), .NewFFLayout("false")) t_ff_2 (
    .clk(clock_1_out), .T(or_1_out), .Q(out_3));  // open: Qn, preset, reset, en
  or or_1 (or_1_out, and_1_out, and_2_out);
  and and_3 (and_3_out, out_2, out_3);
  and and_4 (and_4_out, out_2, out_4);
  and and_5 (and_5_out, out_4, out_3);
  // Probe on out_4
  or or_2 (or_2_out, and_3_out, and_4_out);
  T_Flip_Flop #(.Pre_Clr_Positions("LEGACY"), .enable("true"), .NewFFLayout("false")) t_ff_3 (
    .clk(clock_1_out), .T(or_3_out), .Q(out_4), .Qn(t_ff_3_qn));  // open: preset, reset, en
  or or_3 (or_3_out, or_2_out, and_5_out);
endmodule
