// Logisim project circuitos.circ as structural Verilog: 5 circuits, main circuit 01
module _01 (
  input  in,
  input  clr
);

  wire clock_1_out, d_ff_1_q, d_ff_2_q, d_ff_3_q, d_ff_4_q, d_ff_5_q;

  Clock clock_1 (.out(clock_1_out));
  // Probe on d_ff_1_q
  D_Flip_Flop d_ff_1 (.clk(clock_1_out), .D(d_ff_2_q), .Q(d_ff_1_q), .reset(clr));  // open: Qn, preset
  // Probe on d_ff_2_q
  D_Flip_Flop d_ff_2 (.clk(clock_1_out), .D(d_ff_3_q), .Q(d_ff_2_q), .reset(clr));  // open: Qn, preset
  // Probe on d_ff_3_q
  D_Flip_Flop d_ff_3 (.clk(clock_1_out), .D(d_ff_4_q), .Q(d_ff_3_q), .reset(clr));  // open: Qn, preset
  // Probe on d_ff_4_q
  D_Flip_Flop d_ff_4 (.clk(clock_1_out), .D(d_ff_5_q), .Q(d_ff_4_q), .reset(clr));  // open: Qn, preset
  // Probe on d_ff_5_q
  D_Flip_Flop d_ff_5 (.clk(clock_1_out), .D(in), .Q(d_ff_5_q), .reset(clr));  // open: Qn, preset
endmodule

module _02 (
  input  in,
  input  clr
);

  wire clock_1_out, d_ff_1_q, d_ff_2_q, d_ff_3_q, d_ff_4_q, d_ff_5_q;

  Clock clock_1 (.out(clock_1_out));
  // Probe on d_ff_1_q
  D_Flip_Flop #(.Pre_Clr_Positions("BELOW_ABOVE")) d_ff_1 (
    .clk(clock_1_out), .D(d_ff_2_q), .Q(d_ff_1_q), .preset(clr));  // open: Qn, reset
  // Probe on d_ff_2_q
  D_Flip_Flop #(.Pre_Clr_Positions("BELOW_ABOVE")) d_ff_2 (
    .clk(clock_1_out), .D(d_ff_3_q), .Q(d_ff_2_q), .preset(clr));  // open: Qn, reset
  D_Flip_Flop #(.Pre_Clr_Positions("BELOW_ABOVE")) d_ff_3 (
    .clk(clock_1_out), .D(d_ff_4_q), .Q(d_ff_3_q), .preset(clr));  // open: Qn, reset
  // Probe on d_ff_3_q
  // Probe on d_ff_4_q
  D_Flip_Flop #(.Pre_Clr_Positions("BELOW_ABOVE")) d_ff_4 (
    .clk(clock_1_out), .D(d_ff_5_q), .Q(d_ff_4_q), .preset(clr));  // open: Qn, reset
  // Probe on d_ff_5_q
  D_Flip_Flop #(.Pre_Clr_Positions("BELOW_ABOVE")) d_ff_5 (
    .clk(clock_1_out), .D(in), .Q(d_ff_5_q), .preset(clr));  // open: Qn, reset
endmodule

module _03 (
  input  in,
  input  clr
);

  wire clock_1_out, d_ff_1_q, d_ff_2_q, d_ff_3_q, d_ff_4_q, d_ff_5_q, or_1_out;

  Clock clock_1 (.out(clock_1_out));
  or or_1 (or_1_out, in, d_ff_5_q);
  // Probe on d_ff_1_q
  D_Flip_Flop #(.Pre_Clr_Positions("BELOW_ABOVE")) d_ff_1 (
    .clk(clock_1_out), .D(or_1_out), .Q(d_ff_1_q), .preset(clr));  // open: Qn, reset
  // Probe on d_ff_2_q
  D_Flip_Flop d_ff_2 (.clk(clock_1_out), .D(d_ff_1_q), .Q(d_ff_2_q), .reset(clr));  // open: Qn, preset
  // Probe on d_ff_3_q
  D_Flip_Flop d_ff_3 (.clk(clock_1_out), .D(d_ff_2_q), .Q(d_ff_3_q), .reset(clr));  // open: Qn, preset
  // Probe on d_ff_4_q
  D_Flip_Flop d_ff_4 (.clk(clock_1_out), .D(d_ff_3_q), .Q(d_ff_4_q), .reset(clr));  // open: Qn, preset
  // Probe on d_ff_5_q
  D_Flip_Flop d_ff_5 (.clk(clock_1_out), .D(d_ff_4_q), .Q(d_ff_5_q), .reset(clr));  // open: Qn, preset
endmodule

module _04 (
  input  clr
);

  wire clock_1_out, d_ff_1_q, d_ff_1_qn, d_ff_2_q, d_ff_3_q, d_ff_4_q, d_ff_5_q;

  Clock clock_1 (.out(clock_1_out));
  // Probe on d_ff_1_q
  D_Flip_Flop d_ff_1 (.clk(clock_1_out), .D(d_ff_2_q), .Q(d_ff_1_q), .Qn(d_ff_1_qn), .reset(clr));  // open: preset
  // Probe on d_ff_2_q
  D_Flip_Flop d_ff_2 (.clk(clock_1_out), .D(d_ff_3_q), .Q(d_ff_2_q), .reset(clr));  // open: Qn, preset
  // Probe on d_ff_3_q
  D_Flip_Flop d_ff_3 (.clk(clock_1_out), .D(d_ff_4_q), .Q(d_ff_3_q), .reset(clr));  // open: Qn, preset
  // Probe on d_ff_4_q
  D_Flip_Flop d_ff_4 (.clk(clock_1_out), .D(d_ff_5_q), .Q(d_ff_4_q), .reset(clr));  // open: Qn, preset
  // Probe on d_ff_5_q
  D_Flip_Flop d_ff_5 (.clk(clock_1_out), .D(d_ff_1_qn), .Q(d_ff_5_q), .reset(clr));  // open: Qn, preset
endmodule

module _05 (
  input  clr,
  input  ld,
  input  in_3,
  input  in_4,
  input  in_5,
  input  in_6,
  input  in_7
);

  wire and_1_out, and_2_out, and_3_out, and_4_out, and_5_out, and_6_out, and_7_out, and_8_out, and_9_out,
       and_10_out, clock_1_out, d_ff_1_q, d_ff_2_q, d_ff_3_q, d_ff_4_q, d_ff_5_q, or_1_out, or_2_out,
       or_3_out, or_4_out, or_5_out;

  Clock clock_1 (.out(clock_1_out));
  and and_1 (and_1_out, ld, in_3);
  // Probe on d_ff_1_q
  D_Flip_Flop #(.Pre_Clr_Positions("LEGACY")) d_ff_1 (
    .clk(clock_1_out), .D(1'b0), .Q(d_ff_1_q), .preset(and_1_out), .reset(or_1_out));  // open: Qn
  or or_1 (or_1_out, clr, and_2_out);
  and and_2 (and_2_out, ~in_3, ld);  // AND_Gate
  // Probe on d_ff_2_q
  D_Flip_Flop #(.Pre_Clr_Positions("LEGACY")) d_ff_2 (
    .clk(clock_1_out), .D(d_ff_1_q), .Q(d_ff_2_q), .preset(and_4_out), .reset(or_2_out));  // open: Qn
  or or_2 (or_2_out, clr, and_3_out);
  and and_3 (and_3_out, ~in_4, ld);  // AND_Gate
  and and_4 (and_4_out, ld, in_4);
  // Probe on d_ff_3_q
  D_Flip_Flop #(.Pre_Clr_Positions("LEGACY")) d_ff_3 (
    .clk(clock_1_out), .D(d_ff_2_q), .Q(d_ff_3_q), .preset(and_6_out), .reset(or_3_out));  // open: Qn
  or or_3 (or_3_out, clr, and_5_out);
  and and_5 (and_5_out, ~in_5, ld);  // AND_Gate
  and and_6 (and_6_out, ld, in_5);
  or or_4 (or_4_out, clr, and_8_out);
  and and_7 (and_7_out, ld, in_6);
  // Probe on d_ff_4_q
  D_Flip_Flop #(.Pre_Clr_Positions("LEGACY")) d_ff_4 (
    .clk(clock_1_out), .D(d_ff_3_q), .Q(d_ff_4_q), .preset(and_7_out), .reset(or_4_out));  // open: Qn
  and and_8 (and_8_out, ~in_6, ld);  // AND_Gate
  and and_9 (and_9_out, ld, in_7);
  // Probe on d_ff_5_q
  D_Flip_Flop #(.Pre_Clr_Positions("LEGACY")) d_ff_5 (
    .clk(clock_1_out), .D(d_ff_4_q), .Q(d_ff_5_q), .preset(and_9_out), .reset(or_5_out));  // open: Qn
  or or_5 (or_5_out, clr, and_10_out);
  and and_10 (and_10_out, ~in_7, ld);  // AND_Gate
endmodule
