// Logisim project 08_10.circ as structural Verilog: 3 circuits, main circuit 08
module _08 (
  input  a,
  input  b,
  input  c,
  output out_4
);

  wire multiplexer_1_out, multiplexer_2_out, not_1_out, not_2_out, not_3_out;

  not not_1 (not_1_out, a);
  not not_2 (not_2_out, b);
  not not_3 (not_3_out, c);
  Multiplexer #(.enable("false")) multiplexer_1 (.in0(b), .in1(c), .out(multiplexer_1_out), .sel(not_1_out));
  Multiplexer #(.enable("false")) multiplexer_2 (
    .in0(not_1_out), .in1(not_2_out), .out(multiplexer_2_out), .sel(not_3_out));
  Multiplexer #(.enable("false")) multiplexer_3 (
    .in0(multiplexer_1_out), .in1(multiplexer_2_out), .out(out_4), .sel(not_3_out));
endmodule

module _09 (
  input  a,
  input  b,
  input  d,
  output s
);

  wire nor_1_out, nor_2_out;

  nor nor_1 (nor_1_out, a, b);
  nor nor_2 (nor_2_out, b, d);
  nor nor_3 (s, nor_1_out, nor_2_out);
endmodule

module _10 (
  input  a,
  input  b,
  input  c,
  output s
);

  wire a_a_out, b_b_out, b_c_out, c_c_out, nand_1_out, nand_2_out;

  nand a_a (a_a_out, a, a);
  nand b_b (b_b_out, b, b);
  nand c_c (c_c_out, c, c);
  nand nand_1 (nand_1_out, b_b_out, c_c_out);
  nand b_c (b_c_out, b, c);
  nand nand_2 (nand_2_out, a_a_out, nand_1_out);
  nand nand_3 (s, nand_2_out, b_c_out);
endmodule
