// Logisim project guia_0401.circ as structural Verilog: 1 circuit, main circuit main
module main (
  input  x,
  input  y,
  input  z,
  input  x_2,
  input  y_2,
  input  z_2,
  input  x_3,
  input  y_3,
  input  z_3,
  input  x_4,
  input  y_4,
  input  z_4,
  input  x_5,
  input  y_5,
  input  y_6,
  input  z_5,
  output out_17,
  output out_18,
  output out_19,
  output out_20,
  output out_21
);

  wire and_1_out, and_2_out, and_3_out, and_4_out, not_1_out, not_2_out, not_3_out, not_4_out, or_1_out,
       or_2_out;

  and and_1 (and_1_out, y, z);
  and and_2 (and_2_out, x_2, y_2);
  or or_1 (or_1_out, x_3, y_3);
  or or_2 (or_2_out, x_4, y_4);
  and and_3 (and_3_out, x_5, y_5);
  and and_4 (and_4_out, y_6, z_5);
  not not_1 (not_1_out, and_1_out);
  not not_2 (not_2_out, and_2_out);
  not not_3 (not_3_out, or_1_out);
  not not_4 (not_4_out, or_2_out);
  or or_3 (out_21, and_3_out, and_4_out);
  or or_4 (out_17, x, not_1_out);
  or or_5 (out_18, not_2_out, z_2);
  or or_6 (out_19, not_3_out, z_3);
  or or_7 (out_20, not_4_out, z_4);

  // Notes on the sheet:
  //   a)
  //   b)
  //   c)
  //   d)
  //   e)
endmodule
