// Logisim project guia_0402.circ as structural Verilog: 1 circuit, main circuit main
module main (
  input  x,
  input  x_2,
  input  y,
  input  x_3,
  input  y_2,
  input  x_4,
  input  y_3,
  input  x_5,
  input  y_4,
  input  x_6,
  input  y_5,
  input  x_7,
  input  y_6,
  input  x_8,
  input  y_7,
  input  x_9,
  input  y_8,
  input  x_10,
  input  y_9,
  output out_20,
  output out_21,
  output out_22,
  output out_23,
  output out_24
);

  wire and_1_out, and_2_out, and_3_out, and_4_out, and_5_out, and_6_out, not_1_out, not_2_out, not_3_out,
       not_4_out, not_5_out, or_1_out, or_2_out, or_3_out;

  and and_1 (and_1_out, x_2, y);
  and and_2 (and_2_out, x_3, y_2);
  or or_1 (or_1_out, x_4, y_3);
  or or_2 (or_2_out, x_5, y_4);
  and and_3 (and_3_out, x_6, y_5);
  or or_3 (or_3_out, x_7, y_6);
  and and_4 (and_4_out, x_8, y_7);
  and and_5 (and_5_out, x_9, y_8);
  and and_6 (and_6_out, x_10, y_9);
  not not_1 (not_1_out, and_1_out);
  and and_7 (out_21, and_2_out, or_1_out);
  not not_2 (not_2_out, or_2_out);
  not not_3 (not_3_out, or_3_out);
  not not_4 (not_4_out, and_4_out);
  not not_5 (not_5_out, and_5_out);
  or or_4 (out_20, x, not_1_out);
  or or_5 (out_22, not_2_out, and_3_out);
  and and_8 (out_23, not_3_out, not_4_out);
  or or_6 (out_24, not_5_out, and_6_out);

  // Notes on the sheet:
  //   a)
  //   b)
  //   c)
  //   d)
  //   e)
endmodule
