// Logisim project guia0401.circ as structural Verilog: 5 circuits, main circuit letraA
module letraA (
  input  x,
  input  y,
  input  z,
  output out_4
);

  wire not_1_out, not_2_out, not_3_out, or_1_out;

  not not_1 (not_1_out, z);
  not not_2 (not_2_out, y);
  or or_1 (or_1_out, not_1_out, not_2_out);
  not not_3 (not_3_out, or_1_out);
  and and_1 (out_4, not_3_out, x);
endmodule

module letraB (
  input  x,
  input  y,
  input  z,
  output out_4
);

  wire not_1_out, not_2_out, not_3_out, or_1_out;

  not not_1 (not_1_out, x);
  not not_2 (not_2_out, z);
  or or_1 (or_1_out, y, not_1_out);
  not not_3 (not_3_out, or_1_out);
  and and_1 (out_4, not_2_out, not_3_out);
endmodule

module letraC (
  input  x,
  input  y,
  input  z,
  output out_4
);

  wire and_1_out, not_1_out, not_2_out;

  not not_1 (not_1_out, x);
  and and_1 (and_1_out, y, not_1_out);
  not not_2 (not_2_out, and_1_out);
  and and_2 (out_4, z, not_2_out);
endmodule

module letraD (
  input  x,
  input  y,
  input  z,
  output out_4
);

  wire and_1_out, not_1_out, not_2_out;

  not not_1 (not_1_out, y);
  and and_1 (and_1_out, not_1_out, x);
  not not_2 (not_2_out, and_1_out);
  and and_2 (out_4, z, not_2_out);
endmodule

module letraE (
  input  x,
  input  y,
  input  z,
  output out_4
);

  wire not_1_out, or_1_out, or_2_out;

  not not_1 (not_1_out, z);
  or or_1 (or_1_out, y, x);
  or or_2 (or_2_out, not_1_out, y);
  and and_1 (out_4, or_2_out, or_1_out);
endmodule
