// Logisim project guia_0505.circ as structural Verilog: 1 circuit, main circuit main
module main (
  input  a,
  input  in_2,
  input  b,
  input  in_4,
  output out_5
);

  wire nand_1_out, nand_2_out;

  nand nand_1 (nand_1_out, a, in_2);
  nand nand_2 (nand_2_out, b, in_4);
  xnor xnor_1 (out_5, nand_1_out, nand_2_out);
endmodule
