// Logisim project guia_0506.circ as structural Verilog: 1 circuit, main circuit main
module main (
  input  a,
  input  in_2,
  input  b,
  input  in_4,
  output out_5
);

  wire nor_1_out, nor_2_out;

  nor nor_1 (nor_1_out, a, in_2);
  nor nor_2 (nor_2_out, b, in_4);
  xor xor_1 (out_5, nor_1_out, nor_2_out);
endmodule
