// Logisim project 03 Circuito.circ as structural Verilog
module _01 (
  input  in_1,
  input  in_2,
  input  in_3,
  input  in_4,
  input  in_5,
  input  in_6,
  input  in_7,
  input  in_8,
  output out_9,
  output out_10,
  output out_11,
  output out_12
);

  wire nand_2_out, nand_3_out, nand_4_out, nand_out;

  nand \nand  (nand_out, in_1, in_1);
  nand nand_2 (nand_2_out, in_3, in_3);
  nand nand_3 (nand_3_out, in_5, in_5);
  nand nand_4 (nand_4_out, in_7, in_7);
  nand nand_5 (out_9, nand_out, in_2);
  nand nand_6 (out_10, nand_2_out, in_4);
  nand nand_7 (out_11, nand_3_out, in_6);
  nand nand_8 (out_12, nand_4_out, in_8);
endmodule

module _02 (
  input  in_1,
  input  in_2,
  input  in_3,
  input  in_4,
  input  in_5,
  input  in_6,
  input  in_7,
  input  in_8,
  output out_9,
  output out_10,
  output out_11,
  output out_12
);

  wire nor_2_out, nor_3_out, nor_4_out, nor_out;

  nor \nor  (nor_out, in_2, in_2);
  nor nor_2 (nor_2_out, in_4, in_4);
  nor nor_3 (nor_3_out, in_6, in_6);
  nor nor_4 (nor_4_out, in_8, in_8);
  nor nor_5 (out_9, in_1, nor_out);
  nor nor_6 (out_10, in_3, nor_2_out);
  nor nor_7 (out_11, in_5, nor_3_out);
  nor nor_8 (out_12, in_7, nor_4_out);
endmodule

module _03 (
  input  in_1,
  input  in_2,
  input  in_3,
  input  in_4,
  input  in_5,
  input  in_6,
  input  in_7,
  input  in_8,
  output out_9,
  output out_10,
  output out_11,
  output out_12
);

  wire nand_2_out, nand_3_out, nand_4_out, nand_5_out, nand_6_out, nand_7_out, nand_8_out, nand_out;

  nand \nand  (nand_out, in_1, in_1);
  nand nand_2 (nand_2_out, in_2, in_2);
  nand nand_3 (nand_3_out, in_3, in_3);
  nand nand_4 (nand_4_out, in_4, in_4);
  nand nand_5 (nand_5_out, in_5, in_5);
  nand nand_6 (nand_6_out, in_6, in_6);
  nand nand_7 (nand_7_out, in_7, in_7);
  nand nand_8 (nand_8_out, in_8, in_8);
  nand nand_9 (out_9, nand_out, nand_2_out);
  nand nand_10 (out_10, nand_3_out, nand_4_out);
  nand nand_11 (out_11, nand_5_out, nand_6_out);
  nand nand_12 (out_12, nand_7_out, nand_8_out);
endmodule

module _04 (
  input  in_1,
  input  in_2,
  input  in_3,
  input  in_4,
  input  in_5,
  input  in_6,
  input  in_7,
  input  in_8,
  output out_9,
  output out_10,
  output out_11,
  output out_12
);

  wire nor_2_out, nor_3_out, nor_4_out, nor_5_out, nor_6_out, nor_7_out, nor_8_out, nor_out;

  nor \nor  (nor_out, in_1, in_1);
  nor nor_2 (nor_2_out, in_2, in_2);
  nor nor_3 (nor_3_out, in_3, in_3);
  nor nor_4 (nor_4_out, in_4, in_4);
  nor nor_5 (nor_5_out, in_5, in_5);
  nor nor_6 (nor_6_out, in_6, in_6);
  nor nor_7 (nor_7_out, in_7, in_7);
  nor nor_8 (nor_8_out, in_8, in_8);
  nor nor_9 (out_9, nor_out, nor_2_out);
  nor nor_10 (out_10, nor_3_out, nor_4_out);
  nor nor_11 (out_11, nor_5_out, nor_6_out);
  nor nor_12 (out_12, nor_7_out, nor_8_out);
endmodule

module _05 (
  input  in_1,
  input  in_2,
  input  in_3,
  input  in_4,
  input  in_5,
  input  in_6,
  input  in_7,
  input  in_8,
  output out_9,
  output out_10,
  output out_11,
  output out_12
);

  wire nand_1_out, nand_2_out, nand_3_out, nand_4_out, nand_5_out, nand_6_out, nand_7_out, nand_8_out,
       nand_9_out, nand_10_out, nand_11_out, nand_12_out, nand_13_out, nand_14_out, nand_15_out, nand_16_out;

  nand nand_1 (nand_1_out, in_1, in_2);
  nand nand_2 (nand_2_out, in_3, in_4);
  nand nand_3 (nand_3_out, in_5, in_6);
  nand nand_4 (nand_4_out, in_7, in_8);
  nand nand_5 (nand_5_out, in_1, nand_1_out);
  nand nand_6 (nand_6_out, nand_1_out, in_2);
  nand nand_7 (nand_7_out, in_3, nand_2_out);
  nand nand_8 (nand_8_out, nand_2_out, in_4);
  nand nand_9 (nand_9_out, in_5, nand_3_out);
  nand nand_10 (nand_10_out, nand_3_out, in_6);
  nand nand_11 (nand_11_out, in_7, nand_4_out);
  nand nand_12 (nand_12_out, nand_4_out, in_8);
  nand nand_13 (nand_13_out, nand_5_out, nand_6_out);
  nand nand_14 (nand_14_out, nand_7_out, nand_8_out);
  nand nand_15 (nand_15_out, nand_9_out, nand_10_out);
  nand nand_16 (nand_16_out, nand_11_out, nand_12_out);
  nand nand_17 (out_9, nand_13_out, nand_13_out);
  nand nand_18 (out_10, nand_14_out, nand_14_out);
  nand nand_19 (out_11, nand_15_out, nand_15_out);
  nand nand_20 (out_12, nand_16_out, nand_16_out);
endmodule

module _06 (
  input  in_1,
  input  in_2,
  input  in_3,
  input  in_4,
  input  in_5,
  input  in_6,
  input  in_7,
  input  in_8,
  output out_9,
  output out_10,
  output out_11,
  output out_12
);

  wire nor_2_out, nor_3_out, nor_4_out, nor_5_out, nor_6_out, nor_7_out, nor_8_out, nor_9_out, nor_10_out,
       nor_11_out, nor_12_out, nor_13_out, nor_14_out, nor_15_out, nor_16_out, nor_out;

  nor \nor  (nor_out, in_1, in_2);
  nor nor_2 (nor_2_out, in_3, in_4);
  nor nor_3 (nor_3_out, in_5, in_6);
  nor nor_4 (nor_4_out, in_7, in_8);
  nor nor_5 (nor_5_out, in_1, nor_out);
  nor nor_6 (nor_6_out, nor_out, in_2);
  nor nor_7 (nor_7_out, in_3, nor_2_out);
  nor nor_8 (nor_8_out, nor_2_out, in_4);
  nor nor_9 (nor_9_out, in_5, nor_3_out);
  nor nor_10 (nor_10_out, nor_3_out, in_6);
  nor nor_11 (nor_11_out, in_7, nor_4_out);
  nor nor_12 (nor_12_out, nor_4_out, in_8);
  nor nor_13 (nor_13_out, nor_5_out, nor_6_out);
  nor nor_14 (nor_14_out, nor_7_out, nor_8_out);
  nor nor_15 (nor_15_out, nor_9_out, nor_10_out);
  nor nor_16 (nor_16_out, nor_11_out, nor_12_out);
  nor nor_17 (out_9, nor_13_out, nor_13_out);
  nor nor_18 (out_10, nor_14_out, nor_14_out);
  nor nor_19 (out_11, nor_15_out, nor_15_out);
  nor nor_20 (out_12, nor_16_out, nor_16_out);
endmodule
