// Logisim project guia05.circ as structural Verilog: 1 circuit, main circuit main
module main (
  input  na___b,
  input  na___b_2,
  input  in_3,
  input  in_4,
  input  in_5,
  input  in_6,
  input  in_7,
  input  in_8,
  input  in_9,
  input  in_10,
  input  in_11,
  input  in_12,
  input  na___nb,
  input  na___nb_2,
  input  in_15,
  input  in_16,
  input  in_17,
  input  in_18,
  input  in_19,
  input  in_20,
  output out_21,
  output out_22,
  output out_23,
  output out_24,
  output out_25,
  output out_26,
  output out_27,
  output out_28,
  output out_29,
  output out_30
);

  wire and_2_out, and_3_out, and_5_out, and_6_out, and_7_out, and_8_out, not_1_out, not_2_out, not_3_out,
       not_4_out, not_5_out, not_6_out, not_7_out, not_8_out, not_9_out, not_10_out, not_13_out, not_14_out,
       not_15_out, not_16_out, not_17_out, not_18_out, not_19_out, not_20_out, not_21_out, not_22_out,
       not_25_out, not_26_out, not_27_out, not_28_out, or_1_out, or_4_out, or_5_out, or_6_out;

  not not_1 (not_1_out, na___b);
  and and_1 (out_21, not_1_out, in_4);
  not not_2 (not_2_out, in_6);
  not not_3 (not_3_out, not_2_out);
  or or_1 (or_1_out, not_3_out, not_4_out);
  not not_4 (not_4_out, in_9);
  not not_5 (not_5_out, na___nb);
  or or_2 (out_27, not_5_out, not_6_out);
  not not_6 (not_6_out, in_15);
  not not_7 (not_7_out, in_17);
  not not_8 (not_8_out, not_7_out);
  and and_2 (and_2_out, not_8_out, not_10_out);
  not not_9 (not_9_out, in_19);
  not not_10 (not_10_out, not_9_out);
  not not_11 (out_24, or_1_out);
  not not_12 (out_29, and_2_out);
  or or_3 (out_22, na___b_2, not_13_out);
  not not_13 (not_13_out, in_5);
  not not_14 (not_14_out, in_7);
  and and_3 (and_3_out, not_14_out, not_16_out);
  not not_15 (not_15_out, in_10);
  not not_16 (not_16_out, not_15_out);
  not not_17 (not_17_out, na___nb_2);
  and and_4 (out_28, not_17_out, not_18_out);
  not not_18 (not_18_out, in_16);
  not not_19 (not_19_out, not_20_out);
  not not_20 (not_20_out, in_18);
  or or_4 (or_4_out, not_19_out, not_22_out);
  not not_21 (not_21_out, in_20);
  not not_22 (not_22_out, not_21_out);
  not not_23 (out_25, and_3_out);
  not not_24 (out_30, or_4_out);
  not not_25 (not_25_out, in_3);
  and and_5 (and_5_out, not_25_out, not_26_out);
  not not_26 (not_26_out, in_8);
  and and_6 (and_6_out, in_3, in_8);
  not not_27 (not_27_out, in_11);
  and and_7 (and_7_out, not_27_out, not_28_out);
  not not_28 (not_28_out, in_12);
  and and_8 (and_8_out, in_11, in_12);
  or or_5 (or_5_out, and_5_out, and_6_out);
  not not_29 (out_23, or_5_out);
  or or_6 (or_6_out, and_7_out, and_8_out);
  not not_30 (out_26, or_6_out);
endmodule
