// Logisim project Exemplo_0502.circ as structural Verilog: 1 circuit, main circuit main
module main (
  input  A,
  input  B,
  output S
);

  wire nand_1_out, not_1_out;

  not not_1 (not_1_out, A);
  nand nand_1 (nand_1_out, not_1_out, B);
  nand nand_2 (S, nand_1_out, nand_1_out);
endmodule
