// Logisim project Exemplo_0503.circ as structural Verilog: 1 circuit, main circuit main
module main (
  input  A,
  input  B,
  input  A_2,
  input  B_2,
  output S,
  output S_2
);

  wire nor_1_out, not_1_out, not_2_out;

  not not_1 (not_1_out, B);
  not not_2 (not_2_out, B_2);
  nor nor_1 (nor_1_out, A, not_1_out);
  or or_1 (S_2, A_2, not_2_out);
  nor nor_2 (S, nor_1_out, nor_1_out);
endmodule
