// Logisim project Exemplo_0504.circ as structural Verilog: 1 circuit, main circuit main
module main (
  input  A,
  input  B,
  input  A_2,
  input  B_2,
  output S,
  output out_6
);

  wire nand_1_out, nand_2_out, not_1_out, not_2_out, not_3_out, not_4_out;

  not not_1 (not_1_out, A);
  not not_2 (not_2_out, B);
  not not_3 (not_3_out, A_2);
  not not_4 (not_4_out, B_2);
  nand nand_1 (nand_1_out, not_1_out, not_1_out);
  nand nand_2 (nand_2_out, not_2_out, not_2_out);
  or or_1 (out_6, not_3_out, not_4_out);
  nand nand_3 (S, nand_1_out, nand_2_out);
endmodule
