// Logisim project Exemplo_0505.circ as structural Verilog: 1 circuit, main circuit main
module main (
  input  A,
  input  B,
  input  in_3,
  input  in_4,
  output S,
  output out_6
);

  wire nor_1_out, nor_2_out, not_1_out, not_2_out, not_3_out, not_4_out;

  not not_1 (not_1_out, A);
  not not_2 (not_2_out, B);
  not not_3 (not_3_out, in_3);
  not not_4 (not_4_out, in_4);
  nor nor_1 (nor_1_out, not_1_out, not_1_out);
  nor nor_2 (nor_2_out, not_2_out, not_2_out);
  and and_1 (out_6, not_3_out, not_4_out);
  nor nor_3 (S, nor_1_out, nor_2_out);
endmodule
