// Logisim project EXemplo0501.circ as structural Verilog: 1 circuit, main circuit main
module main (
  input  a,
  input  a_2,
  input  b,
  input  b_2,
  input  a_3,
  input  b_3,
  input  a_4,
  input  b_4,
  output na___b,
  output na___b_2,
  output na___b_3,
  output na___b_4
);

  wire nand_1_out, nand_2_out, nand_3_out, nand_7_out;

  nand nand_1 (nand_1_out, a_2, a_2);
  nand nand_2 (nand_2_out, a_3, a_3);
  nand nand_3 (nand_3_out, a_4, a_4);
  nand nand_4 (na___b_2, nand_1_out, b_2);
  nand nand_5 (na___b_3, nand_2_out, b_3);
  nand nand_6 (na___b_4, nand_3_out, b_4);
  nand nand_7 (nand_7_out, a, a);
  nand nand_8 (na___b, nand_7_out, b);

  // Notes on the sheet:
  //   Matricula : 747560
  //   Nome: Luisa Nogueira Campos SIlva Souza
endmodule
