// Logisim project Exemplo0502.circ as structural Verilog: 1 circuit, main circuit main
module main (
  input  a,
  input  a_2,
  input  b,
  input  b_2,
  input  a_3,
  input  b_3,
  input  a_4,
  input  b_4,
  output na___b,
  output na___b_2,
  output na___b_3,
  output na___b_4
);

  wire NAND_2_out, NAND_3_out, NAND_7_out, NAND_out;

  nand NAND (NAND_out, a, a);
  nand NAND_2 (NAND_2_out, a_3, a_3);
  nand NAND_3 (NAND_3_out, a_4, a_4);
  nand NAND_4 (na___b, NAND_out, b);
  nand NAND_5 (na___b_3, NAND_2_out, b_3);
  nand NAND_6 (na___b_4, NAND_3_out, b_4);
  nand NAND_7 (NAND_7_out, a_2, a_2);
  nand NAND_8 (na___b_2, NAND_7_out, b_2);

  // Notes on the sheet:
  //   Matricula: 747560
  //   Nome: Luisa Nogueira Campos Silva Souza
endmodule
