// Logisim project Exemplo0503.circ as structural Verilog: 1 circuit, main circuit main
module main (
  input  a,
  input  a_2,
  input  b,
  input  b_2,
  input  a_3,
  input  a_4,
  input  b_3,
  input  b_4,
  output a___nb,
  output a___nb_2,
  output a___nb_3,
  output a___nb_4
);

  wire NOR_2_out, NOR_5_out, NOR_6_out, NOR_out;

  nor NOR (NOR_out, b, b);
  nor NOR_2 (NOR_2_out, b_3, b_3);
  nor NOR_3 (a___nb, a, NOR_out);
  nor NOR_4 (a___nb_3, a_3, NOR_2_out);
  nor NOR_5 (NOR_5_out, b_2, b_2);
  nor NOR_6 (NOR_6_out, b_4, b_4);
  nor NOR_7 (a___nb_2, a_2, NOR_5_out);
  nor NOR_8 (a___nb_4, a_4, NOR_6_out);

  // Notes on the sheet:
  //   Matricula: 747560
  //   Nome: Luisa Nogueira Campos Silva Souza
endmodule
