// Logisim project Exemplo0504.circ as structural Verilog: 1 circuit, main circuit main
module main (
  input  a,
  input  a_2,
  input  b,
  input  b_2,
  input  a_3,
  input  a_4,
  input  b_3,
  input  b_4,
  output na___nb,
  output na___nb_2,
  output na___nb_3,
  output na___nb_4
);

  wire NAND_2_out, NAND_3_out, NAND_4_out, NAND_7_out, NAND_8_out, NAND_9_out, NAND_10_out, NAND_out;

  nand NAND (NAND_out, a, a);
  nand NAND_2 (NAND_2_out, b, b);
  nand NAND_3 (NAND_3_out, a_3, a_3);
  nand NAND_4 (NAND_4_out, b_3, b_3);
  nand NAND_5 (na___nb, NAND_out, NAND_2_out);
  nand NAND_6 (na___nb_3, NAND_3_out, NAND_4_out);
  nand NAND_7 (NAND_7_out, a_2, a_2);
  nand NAND_8 (NAND_8_out, b_2, b_2);
  nand NAND_9 (NAND_9_out, a_4, a_4);
  nand NAND_10 (NAND_10_out, b_4, b_4);
  nand NAND_11 (na___nb_2, NAND_7_out, NAND_8_out);
  nand NAND_12 (na___nb_4, NAND_9_out, NAND_10_out);

  // Notes on the sheet:
  //   Matricula: 747560
  //   Nome: Luisa Nogueira Campos Silva Souza
endmodule
