// Logisim project Exemplo0505.circ as structural Verilog: 1 circuit, main circuit main
module main (
  input  a,
  input  a_2,
  input  b,
  input  b_2,
  input  a_3,
  input  a_4,
  input  b_3,
  input  b_4,
  output na___nb,
  output na___nb_2,
  output na___nb_3,
  output na___nb_4
);

  wire NOR_2_out, NOR_3_out, NOR_4_out, NOR_7_out, NOR_8_out, NOR_9_out, NOR_10_out, NOR_out;

  nor NOR (NOR_out, a, a);
  nor NOR_2 (NOR_2_out, b, b);
  nor NOR_3 (NOR_3_out, a_3, a_3);
  nor NOR_4 (NOR_4_out, b_3, b_3);
  nor NOR_5 (na___nb, NOR_out, NOR_2_out);
  nor NOR_6 (na___nb_3, NOR_3_out, NOR_4_out);
  nor NOR_7 (NOR_7_out, a_2, a_2);
  nor NOR_8 (NOR_8_out, b_2, b_2);
  nor NOR_9 (NOR_9_out, a_4, a_4);
  nor NOR_10 (NOR_10_out, b_4, b_4);
  nor NOR_11 (na___nb_2, NOR_7_out, NOR_8_out);
  nor NOR_12 (na___nb_4, NOR_9_out, NOR_10_out);

  // Notes on the sheet:
  //   Nome: Luisa Nogueira Campos Silva Souza
  //   Matricula: 747560
endmodule
