// Logisim project Exemplo0506.circ as structural Verilog: 1 circuit, main circuit main
module main (
  input  a,
  input  a_2,
  input  b,
  input  b_2,
  input  a_3,
  input  a_4,
  input  b_3,
  input  b_4,
  output out_9,
  output out_10,
  output out_11,
  output out_12
);

  wire and_1_out, and_2_out, and_3_out, and_4_out, and_5_out, and_6_out, and_7_out, and_8_out;

  and and_1 (and_1_out, a_2, b_2);
  and and_2 (and_2_out, a_2, b_2, b_2);
  and and_3 (and_3_out, a_4, b_4);
  and and_4 (and_4_out, a_4, b_4, b_4);
  xnor NOR (out_10, and_1_out, and_2_out);
  xnor NOR_2 (out_12, and_3_out, and_4_out);
  and and_5 (and_5_out, a, b);
  and and_6 (and_6_out, a, b, b);
  and and_7 (and_7_out, a_3, b_3);
  and and_8 (and_8_out, a_3, b_3, b_3);
  xnor NOR_3 (out_9, and_5_out, and_6_out);
  xnor NOR_4 (out_11, and_7_out, and_8_out);

  // Notes on the sheet:
  //   Nome: Luisa Nogueira Campos Silva Souza
  //   Matricula:747560
endmodule
