// Logisim project Exemplo0507.circ as structural Verilog: 1 circuit, main circuit main
module main (
  input  a,
  input  a_2,
  input  b,
  input  b_2,
  input  a_3,
  input  a_4,
  input  b_3,
  input  b_4,
  output a_XOR_b,
  output a_XOR_b_2,
  output a_XOR_b_3,
  output a_XOR_b_4
);

  wire and_1_out, and_2_out, and_3_out, and_4_out, and_5_out, and_6_out, and_7_out, and_8_out, not_1_out,
       not_2_out, not_3_out, not_4_out, not_5_out, not_6_out, not_7_out, not_8_out;

  not not_1 (not_1_out, a);
  not not_2 (not_2_out, a_3);
  not not_3 (not_3_out, b);
  not not_4 (not_4_out, b_3);
  and and_1 (and_1_out, not_1_out, b);
  and and_2 (and_2_out, a, not_3_out);
  and and_3 (and_3_out, not_2_out, b_3);
  and and_4 (and_4_out, a_3, not_4_out);
  or or_1 (a_XOR_b, and_1_out, and_2_out);
  or or_2 (a_XOR_b_3, and_3_out, and_4_out);
  not not_5 (not_5_out, a_2);
  not not_6 (not_6_out, b_2);
  not not_7 (not_7_out, a_4);
  not not_8 (not_8_out, b_4);
  and and_5 (and_5_out, not_7_out, b_4);
  and and_6 (and_6_out, a_4, not_8_out);
  and and_7 (and_7_out, not_5_out, b_2);
  and and_8 (and_8_out, a_2, not_6_out);
  or or_3 (a_XOR_b_2, and_7_out, and_8_out);
  or or_4 (a_XOR_b_4, and_5_out, and_6_out);

  // Notes on the sheet:
  //   Nome: Luisa Nogueira Campos Silva Souza
  //   Matricula: 747560
endmodule
