// Logisim project Exemplo_0503.circ as structural Verilog: 1 circuit, main circuit main
module main (
  input  in_1,
  input  in_2,
  output out_3
);

  wire nor_1_out, nor_2_out;

  nor nor_1 (nor_1_out, in_2, in_2);
  nor nor_2 (nor_2_out, in_1, nor_1_out);
  nor nor_3 (out_3, nor_2_out, nor_2_out);

  // Notes on the sheet:
  //   748022
  //   Exemplo_0503
  //   Joao Vitor Lima de Melo
endmodule
