// Logisim project Exemplo_0507.circ as structural Verilog: 1 circuit, main circuit main
module main (
  input  in_1,
  input  in_2,
  output out_3
);

  wire xor_1_out, xor_2_out, xor_3_out;

  xor xor_1 (xor_1_out, in_1, in_2);
  xor xor_2 (xor_2_out, in_1, xor_1_out);
  xor xor_3 (xor_3_out, xor_1_out, in_2);
  xor xor_4 (out_3, xor_2_out, xor_3_out);

  // Notes on the sheet:
  //   748022
  //   Exemplo_0507
  //   Joao Vitor Lima de Melo
endmodule
