// Logisim project LOGISIM-0502.circ as structural Verilog: 1 circuit, main circuit ex0502
module ex0502 (
  input  a,
  input  b,
  output s
);

  wire NAND_2_out, NAND_out;

  nand NAND (NAND_out, a, a);
  nand NAND_2 (NAND_2_out, NAND_out, b);
  nand NAND_3 (s, NAND_2_out, NAND_2_out);

  // Notes on the sheet:
  //   748190
  //   BARBARA LUCIANO ARAUJO
endmodule
