// Logisim project LOGISIM-0503.circ as structural Verilog: 1 circuit, main circuit ex0503
module ex0503 (
  input  a,
  input  b,
  output s
);

  wire NOR_2_out, NOR_out;

  nor NOR (NOR_out, b, b);
  nor NOR_2 (NOR_2_out, a, NOR_out);
  nor NOR_3 (s, NOR_2_out, NOR_2_out);

  // Notes on the sheet:
  //   BARBARA LUCIANO ARAUJO
  //   748190
endmodule
