// Logisim project LOGISIM-0504.circ as structural Verilog: 1 circuit, main circuit ex0504
module ex0504 (
  input  a,
  input  b,
  output s
);

  wire NAND_2_out, NAND_3_out, NAND_out;

  nand NAND (NAND_out, a, a);
  nand NAND_2 (NAND_2_out, b, b);
  nand NAND_3 (NAND_3_out, NAND_out, NAND_2_out);
  nand NAND_4 (s, NAND_3_out, NAND_3_out);

  // Notes on the sheet:
  //   BARBARA LUCIANO ARAUJO
  //   748190
endmodule
