// Logisim project LOGISIM-0505.circ as structural Verilog: 1 circuit, main circuit ex0505
module ex0505 (
  input  a,
  input  b,
  output s
);

  wire NOR_2_out, NOR_out;

  nor NOR (NOR_out, a, a);
  nor NOR_2 (NOR_2_out, b, b);
  nor NOR_3 (s, NOR_out, NOR_2_out);

  // Notes on the sheet:
  //   748190
  //   BARBARA LUCIANO ARAUJO
endmodule
