// Logisim project LOGISIM-0506.circ as structural Verilog: 1 circuit, main circuit ex0506
module ex0506 (
  input  a,
  input  b,
  output s
);

  wire NAND_2_out, NAND_3_out, NAND_4_out, NAND_out;

  nand NAND (NAND_out, a, b);
  nand NAND_2 (NAND_2_out, a, NAND_out);
  nand NAND_3 (NAND_3_out, NAND_out, b);
  nand NAND_4 (NAND_4_out, NAND_2_out, NAND_3_out);
  nand NAND_5 (s, NAND_4_out, NAND_4_out);

  // Notes on the sheet:
  //   748190
  //   748190
  //   748190
  //   748190
  //   748190
  //   748190
  //   748190
  //   BARBARA LUCIANO ARAUJO
  //   BARBARA LUCIANO ARAUJO
  //   BARBARA LUCIANO ARAUJO
  //   BARBARA LUCIANO ARAUJO
  //   BARBARA LUCIANO ARAUJO
  //   BARBARA LUCIANO ARAUJO
  //   BARBARA LUCIANO ARAUJO
  //   748190
  //   BARBARA LUCIANO ARAUJO
endmodule
