// Logisim project LOGISIM-0507.circ as structural Verilog: 1 circuit, main circuit ex0507
module ex0507 (
  input  a,
  input  b,
  output s
);

  wire NOR_2_out, NOR_3_out, NOR_4_out, NOR_out;

  nor NOR (NOR_out, a, b);
  nor NOR_2 (NOR_2_out, a, NOR_out);
  nor NOR_3 (NOR_3_out, NOR_out, b);
  nor NOR_4 (NOR_4_out, NOR_2_out, NOR_3_out);
  nor NOR_5 (s, NOR_4_out, NOR_4_out);

  // Notes on the sheet:
  //   BARBARA LUCIANO ARAUJO
  //   748190
  //   748190
  //   BARBARA LUCIANO ARAUJO
endmodule
