// Logisim project Exemplo_0502.circ as structural Verilog: 1 circuit, main circuit main
module main (
  input  a,
  input  b,
  output s
);

  wire nand_2_out, nand_out;

  nand \nand  (nand_out, a, a);
  nand nand_2 (nand_2_out, nand_out, b);
  nand nand_3 (s, nand_2_out, nand_2_out);
endmodule
