// Logisim project Exemplo_0503.circ as structural Verilog: 1 circuit, main circuit main
module main (
  input  a,
  input  b,
  output s
);

  wire nor_2_out, nor_out;

  nor \nor  (nor_out, a, nor_2_out);
  nor nor_2 (nor_2_out, b, b);
  nor nor_3 (s, nor_out, nor_out);
endmodule
