// Logisim project Exemplo_0504.circ as structural Verilog: 1 circuit, main circuit main
module main (
  input  a,
  input  b,
  output s
);

  wire nand_2_out, nand_3_out, nand_4_out, nand_out;

  nand \nand  (nand_out, a, a);
  nand nand_2 (nand_2_out, b, b);
  nand nand_3 (nand_3_out, nand_out, nand_out);
  nand nand_4 (nand_4_out, nand_2_out, nand_2_out);
  nand nand_5 (s, nand_3_out, nand_4_out);
endmodule
