// Logisim project Exemplo_0505.circ as structural Verilog: 1 circuit, main circuit main
module main (
  input  a,
  input  b,
  output s
);

  wire nor_2_out, nor_3_out, nor_4_out, nor_out;

  nor \nor  (nor_out, a, a);
  nor nor_2 (nor_2_out, b, b);
  nor nor_3 (nor_3_out, nor_out, nor_out);
  nor nor_4 (nor_4_out, nor_2_out, nor_2_out);
  nor nor_5 (s, nor_3_out, nor_4_out);
endmodule
