// Logisim project Exemplo_0506.circ as structural Verilog: 1 circuit, main circuit main
module main (
  input  a,
  input  b,
  output s
);

  wire nand_2_out, nand_3_out, nand_out;

  nand \nand  (nand_out, a, a);
  nand nand_2 (nand_2_out, b, b);
  nand nand_3 (nand_3_out, nand_2_out, nand_2_out);
  nand nand_4 (s, nand_out, nand_3_out);
endmodule
