// Logisim project Exemplo_0507.circ as structural Verilog: 1 circuit, main circuit main
module main (
  input  a,
  input  b,
  output s
);

  wire nor_out;

  nor \nor  (nor_out, a, b);
  nor nor_2 (s, nor_out, nor_out);
endmodule
