// Logisim project GUIA0500.circ as structural Verilog: 7 circuits, main circuit main
module main (
  input  a,
  input  in_2,
  input  b
);

  wire nand_2_out, nand_out;

  nand \nand  (nand_out, a, a, a);
  nand nand_2 (nand_2_out, nand_out, b);
endmodule

module GUIA0502 (
  input  a,
  input  a_2,
  input  in_3,
  input  in_4,
  input  b,
  input  b_2,
  input  a_3,
  input  a_4,
  input  in_9,
  input  in_10,
  input  b_3,
  input  b_4
);

  wire NOR_2_out, NOR_3_out, NOR_4_out, NOR_5_out, NOR_6_out, NOR_7_out, NOR_8_out, NOR_out;

  nor NOR (NOR_out, b, b);
  nor NOR_2 (NOR_2_out, b_4, b_4);
  nor NOR_3 (NOR_3_out, a, NOR_out);
  nor NOR_4 (NOR_4_out, a_4, NOR_2_out);
  nor NOR_5 (NOR_5_out, b_2, b_2);
  nor NOR_6 (NOR_6_out, b_3, b_3);
  nor NOR_7 (NOR_7_out, a_2, NOR_5_out);
  nor NOR_8 (NOR_8_out, a_3, NOR_6_out);
endmodule

module GUIA0501 (
  input  a,
  input  in_2,
  input  b,
  input  a_2,
  input  in_5,
  input  b_2,
  input  a_3,
  input  in_8,
  input  b_3,
  input  a_4,
  input  in_11,
  input  b_4
);

  wire nand_2_out, nand_3_out, nand_4_out, nand_5_out, nand_6_out, nand_7_out, nand_8_out, nand_out;

  nand \nand  (nand_out, a_3, a_3);
  nand nand_2 (nand_2_out, a, a, a);
  nand nand_3 (nand_3_out, a_2, a_2, a_2);
  nand nand_4 (nand_4_out, a_4, a_4);
  nand nand_5 (nand_5_out, nand_2_out, b);
  nand nand_6 (nand_6_out, nand_3_out, b_2);
  nand nand_7 (nand_7_out, nand_out, b_3);
  nand nand_8 (nand_8_out, nand_4_out, b_4);
endmodule

module GUIA0503 (
  input  a,
  input  in_2,
  input  b,
  input  a_2,
  input  in_5,
  input  b_2,
  input  a_3,
  input  in_8,
  input  b_3,
  input  a_4,
  input  in_11,
  input  b_4
);

  wire nand_2_out, nand_3_out, nand_4_out, nand_5_out, nand_6_out, nand_7_out, nand_8_out, nand_9_out,
       nand_10_out, nand_11_out, nand_12_out, nand_out;

  nand \nand  (nand_out, a, a, a);
  nand nand_2 (nand_2_out, b, b);
  nand nand_3 (nand_3_out, a_2, a_2, a_2);
  nand nand_4 (nand_4_out, b_2, b_2);
  nand nand_5 (nand_5_out, a_3, a_3, a_3);
  nand nand_6 (nand_6_out, b_3, b_3);
  nand nand_7 (nand_7_out, a_4, a_4, a_4);
  nand nand_8 (nand_8_out, b_4, b_4);
  nand nand_9 (nand_9_out, nand_out, nand_2_out);
  nand nand_10 (nand_10_out, nand_3_out, nand_4_out);
  nand nand_11 (nand_11_out, nand_5_out, nand_6_out);
  nand nand_12 (nand_12_out, nand_7_out, nand_8_out);
endmodule

module GUIA0504 (
  input  a,
  input  in_2,
  input  b,
  input  a_2,
  input  in_5,
  input  b_2,
  input  a_3,
  input  in_8,
  input  b_3,
  input  a_4,
  input  in_11,
  input  b_4
);

  wire NOR_2_out, NOR_3_out, NOR_4_out, NOR_5_out, NOR_6_out, NOR_7_out, NOR_8_out, NOR_9_out, NOR_10_out,
       NOR_11_out, NOR_12_out, NOR_out;

  nor NOR (NOR_out, b_2, b_2);
  nor NOR_2 (NOR_2_out, b_4, b_4);
  nor NOR_3 (NOR_3_out, a_2, a_2);
  nor NOR_4 (NOR_4_out, a_4, a_4);
  nor NOR_5 (NOR_5_out, NOR_3_out, NOR_out);
  nor NOR_6 (NOR_6_out, NOR_4_out, NOR_2_out);
  nor NOR_7 (NOR_7_out, a, a);
  nor NOR_8 (NOR_8_out, b, b);
  nor NOR_9 (NOR_9_out, a_3, a_3);
  nor NOR_10 (NOR_10_out, b_3, b_3);
  nor NOR_11 (NOR_11_out, NOR_7_out, NOR_8_out);
  nor NOR_12 (NOR_12_out, NOR_9_out, NOR_10_out);
endmodule

module GUIA0505 (
  input  in_1,
  input  in_2,
  input  in_3,
  input  in_4,
  input  in_5,
  input  in_6,
  input  in_7,
  input  in_8,
  input  in_9,
  input  in_10,
  input  in_11,
  input  in_12
);

  wire nand_2_out, nand_3_out, nand_4_out, nand_5_out, nand_6_out, nand_7_out, nand_8_out, nand_9_out,
       nand_10_out, nand_11_out, nand_12_out, nand_13_out, nand_14_out, nand_15_out, nand_16_out,
       nand_17_out, nand_18_out, nand_19_out, nand_20_out, nand_out;

  nand \nand  (nand_out, in_7, in_9);
  nand nand_2 (nand_2_out, in_10, in_12);
  nand nand_3 (nand_3_out, in_1, in_3);
  nand nand_4 (nand_4_out, in_4, in_6);
  nand nand_5 (nand_5_out, in_1, nand_3_out);
  nand nand_6 (nand_6_out, in_4, nand_4_out);
  nand nand_7 (nand_7_out, in_7, nand_out);
  nand nand_8 (nand_8_out, in_10, nand_2_out);
  not nand_9 (nand_9_out, nand_3_out);  // NAND_Gate
  not nand_10 (nand_10_out, nand_4_out);  // NAND_Gate
  not nand_11 (nand_11_out, nand_out);  // NAND_Gate
  not nand_12 (nand_12_out, nand_2_out);  // NAND_Gate
  nand nand_13 (nand_13_out, nand_6_out, nand_10_out);
  nand nand_14 (nand_14_out, nand_7_out, nand_11_out);
  nand nand_15 (nand_15_out, nand_8_out, nand_12_out);
  nand nand_16 (nand_16_out, nand_5_out, nand_9_out);
  nand nand_17 (nand_17_out, nand_14_out, nand_14_out);
  nand nand_18 (nand_18_out, nand_15_out, nand_15_out);
  nand nand_19 (nand_19_out, nand_16_out, nand_16_out);
  nand nand_20 (nand_20_out, nand_13_out, nand_13_out);
endmodule

module GUIA0506 (
  input  in_1,
  input  in_2,
  input  in_3,
  input  in_4,
  input  in_5,
  input  in_6,
  input  in_7,
  input  in_8,
  input  in_9,
  input  in_10,
  input  in_11,
  input  in_12
);

  wire NOR_2_out, NOR_3_out, NOR_4_out, NOR_5_out, NOR_6_out, NOR_7_out, NOR_8_out, NOR_9_out, NOR_10_out,
       NOR_11_out, NOR_12_out, NOR_13_out, NOR_14_out, NOR_15_out, NOR_16_out, NOR_17_out, NOR_18_out,
       NOR_19_out, NOR_20_out, NOR_out;

  nor NOR (NOR_out, in_7, in_9);
  nor NOR_2 (NOR_2_out, in_10, in_12);
  nor NOR_3 (NOR_3_out, in_1, in_3);
  nor NOR_4 (NOR_4_out, in_4, in_6);
  nor NOR_5 (NOR_5_out, in_10, NOR_2_out);
  nor NOR_6 (NOR_6_out, in_1, NOR_3_out);
  nor NOR_7 (NOR_7_out, in_4, NOR_4_out);
  nor NOR_8 (NOR_8_out, in_7, NOR_out);
  not NOR_9 (NOR_9_out, NOR_2_out);  // NOR_Gate
  not NOR_10 (NOR_10_out, NOR_3_out);  // NOR_Gate
  not NOR_11 (NOR_11_out, NOR_4_out);  // NOR_Gate
  not NOR_12 (NOR_12_out, NOR_out);  // NOR_Gate
  nor NOR_13 (NOR_13_out, NOR_7_out, NOR_11_out);
  nor NOR_14 (NOR_14_out, NOR_8_out, NOR_12_out);
  nor NOR_15 (NOR_15_out, NOR_5_out, NOR_9_out);
  nor NOR_16 (NOR_16_out, NOR_6_out, NOR_10_out);
  nor NOR_17 (NOR_17_out, NOR_13_out, NOR_13_out);
  nor NOR_18 (NOR_18_out, NOR_14_out, NOR_14_out);
  nor NOR_19 (NOR_19_out, NOR_15_out, NOR_15_out);
  nor NOR_20 (NOR_20_out, NOR_16_out, NOR_16_out);
endmodule
