// Logisim project Guia_05.circ as structural Verilog
module Guia_0501 (
  input  A,
  input  B,
  input  A_2,
  input  B_2,
  input  A_3,
  input  B_3,
  input  A_4,
  input  B_4,
  output S,
  output S_2,
  output S_3,
  output S_4
);

  wire NAND_2_out, NAND_3_out, NAND_4_out, NAND_out;

  nand NAND (NAND_out, A, A);
  nand NAND_2 (NAND_2_out, A_2, A_2);
  nand NAND_3 (NAND_3_out, A_3, A_3);
  nand NAND_4 (NAND_4_out, A_4, A_4);
  nand NAND_5 (S, NAND_out, B);
  nand NAND_6 (S_2, NAND_2_out, B_2);
  nand NAND_7 (S_3, NAND_3_out, B_3);
  nand NAND_8 (S_4, NAND_4_out, B_4);
endmodule

module Guia_0502 (
  input  A,
  input  B,
  input  A_2,
  input  B_2,
  input  A_3,
  input  B_3,
  input  A_4,
  input  B_4,
  output S,
  output S_2,
  output S_3,
  output S_4
);

  wire NOR_2_out, NOR_3_out, NOR_4_out, NOR_out;

  nor NOR (NOR_out, B, B);
  nor NOR_2 (NOR_2_out, B_2, B_2);
  nor NOR_3 (NOR_3_out, B_3, B_3);
  nor NOR_4 (NOR_4_out, B_4, B_4);
  nor NOR_5 (S, A, NOR_out);
  nor NOR_6 (S_2, A_2, NOR_2_out);
  nor NOR_7 (S_3, A_3, NOR_3_out);
  nor NOR_8 (S_4, A_4, NOR_4_out);
endmodule

module Guia_0503 (
  input  A,
  input  B,
  input  A_2,
  input  B_2,
  input  A_3,
  input  B_3,
  input  A_4,
  input  B_4,
  output S,
  output S_2,
  output S_3,
  output S_4
);

  wire NAND_2_out, NAND_3_out, NAND_4_out, NAND_5_out, NAND_6_out, NAND_7_out, NAND_8_out, NAND_out;

  nand NAND (NAND_out, A, A);
  nand NAND_2 (NAND_2_out, B, B);
  nand NAND_3 (NAND_3_out, A_2, A_2);
  nand NAND_4 (NAND_4_out, B_2, B_2);
  nand NAND_5 (NAND_5_out, A_3, A_3);
  nand NAND_6 (NAND_6_out, B_3, B_3);
  nand NAND_7 (NAND_7_out, A_4, A_4);
  nand NAND_8 (NAND_8_out, B_4, B_4);
  nand NAND_9 (S, NAND_out, NAND_2_out);
  nand NAND_10 (S_2, NAND_3_out, NAND_4_out);
  nand NAND_11 (S_3, NAND_5_out, NAND_6_out);
  nand NAND_12 (S_4, NAND_7_out, NAND_8_out);
endmodule

module Guia_0504 (
  input  A,
  input  B,
  input  A_2,
  input  B_2,
  input  A_3,
  input  B_3,
  input  A_4,
  input  B_4,
  output S,
  output S_2,
  output S_3,
  output S_4
);

  wire NOR_2_out, NOR_3_out, NOR_4_out, NOR_5_out, NOR_6_out, NOR_7_out, NOR_8_out, NOR_out;

  nor NOR (NOR_out, A, A);
  nor NOR_2 (NOR_2_out, B, B);
  nor NOR_3 (NOR_3_out, A_2, A_2);
  nor NOR_4 (NOR_4_out, B_2, B_2);
  nor NOR_5 (NOR_5_out, A_3, A_3);
  nor NOR_6 (NOR_6_out, B_3, B_3);
  nor NOR_7 (NOR_7_out, A_4, A_4);
  nor NOR_8 (NOR_8_out, B_4, B_4);
  nor NOR_9 (S, NOR_out, NOR_2_out);
  nor NOR_10 (S_2, NOR_3_out, NOR_4_out);
  nor NOR_11 (S_3, NOR_5_out, NOR_6_out);
  nor NOR_12 (S_4, NOR_7_out, NOR_8_out);
endmodule

module Guia_0505 (
  input  A,
  input  B,
  input  A_2,
  input  B_2,
  input  A_3,
  input  B_3,
  input  A_4,
  input  B_4,
  output S,
  output S_2,
  output S_3,
  output S_4
);

  wire NAND_2_out, NAND_3_out, NAND_4_out, NAND_5_out, NAND_6_out, NAND_7_out, NAND_8_out, NAND_9_out,
       NAND_10_out, NAND_11_out, NAND_12_out, NAND_13_out, NAND_14_out, NAND_15_out, NAND_16_out, NAND_out;

  nand NAND (NAND_out, A, B);
  nand NAND_2 (NAND_2_out, A_2, B_2);
  nand NAND_3 (NAND_3_out, A_3, B_3);
  nand NAND_4 (NAND_4_out, A_4, B_4);
  nand NAND_5 (NAND_5_out, A, NAND_out);
  nand NAND_6 (NAND_6_out, NAND_out, B);
  nand NAND_7 (NAND_7_out, A_2, NAND_2_out);
  nand NAND_8 (NAND_8_out, NAND_2_out, B_2);
  nand NAND_9 (NAND_9_out, A_3, NAND_3_out);
  nand NAND_10 (NAND_10_out, NAND_3_out, B_3);
  nand NAND_11 (NAND_11_out, A_4, NAND_4_out);
  nand NAND_12 (NAND_12_out, NAND_4_out, B_4);
  nand NAND_13 (NAND_13_out, NAND_5_out, NAND_6_out);
  nand NAND_14 (NAND_14_out, NAND_7_out, NAND_8_out);
  nand NAND_15 (NAND_15_out, NAND_9_out, NAND_10_out);
  nand NAND_16 (NAND_16_out, NAND_11_out, NAND_12_out);
  nand NAND_17 (S, NAND_13_out, NAND_13_out);
  nand NAND_18 (S_2, NAND_14_out, NAND_14_out);
  nand NAND_19 (S_3, NAND_15_out, NAND_15_out);
  nand NAND_20 (S_4, NAND_16_out, NAND_16_out);
endmodule

module Guia_0506 (
  input  A,
  input  B,
  input  A_2,
  input  B_2,
  input  A_3,
  input  B_3,
  input  A_4,
  input  B_4,
  output S,
  output S_2,
  output S_3,
  output S_4
);

  wire NOR_2_out, NOR_3_out, NOR_4_out, NOR_5_out, NOR_6_out, NOR_7_out, NOR_8_out, NOR_9_out, NOR_10_out,
       NOR_11_out, NOR_12_out, NOR_13_out, NOR_14_out, NOR_15_out, NOR_16_out, NOR_out;

  nor NOR (NOR_out, A, B);
  nor NOR_2 (NOR_2_out, A_2, B_2);
  nor NOR_3 (NOR_3_out, A_3, B_3);
  nor NOR_4 (NOR_4_out, A_4, B_4);
  nor NOR_5 (NOR_5_out, A, NOR_out);
  nor NOR_6 (NOR_6_out, NOR_out, B);
  nor NOR_7 (NOR_7_out, A_2, NOR_2_out);
  nor NOR_8 (NOR_8_out, NOR_2_out, B_2);
  nor NOR_9 (NOR_9_out, A_3, NOR_3_out);
  nor NOR_10 (NOR_10_out, NOR_3_out, B_3);
  nor NOR_11 (NOR_11_out, A_4, NOR_4_out);
  nor NOR_12 (NOR_12_out, NOR_4_out, B_4);
  nor NOR_13 (NOR_13_out, NOR_5_out, NOR_6_out);
  nor NOR_14 (NOR_14_out, NOR_7_out, NOR_8_out);
  nor NOR_15 (NOR_15_out, NOR_9_out, NOR_10_out);
  nor NOR_16 (NOR_16_out, NOR_11_out, NOR_12_out);
  nor NOR_17 (S, NOR_13_out, NOR_13_out);
  nor NOR_18 (S_2, NOR_14_out, NOR_14_out);
  nor NOR_19 (S_3, NOR_15_out, NOR_15_out);
  nor NOR_20 (S_4, NOR_16_out, NOR_16_out);
endmodule
