// Logisim project Exemplo_0502.circ as structural Verilog: 1 circuit, main circuit main
module main (
  input  a,
  input  b,
  input  a_2,
  input  b_2,
  output s,
  output s_2
);

  wire nand_a_out, nand_c_out, not_a_out;

  nand nand_a (nand_a_out, a_2, a_2);
  not not_a (not_a_out, a);
  and and_c (s, not_a_out, b);
  nand nand_c (nand_c_out, nand_a_out, b_2);
  nand nand_c2 (s_2, nand_c_out, nand_c_out);
endmodule
