// Logisim project Exemplo_0503.circ as structural Verilog: 1 circuit, main circuit main
module main (
  input  a,
  input  b,
  input  a_2,
  input  b_2,
  output s,
  output s_2
);

  wire nor_b_out, nor_c_out, not_b_out;

  or or_c (s, a, not_b_out);
  not not_b (not_b_out, b);
  nor nor_c (nor_c_out, a_2, nor_b_out);
  nor nor_b (nor_b_out, b_2, b_2);
  nor nor_c2 (s_2, nor_c_out, nor_c_out);
endmodule
