// Logisim project Exemplo_0505.circ as structural Verilog: 1 circuit, main circuit main
module main (
  input  a,
  input  b,
  input  a_2,
  input  b_2,
  output s,
  output s_2
);

  wire nor_a2_out, nor_a_out, nor_b2_out, nor_b_out, not_a_out, not_b_out;

  not not_a (not_a_out, a);
  not not_b (not_b_out, b);
  and and_c (s, not_a_out, not_b_out);
  nor nor_a (nor_a_out, a_2, a_2);
  nor nor_b (nor_b_out, b_2, b_2);
  nor nor_a2 (nor_a2_out, nor_a_out, nor_a_out);
  nor nor_b2 (nor_b2_out, nor_b_out, nor_b_out);
  nor nor_c (s_2, nor_a2_out, nor_b2_out);
endmodule
