// Logisim project Exemplo_0506.circ as structural Verilog: 1 circuit, main circuit main
module main (
  input  a,
  input  b,
  input  a_2,
  input  b_2,
  output s,
  output s_2,
  output s_3,
  output s_4
);

  wire nand_a_out, nand_b_out, nand_c2_out, nand_c3_out, nand_c_out, xnor_c_out;

  xor xnor_c (xnor_c_out, a, b);
  not not_1 (s, xnor_c_out);
  xnor nxor_c2 (s_2, b, a);
  xnor xnor_c_2 (s_4, a_2, b_2);
  nand nand_a (nand_a_out, b_2, b_2);
  nand nand_b (nand_b_out, a_2, a_2);
  nand nand_c (nand_c_out, nand_a_out, a_2);
  nand nand_c2 (nand_c2_out, b_2, nand_b_out);
  nand nand_c3 (nand_c3_out, nand_c_out, nand_c2_out);
  nand nand_c4 (s_3, nand_c3_out, nand_c3_out);
endmodule
