// Logisim project Exemplo_0507.circ as structural Verilog: 1 circuit, main circuit main
module main (
  input  a,
  input  b,
  input  a_2,
  input  b_2,
  output s,
  output s_2,
  output s_3,
  output s_4
);

  wire nor_a_out, nor_b_out, nor_c2_out, nor_c_out;

  xor xor_c2 (s_2, a, b);
  xor xor_c (s, a, b);
  xor xor_c_2 (s_4, a_2, b_2);
  nor nor_a (nor_a_out, a_2, a_2);
  nor nor_b (nor_b_out, b_2, b_2);
  nor nor_c2 (nor_c2_out, a_2, b_2);
  nor nor_c (nor_c_out, nor_a_out, nor_b_out);
  nor nor_c3 (s_3, nor_c_out, nor_c2_out);
endmodule
