// Logisim project Exemplo_0508.circ as structural Verilog: 1 circuit, main circuit main
module main (
  input  a,
  input  b,
  input  a_2,
  input  b_2,
  output s,
  output s_2
);

  wire nand_a2_out, nand_a_out, nand_b2_out, nand_b_out, nand_c_out, not_a_out, not_b_out;

  not not_a (not_a_out, a);
  not not_b (not_b_out, b);
  nand nand_a (nand_a_out, a_2, a_2);
  nand nand_b (nand_b_out, b_2, b_2);
  xor xor_c (s, not_a_out, not_b_out);
  nand nand_c (nand_c_out, nand_a_out, nand_b_out);
  nand nand_a2 (nand_a2_out, nand_a_out, nand_c_out);
  nand nand_b2 (nand_b2_out, nand_c_out, nand_b_out);
  nand nand_c2 (s_2, nand_a2_out, nand_b2_out);
endmodule
