// Logisim project Exemplo_0509.circ as structural Verilog: 1 circuit, main circuit main
module main (
  input  a,
  input  b,
  input  a_2,
  input  b_2,
  output s,
  output s_2
);

  wire and_c_out, nor_a_out, nor_b_out, nor_c2_out, nor_c3_out, nor_c4_out, nor_c_out;

  and and_c (and_c_out, a, b);
  nor nor_a (nor_a_out, a_2, a_2);
  nor nor_b (nor_b_out, b_2, b_2);
  not not_c (s, and_c_out);
  nor nor_c (nor_c_out, nor_a_out, nor_b_out);
  nor nor_c2 (nor_c2_out, nor_c_out, nor_c_out);
  nor nor_c3 (nor_c3_out, nor_c2_out, nor_c2_out);
  nor nor_c4 (nor_c4_out, nor_c2_out, nor_c2_out);
  nor nor_1 (s_2, nor_c3_out, nor_c4_out);
endmodule
