// Logisim project Guia0502.circ as structural Verilog: 1 circuit, main circuit main
module main (
  input  a,
  input  b,
  output out_3
);

  wire nor_1_out, nor_2_out;

  nor nor_1 (nor_1_out, b, b);
  nor nor_2 (nor_2_out, a, nor_1_out);
  nor nor_3 (out_3, nor_2_out, nor_2_out);

  // Notes on the sheet:
  //   754065-5
  //   Arquitetura de Computadores 1
  //   Larissa Valadares Silqueira
  //   Guia05 - 02) a | ~b
endmodule
