// Logisim project Guia0503.circ as structural Verilog: 1 circuit, main circuit main
module main (
  input  a,
  input  b,
  output out_3
);

  nand nand_1 (out_3, a, b);

  // Notes on the sheet:
  //   754065-5
  //   Arquitetura de Computadores 1
  //   Larissa Valadares Silqueira
  //   Guia05 - 03) ~a | ~b
endmodule
