// Logisim project Guia0504.circ as structural Verilog: 1 circuit, main circuit main
module main (
  input  a,
  input  b,
  output out_3
);

  nor nor_1 (out_3, a, b);

  // Notes on the sheet:
  //   754065-5
  //   Arquitetura de Computadores 1
  //   Larissa Valadares Silqueira
  //   Guia05 - 04) ~a & ~b
endmodule
