// Logisim project Guia0505.circ as structural Verilog: 1 circuit, main circuit main
module main (
  input  a,
  input  b,
  output out_3
);

  wire nand_1_out, nand_2_out, nand_3_out, nand_4_out;

  nand nand_1 (nand_1_out, a, b);
  nand nand_2 (nand_2_out, a, nand_1_out);
  nand nand_3 (nand_3_out, nand_1_out, b);
  nand nand_4 (nand_4_out, nand_2_out, nand_3_out);
  nand nand_5 (out_3, nand_4_out, nand_4_out);

  // Notes on the sheet:
  //   754065-5
  //   Arquitetura de Computadores 1
  //   Larissa Valadares Silqueira
  //   Guia05 - 05) ~(a ^ b) = a xnor b
endmodule
