// Logisim project Guia0508.circ as structural Verilog: 1 circuit, main circuit main
module main (
  input  a,
  input  b,
  output out_3
);

  wire nor_1_out, nor_2_out, nor_3_out;

  nor nor_1 (nor_1_out, a, a);
  nor nor_2 (nor_2_out, b, b);
  nor nor_3 (nor_3_out, nor_1_out, nor_2_out);
  nor nor_4 (out_3, nor_3_out, nor_3_out);

  // Notes on the sheet:
  //   754065-5
  //   Arquitetura de Computadores 1
  //   Larissa Valadares Silqueira
  //   Guia05 - 08) ~(a & b)
endmodule
