// Logisim project Exercicios_guia_05.circ as structural Verilog
module ex01 (
  input  a,
  input  b,
  input  a_2,
  input  b_2,
  output s,
  output s_2
);

  wire nand_1_out, nand_2_out, not_1_out;

  not not_1 (not_1_out, a);
  and and_1 (s, not_1_out, b);
  nand nand_1 (nand_1_out, a_2, a_2);
  nand nand_2 (nand_2_out, nand_1_out, b_2);
  nand nand_3 (s_2, nand_2_out, nand_2_out);
endmodule

module ex02 (
  input  a,
  input  b,
  input  a_2,
  input  b_2,
  output s,
  output s_2
);

  wire nor_1_out, nor_2_out, not_1_out;

  or or_1 (s, a, not_1_out);
  not not_1 (not_1_out, b);
  nor nor_1 (nor_1_out, b_2, b_2);
  nor nor_2 (nor_2_out, a_2, nor_1_out);
  nor nor_3 (s_2, nor_2_out, nor_2_out);
endmodule

module ex03 (
  input  a,
  input  b,
  input  a_2,
  input  b_2,
  output s,
  output s_2
);

  wire nand_1_out, nand_2_out, nand_3_out, nand_4_out, not_1_out, not_2_out;

  not not_1 (not_1_out, a);
  or or_1 (s, not_1_out, not_2_out);
  not not_2 (not_2_out, b);
  nand nand_1 (nand_1_out, a_2, a_2);
  nand nand_2 (nand_2_out, b_2, b_2);
  nand nand_3 (nand_3_out, nand_1_out, nand_1_out);
  nand nand_4 (nand_4_out, nand_2_out, nand_2_out);
  nand nand_5 (s_2, nand_3_out, nand_4_out);
endmodule

module ex04 (
  input  a,
  input  b,
  input  a_2,
  input  b_2,
  output s,
  output s_2
);

  wire nor_1_out, nor_2_out, nor_3_out, nor_4_out, not_1_out, not_2_out;

  not not_1 (not_1_out, a);
  and and_1 (s, not_1_out, not_2_out);
  not not_2 (not_2_out, b);
  nor nor_1 (nor_1_out, a_2, a_2);
  nor nor_2 (nor_2_out, b_2, b_2);
  nor nor_3 (nor_3_out, nor_1_out, nor_1_out);
  nor nor_4 (nor_4_out, nor_2_out, nor_2_out);
  nor nor_5 (s_2, nor_3_out, nor_4_out);
endmodule

module ex05 (
  input  a,
  input  b,
  input  a_2,
  input  b_2,
  input  a_3,
  input  b_3,
  output s,
  output s_2,
  output s_3
);

  wire and_1_out, and_2_out, NAND1_out, NAND2_out, NAND3_out, NAND4_out, NAND5_out, NAND6_out, NAND7_out,
       NAND8_out, not_1_out, not_2_out;

  xnor xnor_1 (s, a, b);
  not not_1 (not_1_out, a_2);
  and and_1 (and_1_out, not_1_out, not_2_out);
  not not_2 (not_2_out, b_2);
  and and_2 (and_2_out, a_2, b_2);
  nand NAND1 (NAND1_out, a_3, a_3);
  nand NAND2 (NAND2_out, b_3, b_3);
  or or_1 (s_2, and_1_out, and_2_out);
  nand NAND3 (NAND3_out, NAND1_out, NAND2_out);
  nand NAND4 (NAND4_out, a_3, b_3);
  nand NAND5 (NAND5_out, NAND3_out, NAND3_out);
  nand NAND6 (NAND6_out, NAND4_out, NAND4_out);
  nand NAND7 (NAND7_out, NAND5_out, NAND5_out);
  nand NAND9 (s_3, NAND7_out, NAND8_out);
  nand NAND8 (NAND8_out, NAND6_out, NAND6_out);

  // Notes on the sheet:
  //   w1
  //   w2
  //   w3
  //   w4
  //   w5
  //   w6
  //   w7
  //   w8
endmodule

module ex06 (
  input  a,
  input  b,
  input  a_2,
  input  b_2,
  input  a_3,
  input  b_3,
  output s,
  output s_2,
  output s_3
);

  wire and_1_out, and_2_out, NOR1_out, NOR2_out, NOR3_out, NOR4_out, NOR5_out, NOR6_out, NOR7_out, NOR8_out,
       NOR9_out, not_1_out, not_2_out;

  xor xor_1 (s, a, b);
  not not_1 (not_1_out, a_2);
  and and_1 (and_1_out, not_1_out, b_2);
  and and_2 (and_2_out, a_2, not_2_out);
  not not_2 (not_2_out, b_2);
  nor NOR1 (NOR1_out, a_3, a_3);
  nor NOR2 (NOR2_out, b_3, b_3);
  or or_1 (s_2, and_1_out, and_2_out);
  nor NOR3 (NOR3_out, NOR1_out, NOR1_out);
  nor NOR4 (NOR4_out, b_3, b_3);
  nor NOR5 (NOR5_out, a_3, a_3);
  nor NOR6 (NOR6_out, NOR2_out, NOR2_out);
  nor NOR7 (NOR7_out, NOR3_out, NOR4_out);
  nor NOR8 (NOR8_out, NOR5_out, NOR6_out);
  nor NOR10 (s_3, NOR9_out, NOR9_out);
  nor NOR9 (NOR9_out, NOR7_out, NOR8_out);

  // Notes on the sheet:
  //   w1
  //   w2
  //   w3
  //   w4
  //   w5
  //   w6
  //   w7
  //   w8
  //   w9
endmodule
