// Logisim project 05.circ as structural Verilog: 24 circuits, main circuit main
module main (
  input  X,
  input  Y,
  input  Z,
  output out_4
);

  wire and_2_out, and_out, not_1_out;

  not not_1 (not_1_out, Y);
  and \and  (and_out, not_1_out, Z);
  or or_1 (out_4, and_out, and_2_out);
  and and_2 (and_2_out, X, Z);
endmodule

module Templete (
  input  X,
  input  Y,
  input  Z
);

  // AND_Gate and is placed but not wired
  // OR_Gate or is placed but not wired
endmodule

module _01a (
  input  X,
  input  Y,
  input  Z,
  output out_4
);

  wire and_2_out, and_out, not_1_out;

  not not_1 (not_1_out, Y);
  and \and  (and_out, not_1_out, Z);
  or or_1 (out_4, and_out, and_2_out);
  and and_2 (and_2_out, X, Z);
endmodule

module _01b (
  input  X,
  input  Y,
  input  Z,
  output out_4
);

  wire and_2_out, and_out, not_1_out, not_2_out;

  not not_1 (not_1_out, X);
  and \and  (and_out, not_1_out, Y);
  and and_2 (and_2_out, Y, not_2_out);
  not not_2 (not_2_out, Y);
  or \or  (out_4, and_out, and_2_out);
endmodule

module _01c (
  input  X,
  input  Y,
  input  Z,
  output out_4
);

  wire and_2_out, and_3_out, and_out, not_1_out, not_2_out;

  and \and  (and_out, X, not_1_out);
  not not_1 (not_1_out, Z);
  and and_2 (and_2_out, X, not_2_out);
  not not_2 (not_2_out, Z);
  and and_3 (and_3_out, X, Y);
  or \or  (out_4, and_out, and_2_out, and_3_out);
endmodule

module _01d (
  input  X,
  input  Y,
  input  Z,
  output out_4
);

  wire and_2_out, and_3_out, and_out, not_1_out, not_2_out, not_3_out;

  not not_1 (not_1_out, X);
  not not_2 (not_2_out, X);
  not not_3 (not_3_out, Z);
  and \and  (and_out, not_1_out, Z);
  and and_2 (and_2_out, not_2_out, Y);
  and and_3 (and_3_out, not_3_out, Y);
  or \or  (out_4, and_out, and_2_out, and_3_out);
endmodule

module _01e (
  input  X,
  input  Y,
  input  Z,
  output out_4
);

  wire and_2_out, and_out, not_1_out, not_2_out;

  not not_1 (not_1_out, X);
  and \and  (and_out, not_1_out, not_2_out);
  not not_2 (not_2_out, Z);
  and and_2 (and_2_out, X, Z);
  or \or  (out_4, and_out, and_2_out);
endmodule

module _02a (
  input  X,
  input  Y,
  input  Z,
  output out_4
);

  wire not_1_out, not_2_out, not_3_out, or_2_out, or_out;

  not not_1 (not_1_out, X);
  or \or  (or_out, not_1_out, Z);
  not not_2 (not_2_out, X);
  or or_2 (or_2_out, not_2_out, not_3_out);
  not not_3 (not_3_out, Y);
  and \and  (out_4, or_out, or_2_out);
endmodule

module _02b (
  input  X,
  input  Y,
  input  Z,
  output out_4
);

  wire not_1_out, not_2_out, not_3_out, or_2_out, or_out;

  or \or  (or_out, X, not_1_out);
  not not_1 (not_1_out, Z);
  not not_2 (not_2_out, Z);
  or or_2 (or_2_out, not_2_out, not_3_out);
  not not_3 (not_3_out, X);
  and \and  (out_4, or_out, or_2_out);
endmodule

module _02c (
  input  X,
  input  Y,
  input  Z,
  output out_4
);

  wire not_1_out, not_2_out, not_3_out, or_2_out, or_3_out, or_out;

  or \or  (or_out, X, not_1_out);
  not not_1 (not_1_out, Z);
  or or_2 (or_2_out, X, not_2_out);
  not not_2 (not_2_out, Y);
  or or_3 (or_3_out, Y, not_3_out);
  not not_3 (not_3_out, Z);
  and \and  (out_4, or_out, or_2_out, or_3_out);
endmodule

module _02d (
  input  X,
  input  Y,
  input  Z,
  output out_4
);

  wire not_1_out, not_2_out, or_2_out, or_out;

  or \or  (or_out, Y, Z);
  not not_1 (not_1_out, Z);
  or or_2 (or_2_out, not_1_out, not_2_out);
  not not_2 (not_2_out, Y);
  and \and  (out_4, or_out, or_2_out);
endmodule

module _02e (
  input  X,
  input  Y,
  input  Z,
  output out_4
);

  wire not_1_out, not_2_out, not_3_out, or_2_out, or_out;

  not not_1 (not_1_out, Y);
  or \or  (or_out, not_1_out, Z);
  not not_2 (not_2_out, X);
  or or_2 (or_2_out, not_2_out, not_3_out);
  not not_3 (not_3_out, Y);
  and \and  (out_4, or_out, or_2_out);
endmodule

module _03a (
  input  X,
  input  Y,
  input  w,
  input  Z,
  output out_5
);

  wire and_2_out, and_out, not_1_out, not_2_out;

  not not_1 (not_1_out, X);
  not not_2 (not_2_out, Y);
  and \and  (and_out, not_1_out, Y, Y);
  or \or  (out_5, and_out, and_2_out);
  and and_2 (and_2_out, not_2_out, X, w);
endmodule

module _03b (
  input  X,
  input  Y,
  input  w,
  input  Z,
  output out_5
);

  wire and_2_out, and_3_out, and_4_out, and_out, not_1_out, not_2_out, not_3_out, not_4_out, not_5_out,
       not_6_out, not_7_out, not_8_out, not_9_out;

  not not_1 (not_1_out, X);
  not not_2 (not_2_out, Y);
  not not_3 (not_3_out, Z);
  not not_4 (not_4_out, Y);
  not not_5 (not_5_out, w);
  not not_6 (not_6_out, Z);
  not not_7 (not_7_out, Y);
  not not_8 (not_8_out, w);
  not not_9 (not_9_out, w);
  and \and  (and_out, not_1_out, not_2_out, not_3_out);
  and and_2 (and_2_out, not_4_out, not_5_out, not_6_out);
  and and_3 (and_3_out, X, not_7_out, not_8_out);
  and and_4 (and_4_out, X, not_9_out, Z);
  or \or  (out_5, and_out, and_2_out, and_3_out, and_4_out);
endmodule

module _03c (
  input  X,
  input  Y,
  input  w,
  input  Z,
  output out_5
);

  wire and_2_out, and_3_out, and_4_out, and_5_out, and_6_out, and_out, not_1_out, not_2_out, not_3_out,
       not_4_out, not_5_out, not_6_out, not_7_out, not_8_out, not_9_out, not_10_out, not_11_out, not_12_out;

  not not_1 (not_1_out, X);
  not not_2 (not_2_out, Y);
  not not_3 (not_3_out, w);
  not not_4 (not_4_out, X);
  not not_5 (not_5_out, Y);
  not not_6 (not_6_out, Z);
  not not_7 (not_7_out, X);
  not not_8 (not_8_out, w);
  not not_9 (not_9_out, Z);
  not not_10 (not_10_out, Y);
  not not_11 (not_11_out, w);
  not not_12 (not_12_out, Z);
  and \and  (and_out, not_1_out, not_2_out, not_3_out);
  and and_2 (and_2_out, not_4_out, not_5_out, not_6_out);
  and and_3 (and_3_out, not_7_out, not_8_out, not_9_out);
  and and_4 (and_4_out, not_10_out, not_11_out, not_12_out);
  and and_5 (and_5_out, Y, w, Z);
  and and_6 (and_6_out, X, w, Z);
  or \or  (out_5, and_out, and_2_out, and_3_out, and_4_out, and_5_out, and_6_out);
endmodule

module _03d (
  input  X,
  input  Y,
  input  w,
  input  Z,
  output out_5
);

  wire and_2_out, and_3_out, and_4_out, and_out, not_1_out, not_2_out, not_3_out, not_4_out, not_5_out;

  not not_1 (not_1_out, X);
  not not_2 (not_2_out, w);
  not not_3 (not_3_out, X);
  not not_4 (not_4_out, Z);
  not not_5 (not_5_out, Z);
  and \and  (and_out, not_1_out, Y, not_2_out);
  and and_2 (and_2_out, not_3_out, w, Z);
  and and_3 (and_3_out, X, w, not_4_out);
  and and_4 (and_4_out, X, Y, not_5_out);
  or \or  (out_5, and_out, and_2_out, and_3_out, and_4_out);
endmodule

module _03e (
  input  X,
  input  Y,
  input  w,
  input  Z,
  output out_5
);

  wire and_2_out, and_3_out, and_4_out, and_5_out, and_6_out, and_out, not_1_out, not_2_out, not_3_out,
       not_4_out, not_5_out, not_6_out, not_7_out, not_8_out, not_9_out, not_10_out, not_11_out, not_12_out;

  not not_1 (not_1_out, X);
  not not_2 (not_2_out, Y);
  not not_3 (not_3_out, w);
  not not_4 (not_4_out, X);
  not not_5 (not_5_out, w);
  not not_6 (not_6_out, Z);
  not not_7 (not_7_out, w);
  not not_8 (not_8_out, w);
  not not_9 (not_9_out, Z);
  not not_10 (not_10_out, Y);
  not not_11 (not_11_out, w);
  not not_12 (not_12_out, X);
  and \and  (and_out, not_1_out, not_2_out, not_3_out);
  and and_2 (and_2_out, not_4_out, not_5_out, not_6_out);
  and and_3 (and_3_out, X, Y, not_7_out);
  and and_4 (and_4_out, X, not_8_out, not_9_out);
  and and_5 (and_5_out, not_10_out, not_11_out, Z);
  and and_6 (and_6_out, not_12_out, w, Z);
  or \or  (out_5, and_out, and_2_out, and_3_out, and_4_out, and_5_out, and_6_out);
endmodule

module _04a (
  input  X,
  input  Y,
  input  w,
  input  Z,
  output out_5
);

  wire not_1_out, not_2_out, not_3_out, not_4_out, not_5_out, not_6_out, or_2_out, or_3_out, or_out;

  not not_1 (not_1_out, w);
  not not_2 (not_2_out, Z);
  not not_3 (not_3_out, Y);
  not not_4 (not_4_out, Z);
  not not_5 (not_5_out, Y);
  not not_6 (not_6_out, Z);
  or \or  (or_out, X, not_1_out, not_2_out);
  or or_2 (or_2_out, X, not_3_out, not_4_out);
  or or_3 (or_3_out, not_5_out, w, not_6_out);
  and \and  (out_5, or_out, or_2_out, or_3_out);
endmodule

module _04b (
  input  X,
  input  Y,
  input  w,
  input  Z,
  output out_5
);

  wire not_1_out, not_2_out, not_3_out, or_2_out, or_3_out, or_out;

  not not_1 (not_1_out, X);
  not not_2 (not_2_out, X);
  not not_3 (not_3_out, X);
  or \or  (or_out, not_1_out, Y, w);
  or or_2 (or_2_out, not_2_out, Y, Z);
  or or_3 (or_3_out, not_3_out, w, Z);
  and \and  (out_5, or_out, or_2_out, or_3_out);
endmodule

module _04c (
  input  X,
  input  Y,
  input  w,
  input  Z,
  output out_5
);

  wire not_1_out, not_2_out, not_3_out, not_4_out, not_5_out, not_6_out, or_2_out, or_3_out, or_out;

  not not_1 (not_1_out, X);
  not not_2 (not_2_out, X);
  not not_3 (not_3_out, Y);
  not not_4 (not_4_out, X);
  not not_5 (not_5_out, Y);
  not not_6 (not_6_out, Z);
  or \or  (or_out, not_1_out, w, Z);
  or or_2 (or_2_out, not_2_out, not_3_out, w);
  or or_3 (or_3_out, not_4_out, not_5_out, not_6_out);
  and \and  (out_5, or_out, or_2_out, or_3_out);
endmodule

module _04d (
  input  X,
  input  Y,
  input  w,
  input  Z,
  output out_5
);

  wire not_1_out, not_2_out, not_3_out, not_4_out, not_5_out, not_6_out, not_7_out, or_2_out, or_3_out,
       or_out;

  not not_1 (not_1_out, Z);
  not not_2 (not_2_out, Y);
  not not_3 (not_3_out, w);
  not not_4 (not_4_out, Z);
  not not_5 (not_5_out, X);
  not not_6 (not_6_out, Y);
  not not_7 (not_7_out, Z);
  or \or  (or_out, X, w, not_1_out);
  or or_2 (or_2_out, not_2_out, not_3_out, not_4_out);
  or or_3 (or_3_out, not_5_out, not_6_out, not_7_out);
  and \and  (out_5, or_out, or_2_out, or_3_out);
endmodule

module _04e (
  input  X,
  input  Y,
  input  w,
  input  Z,
  output out_5
);

  wire not_1_out, not_2_out, not_3_out, not_4_out, not_5_out, not_6_out, not_7_out, or_2_out, or_3_out,
       or_4_out, or_out;

  not not_1 (not_1_out, w);
  not not_2 (not_2_out, X);
  not not_3 (not_3_out, w);
  not not_4 (not_4_out, X);
  not not_5 (not_5_out, w);
  not not_6 (not_6_out, X);
  not not_7 (not_7_out, w);
  or \or  (or_out, X, not_1_out, Z);
  or or_2 (or_2_out, not_2_out, not_3_out, Z);
  or or_3 (or_3_out, not_4_out, Y, not_5_out);
  or or_4 (or_4_out, not_6_out, not_7_out, Y);
  and \and  (out_5, or_out, or_2_out, or_3_out, or_4_out);
endmodule

module _05 (
  input  x,
  input  y,
  input  z,
  input  x_2,
  input  y_2,
  input  z_2,
  output out_7,
  output out_8
);

  wire and_1_out, and_2_out, and_3_out, and_4_out, not_1_out, not_2_out, not_3_out, not_4_out, not_5_out,
       not_6_out, not_7_out, or_1_out, or_2_out;

  not not_1 (not_1_out, y);
  not not_2 (not_2_out, x);
  and and_1 (and_1_out, z, y);
  not not_3 (not_3_out, x);
  not not_4 (not_4_out, x_2);
  and and_2 (and_2_out, y_2, z_2);
  not not_5 (not_5_out, or_1_out);
  or or_1 (or_1_out, not_1_out, not_2_out);
  not not_6 (not_6_out, and_3_out);
  and and_3 (and_3_out, y, x);
  not not_7 (not_7_out, or_2_out);
  or or_2 (or_2_out, and_1_out, not_3_out);
  or or_3 (out_8, not_4_out, and_2_out);
  and and_4 (and_4_out, not_5_out, not_6_out);
  or or_4 (out_7, and_4_out, not_7_out);

  // Notes on the sheet:
  //   Expressão Original
  //   Simplificado
endmodule

module _06 (
  input  x,
  input  y,
  input  w,
  input  z,
  output out_5
);

  wire and_1_out, and_2_out, and_3_out, not_1_out, not_2_out, not_3_out, not_4_out, not_5_out, not_6_out,
       not_7_out, or_1_out, or_2_out;

  not not_1 (not_1_out, y);
  not not_2 (not_2_out, x);
  not not_3 (not_3_out, w);
  and and_1 (and_1_out, z, w, y);
  not not_4 (not_4_out, x);
  not not_5 (not_5_out, or_1_out);
  or or_1 (or_1_out, not_1_out, w, not_2_out);
  not not_6 (not_6_out, and_2_out);
  and and_2 (and_2_out, y, not_3_out, x);
  or or_2 (or_2_out, and_1_out, not_4_out);
  not not_7 (not_7_out, or_2_out);
  and and_3 (and_3_out, not_5_out, not_6_out);
  or or_3 (out_5, and_3_out, not_7_out);
endmodule
