// Logisim project 06.circ as structural Verilog: 1 circuit, main circuit main
module main (
  input  X,
  input  Y,
  input  W,
  input  Z,
  input  X_2,
  input  Y_2,
  input  W_2,
  input  Z_2,
  output out_9,
  output out_10
);

  wire and_1_out, and_2_out, and_3_out, and_4_out, and_5_out, and_6_out, not_1_out, not_2_out, not_3_out,
       not_4_out, not_5_out, not_6_out, not_7_out, not_8_out, not_9_out, not_10_out, not_11_out, not_12_out,
       not_13_out, not_14_out, not_15_out, or_1_out, or_2_out, or_3_out, or_4_out, or_5_out;

  not not_1 (not_1_out, Y);
  not not_2 (not_2_out, X);
  not not_3 (not_3_out, W);
  and and_1 (and_1_out, Z, W, Y);
  not not_4 (not_4_out, Y_2);
  not not_5 (not_5_out, X_2);
  not not_6 (not_6_out, X_2);
  not not_7 (not_7_out, X_2);
  not not_8 (not_8_out, W_2);
  not not_9 (not_9_out, Z_2);
  not not_10 (not_10_out, X_2);
  not not_11 (not_11_out, Z_2);
  or or_1 (or_1_out, not_1_out, W, not_2_out);
  and and_2 (and_2_out, Y, not_3_out, X);
  or or_2 (or_2_out, and_1_out, not_12_out);
  not not_12 (not_12_out, X);
  or or_3 (or_3_out, not_4_out, not_5_out);
  or or_4 (or_4_out, not_6_out, Y_2);
  and and_3 (and_3_out, not_7_out, not_8_out, Z_2);
  and and_4 (and_4_out, not_9_out, W_2);
  or or_5 (or_5_out, not_10_out, W_2, not_11_out);
  not not_13 (not_13_out, or_1_out);
  not not_14 (not_14_out, and_2_out);
  not not_15 (not_15_out, or_2_out);
  and and_5 (and_5_out, not_13_out, not_14_out);
  and and_6 (and_6_out, or_3_out, or_4_out, and_3_out, and_4_out);
  and and_7 (out_10, and_6_out, or_5_out);
  or or_6 (out_9, and_5_out, not_15_out);

  // Notes on the sheet:
  //   Expressão Original
  //   Simplificada
endmodule
