// Logisim project Guia06.circ as structural Verilog
module Guia_0601 (
  input  X,
  input  Y,
  input  Z,
  input  X_2,
  input  Y_2,
  input  Z_2,
  input  X_3,
  input  Y_3,
  input  Z_3,
  input  X_4,
  input  Y_4,
  input  Z_4,
  input  X_5,
  input  Y_5,
  input  Z_5,
  output S,
  output S_2,
  output S_3,
  output S_4,
  output S_5
);

  wire AND_2_out, AND_3_out, AND_4_out, AND_5_out, AND_6_out, AND_7_out, AND_8_out, AND_9_out, AND_10_out,
       AND_11_out, AND_12_out, AND_out, NOT_2_out, NOT_3_out, NOT_4_out, NOT_5_out, NOT_6_out, NOT_7_out,
       NOT_8_out, NOT_9_out, NOT_10_out, NOT_out;

  not NOT (NOT_out, Y);
  not NOT_2 (NOT_2_out, X_2);
  not NOT_3 (NOT_3_out, Z_2);
  not NOT_4 (NOT_4_out, Y_3);
  not NOT_5 (NOT_5_out, Y_3);
  not NOT_6 (NOT_6_out, X_4);
  not NOT_7 (NOT_7_out, X_4);
  not NOT_8 (NOT_8_out, Z_4);
  not NOT_9 (NOT_9_out, X_5);
  not NOT_10 (NOT_10_out, Z_5);
  and AND (AND_out, NOT_out, Z);
  and AND_2 (AND_2_out, X, Z);
  and AND_3 (AND_3_out, NOT_2_out, Y_2);
  and AND_4 (AND_4_out, Y_2, NOT_3_out);
  and AND_5 (AND_5_out, Y_3, NOT_4_out);
  and AND_6 (AND_6_out, X_3, NOT_5_out);
  and AND_7 (AND_7_out, X_3, Y_3);
  and AND_8 (AND_8_out, NOT_6_out, Z_4);
  and AND_9 (AND_9_out, NOT_7_out, Y_4);
  and AND_10 (AND_10_out, Y_4, NOT_8_out);
  and AND_11 (AND_11_out, NOT_9_out, NOT_10_out);
  and AND_12 (AND_12_out, X_5, Z_5);
  or OR (S, AND_out, AND_2_out);
  or OR_2 (S_2, AND_3_out, AND_4_out);
  or OR_3 (S_3, AND_5_out, AND_6_out, AND_7_out);
  or OR_4 (S_4, AND_8_out, AND_9_out, AND_10_out);
  or OR_5 (S_5, AND_11_out, AND_12_out);

  assign Z_3 = Y_3;

  // Notes on the sheet:
  //   a.) (y' . z) + (x . z)
  //   b.) (x' . y) + (y . z')
  //   c.) (y . z') + (x . z') + (x . y)
  //   d.) (x' . z) + (x' . y) + (y. z')
  //   e.) (x' . z') + (x . z)
endmodule

module Guia_0602 (
  input  X,
  input  Y,
  input  Z,
  input  X_2,
  input  Y_2,
  input  Z_2,
  input  X_3,
  input  Y_3,
  input  Z_3,
  input  X_4,
  input  Y_4,
  input  Z_4,
  input  X_5,
  input  Y_5,
  input  Z_5,
  output S,
  output S_2,
  output S_3,
  output S_4,
  output S_5
);

  wire NOT_2_out, NOT_3_out, NOT_4_out, NOT_5_out, NOT_6_out, NOT_7_out, NOT_8_out, NOT_9_out, NOT_10_out,
       NOT_11_out, NOT_12_out, NOT_13_out, NOT_14_out, NOT_out, OR_2_out, OR_3_out, OR_4_out, OR_5_out,
       OR_6_out, OR_7_out, OR_8_out, OR_9_out, OR_10_out, OR_11_out, OR_out;

  not NOT (NOT_out, X);
  not NOT_2 (NOT_2_out, X);
  not NOT_3 (NOT_3_out, Y);
  not NOT_4 (NOT_4_out, Z_2);
  not NOT_5 (NOT_5_out, X_2);
  not NOT_6 (NOT_6_out, Z_2);
  not NOT_7 (NOT_7_out, Z_3);
  not NOT_8 (NOT_8_out, Z_3);
  not NOT_9 (NOT_9_out, Y_3);
  not NOT_10 (NOT_10_out, Y_4);
  not NOT_11 (NOT_11_out, Z_4);
  not NOT_12 (NOT_12_out, Y_5);
  not NOT_13 (NOT_13_out, X_5);
  not NOT_14 (NOT_14_out, Y_5);
  or OR (OR_out, NOT_out, Z);
  or OR_2 (OR_2_out, NOT_2_out, NOT_3_out);
  or OR_3 (OR_3_out, Y_2, NOT_4_out);
  or OR_4 (OR_4_out, NOT_5_out, NOT_6_out);
  or OR_5 (OR_5_out, X_3, NOT_7_out);
  or OR_6 (OR_6_out, Y_3, NOT_8_out);
  or OR_7 (OR_7_out, X_3, NOT_9_out);
  or OR_8 (OR_8_out, Y_4, Z_4);
  or OR_9 (OR_9_out, NOT_10_out, NOT_11_out);
  or OR_10 (OR_10_out, NOT_12_out, Z_5);
  or OR_11 (OR_11_out, NOT_13_out, NOT_14_out);
  and AND (S, OR_out, OR_2_out);
  and AND_2 (S_2, OR_3_out, OR_4_out);
  and AND_3 (S_3, OR_5_out, OR_6_out, OR_7_out);
  and AND_4 (S_4, OR_8_out, OR_9_out);
  and AND_5 (S_5, OR_10_out, OR_11_out);

  // Notes on the sheet:
  //   a.) (X' + Z) . (X' + Y')
  //   b.) (Y + Z') . (X' + Z')
  //   c.) (X + Z') . (Y + Z') . (X + Y')
  //   d.) (Y + Z) . (Y' + Z')
  //   e.) (Y' + Z) . (X' + Y')
endmodule

module Guia_0603 (
  input  X,
  input  Y,
  input  W,
  input  Z,
  input  X_2,
  input  Y_2,
  input  W_2,
  input  Z_2,
  input  X_3,
  input  Y_3,
  input  W_3,
  input  Z_3,
  input  X_4,
  input  Y_4,
  input  W_4,
  input  Z_4,
  input  X_5,
  input  Y_5,
  input  W_5,
  input  Z_5,
  output S,
  output S_2,
  output S_3,
  output S_4,
  output S_5
);

  wire AND_2_out, AND_3_out, AND_4_out, AND_5_out, AND_6_out, AND_7_out, AND_8_out, AND_9_out, AND_10_out,
       AND_11_out, AND_12_out, AND_13_out, AND_14_out, AND_15_out, AND_16_out, AND_17_out, AND_18_out,
       AND_19_out, AND_20_out, AND_21_out, AND_22_out, AND_23_out, AND_24_out, AND_25_out, AND_26_out,
       AND_27_out, AND_28_out, AND_29_out, AND_out, NOT_2_out, NOT_3_out, NOT_4_out, NOT_5_out, NOT_6_out,
       NOT_7_out, NOT_8_out, NOT_9_out, NOT_10_out, NOT_11_out, NOT_12_out, NOT_13_out, NOT_14_out,
       NOT_15_out, NOT_16_out, NOT_17_out, NOT_18_out, NOT_19_out, NOT_20_out, NOT_21_out, NOT_22_out,
       NOT_23_out, NOT_24_out, NOT_25_out, NOT_26_out, NOT_27_out, NOT_28_out, NOT_29_out, NOT_30_out,
       NOT_31_out, NOT_32_out, NOT_33_out, NOT_34_out, NOT_35_out, NOT_36_out, NOT_37_out, NOT_38_out,
       NOT_39_out, NOT_40_out, NOT_41_out, NOT_42_out, NOT_43_out, NOT_44_out, NOT_45_out, NOT_46_out,
       NOT_47_out, NOT_48_out, NOT_49_out, NOT_50_out, NOT_51_out, NOT_52_out, NOT_53_out, NOT_54_out,
       NOT_55_out, NOT_56_out, NOT_57_out, NOT_out;

  not NOT (NOT_out, X);
  not NOT_2 (NOT_2_out, Z);
  not NOT_3 (NOT_3_out, Y);
  not NOT_4 (NOT_4_out, Z);
  not NOT_5 (NOT_5_out, X);
  not NOT_6 (NOT_6_out, W);
  not NOT_7 (NOT_7_out, X);
  not NOT_8 (NOT_8_out, X_2);
  not NOT_9 (NOT_9_out, Y_2);
  not NOT_10 (NOT_10_out, Z_2);
  not NOT_11 (NOT_11_out, Y_2);
  not NOT_12 (NOT_12_out, W_2);
  not NOT_13 (NOT_13_out, Z_2);
  not NOT_14 (NOT_14_out, X_2);
  not NOT_15 (NOT_15_out, Y_2);
  not NOT_16 (NOT_16_out, W_2);
  not NOT_17 (NOT_17_out, Y_2);
  not NOT_18 (NOT_18_out, W_2);
  not NOT_19 (NOT_19_out, W_2);
  not NOT_20 (NOT_20_out, X_3);
  not NOT_21 (NOT_21_out, Y_3);
  not NOT_22 (NOT_22_out, W_3);
  not NOT_23 (NOT_23_out, X_3);
  not NOT_24 (NOT_24_out, Y_3);
  not NOT_25 (NOT_25_out, Z_3);
  not NOT_26 (NOT_26_out, X_3);
  not NOT_27 (NOT_27_out, W_3);
  not NOT_28 (NOT_28_out, Z_3);
  not NOT_29 (NOT_29_out, Y_3);
  not NOT_30 (NOT_30_out, W_3);
  not NOT_31 (NOT_31_out, Z_3);
  not NOT_32 (NOT_32_out, Y_4);
  not NOT_33 (NOT_33_out, Z_4);
  not NOT_34 (NOT_34_out, X_4);
  not NOT_35 (NOT_35_out, W_4);
  not NOT_36 (NOT_36_out, W_4);
  not NOT_37 (NOT_37_out, Z_4);
  not NOT_38 (NOT_38_out, X_4);
  not NOT_39 (NOT_39_out, Z_4);
  not NOT_40 (NOT_40_out, Z_4);
  not NOT_41 (NOT_41_out, X_5);
  not NOT_42 (NOT_42_out, Y_5);
  not NOT_43 (NOT_43_out, W_5);
  not NOT_44 (NOT_44_out, X_5);
  not NOT_45 (NOT_45_out, Y_5);
  not NOT_46 (NOT_46_out, Z_5);
  not NOT_47 (NOT_47_out, Y_5);
  not NOT_48 (NOT_48_out, W_5);
  not NOT_49 (NOT_49_out, Z_5);
  not NOT_50 (NOT_50_out, Y_5);
  not NOT_51 (NOT_51_out, W_5);
  not NOT_52 (NOT_52_out, X_5);
  not NOT_53 (NOT_53_out, Z_5);
  not NOT_54 (NOT_54_out, Y_5);
  not NOT_55 (NOT_55_out, W_5);
  not NOT_56 (NOT_56_out, W_5);
  not NOT_57 (NOT_57_out, Z_5);
  and AND (AND_out, NOT_out, W, NOT_2_out);
  and AND_2 (AND_2_out, NOT_3_out, W, NOT_4_out);
  and AND_3 (AND_3_out, NOT_5_out, Y, NOT_6_out);
  and AND_4 (AND_4_out, X, NOT_7_out, W);
  and AND_5 (AND_5_out, NOT_8_out, NOT_9_out, NOT_10_out);
  and AND_6 (AND_6_out, NOT_11_out, NOT_12_out, NOT_13_out);
  and AND_7 (AND_7_out, NOT_14_out, NOT_15_out, W_2);
  and AND_8 (AND_8_out, Y_2, NOT_16_out, Z_2);
  and AND_9 (AND_9_out, X_2, NOT_17_out, NOT_18_out);
  and AND_10 (AND_10_out, X_2, NOT_19_out, Z_2);
  and AND_11 (AND_11_out, NOT_20_out, NOT_21_out, NOT_22_out);
  and AND_12 (AND_12_out, NOT_23_out, NOT_24_out, NOT_25_out);
  and AND_13 (AND_13_out, NOT_26_out, NOT_27_out, NOT_28_out);
  and AND_14 (AND_14_out, NOT_29_out, NOT_30_out, NOT_31_out);
  and AND_15 (AND_15_out, Y_3, W_3, Z_3);
  and AND_16 (AND_16_out, Y_3, W_3, Z_3);
  and AND_17 (AND_17_out, NOT_32_out, W_4, NOT_33_out);
  and AND_18 (AND_18_out, NOT_34_out, Y_4, NOT_35_out);
  and AND_19 (AND_19_out, Y_4, NOT_36_out, NOT_37_out);
  and AND_20 (AND_20_out, NOT_38_out, Y_4, Z_4);
  and AND_21 (AND_21_out, X_4, W_4, NOT_39_out);
  and AND_22 (AND_22_out, X_4, Y_4, NOT_40_out);
  and AND_23 (AND_23_out, NOT_41_out, NOT_42_out, NOT_43_out);
  and AND_24 (AND_24_out, NOT_44_out, NOT_45_out, NOT_46_out);
  and AND_25 (AND_25_out, NOT_47_out, NOT_48_out, NOT_49_out);
  and AND_26 (AND_26_out, NOT_50_out, NOT_51_out, Z_5);
  and AND_27 (AND_27_out, NOT_52_out, W_5, NOT_53_out);
  and AND_28 (AND_28_out, X_5, NOT_54_out, NOT_55_out);
  and AND_29 (AND_29_out, X_5, NOT_56_out, NOT_57_out);
  or OR (S, AND_out, AND_2_out, AND_3_out, AND_4_out);
  or OR_2 (S_2, AND_5_out, AND_6_out, AND_7_out, AND_8_out, AND_9_out, AND_10_out);
  or OR_3 (S_3, AND_11_out, AND_12_out, AND_13_out, AND_14_out, AND_15_out, AND_16_out);
  or OR_4 (S_4, AND_17_out, AND_18_out, AND_19_out, AND_20_out, AND_21_out, AND_22_out);
  or OR_5 (S_5, AND_23_out, AND_24_out, AND_25_out, AND_26_out, AND_27_out, AND_28_out, AND_29_out);

  // Notes on the sheet:
  //   a.) (x' . w . z') + (y' . w . z') + (x' . y . w) + (x . y' . w)
  //   b.) (x' . y' . z') + (y' . w' . z') + (x' . y' . w) + (y . w' . z) + (x . y' . w') + (x . w' . z)
  //   c.) (x' . y' .w') + (x' . y' . z') + (x' . w' . z') + (y' . w' . z') + (y . w . z) + (x . w . z)
  //   d.) (y' . w . z') + (x' . y . w') + (y . w' . z') + (x' . y . z) + (x . w . z') + (x . y . z')
  //   e.) (x' . y' . w') + (x' . y' . z') + (y' . w' . z') + (y' . w' . z) + (x' . w . z') + (x . y' . w') + (x . w' . z')
endmodule

module Guia_0604 (
  input  X,
  input  Y,
  input  W,
  input  Z,
  input  X_2,
  input  Y_2,
  input  W_2,
  input  Z_2,
  input  X_3,
  input  Y_3,
  input  W_3,
  input  Z_3,
  input  X_4,
  input  Y_4,
  input  W_4,
  input  Z_4,
  input  X_5,
  input  Y_5,
  input  W_5,
  input  Z_5,
  output S,
  output S_2,
  output S_3,
  output S_4,
  output S_5
);

  wire NOT_2_out, NOT_3_out, NOT_4_out, NOT_5_out, NOT_6_out, NOT_7_out, NOT_8_out, NOT_9_out, NOT_10_out,
       NOT_11_out, NOT_12_out, NOT_13_out, NOT_14_out, NOT_15_out, NOT_16_out, NOT_17_out, NOT_18_out,
       NOT_19_out, NOT_20_out, NOT_21_out, NOT_22_out, NOT_23_out, NOT_24_out, NOT_25_out, NOT_26_out,
       NOT_27_out, NOT_28_out, NOT_29_out, NOT_30_out, NOT_31_out, NOT_32_out, NOT_33_out, NOT_34_out,
       NOT_35_out, NOT_36_out, NOT_37_out, NOT_38_out, NOT_39_out, NOT_out, OR_2_out, OR_3_out, OR_4_out,
       OR_5_out, OR_6_out, OR_7_out, OR_8_out, OR_9_out, OR_10_out, OR_11_out, OR_12_out, OR_13_out,
       OR_14_out, OR_15_out, OR_16_out, OR_17_out, OR_18_out, OR_19_out, OR_20_out, OR_21_out, OR_22_out,
       OR_out;

  not NOT (NOT_out, Y);
  not NOT_2 (NOT_2_out, Z);
  not NOT_3 (NOT_3_out, Y);
  not NOT_4 (NOT_4_out, Z);
  not NOT_5 (NOT_5_out, Y_2);
  not NOT_6 (NOT_6_out, X_2);
  not NOT_7 (NOT_7_out, X_2);
  not NOT_8 (NOT_8_out, X_2);
  not NOT_9 (NOT_9_out, Y_3);
  not NOT_10 (NOT_10_out, X_3);
  not NOT_11 (NOT_11_out, X_3);
  not NOT_12 (NOT_12_out, X_3);
  not NOT_13 (NOT_13_out, Y_3);
  not NOT_14 (NOT_14_out, Z_3);
  not NOT_15 (NOT_15_out, Z_4);
  not NOT_16 (NOT_16_out, Y_4);
  not NOT_17 (NOT_17_out, Z_4);
  not NOT_18 (NOT_18_out, Y_4);
  not NOT_19 (NOT_19_out, Z_4);
  not NOT_20 (NOT_20_out, Y_4);
  not NOT_21 (NOT_21_out, W_4);
  not NOT_22 (NOT_22_out, Z_4);
  not NOT_23 (NOT_23_out, X_4);
  not NOT_24 (NOT_24_out, Y_4);
  not NOT_25 (NOT_25_out, Z_4);
  not NOT_26 (NOT_26_out, Y_5);
  not NOT_27 (NOT_27_out, Y_5);
  not NOT_28 (NOT_28_out, Y_5);
  not NOT_29 (NOT_29_out, Z_5);
  not NOT_30 (NOT_30_out, Y_5);
  not NOT_31 (NOT_31_out, W_5);
  not NOT_32 (NOT_32_out, Y_5);
  not NOT_33 (NOT_33_out, W_5);
  not NOT_34 (NOT_34_out, Y_5);
  not NOT_35 (NOT_35_out, W_5);
  not NOT_36 (NOT_36_out, Z_5);
  not NOT_37 (NOT_37_out, X_5);
  not NOT_38 (NOT_38_out, Y_5);
  not NOT_39 (NOT_39_out, W_5);
  or OR (OR_out, X, NOT_out, NOT_2_out);
  or OR_2 (OR_2_out, NOT_3_out, W, NOT_4_out);
  or OR_3 (OR_3_out, NOT_5_out, W_2, Z_2);
  or OR_4 (OR_4_out, NOT_6_out, Y_2, W_2);
  or OR_5 (OR_5_out, NOT_7_out, Y_2, Z_2);
  or OR_6 (OR_6_out, NOT_8_out, W_2, Z_2);
  or OR_7 (OR_7_out, NOT_9_out, W_3, Z_3);
  or OR_8 (OR_8_out, NOT_10_out, W_3, Z_3);
  or OR_9 (OR_9_out, NOT_11_out, Y_3, W_3);
  or OR_10 (OR_10_out, NOT_12_out, NOT_13_out, NOT_14_out);
  or OR_11 (OR_11_out, X_4, W_4, NOT_15_out);
  or OR_12 (OR_12_out, X_4, NOT_16_out, NOT_17_out);
  or OR_13 (OR_13_out, NOT_18_out, W_4, NOT_19_out);
  or OR_14 (OR_14_out, NOT_20_out, NOT_21_out, NOT_22_out);
  or OR_15 (OR_15_out, NOT_23_out, NOT_24_out, NOT_25_out);
  or OR_16 (OR_16_out, X_5, NOT_26_out, W_5);
  or OR_17 (OR_17_out, X_5, NOT_27_out, Z_5);
  or OR_18 (OR_18_out, X_5, NOT_28_out, NOT_29_out);
  or OR_19 (OR_19_out, X_5, NOT_30_out, NOT_31_out);
  or OR_20 (OR_20_out, NOT_32_out, NOT_33_out, Z_5);
  or OR_21 (OR_21_out, NOT_34_out, NOT_35_out, NOT_36_out);
  or OR_22 (OR_22_out, NOT_37_out, NOT_38_out, NOT_39_out);
  and AND (S, OR_out, OR_2_out);
  and AND_2 (S_2, OR_3_out, OR_4_out, OR_5_out, OR_6_out);
  and AND_3 (S_3, OR_7_out, OR_8_out, OR_9_out, OR_10_out);
  and AND_4 (S_4, OR_11_out, OR_12_out, OR_13_out, OR_14_out, OR_15_out);
  and AND_5 (S_5, OR_16_out, OR_17_out, OR_18_out, OR_19_out, OR_20_out, OR_21_out, OR_22_out);

  // Notes on the sheet:
  //   a.) (X + Y' + Z') . (Y' + W + Z')
  //   b.) (Y' + W + Z) . (X' + Y + W) . (X' + Y + Z) . (X' + W + Z)
  //   c.) (Y' + W + Z) . (X' + W + Z) . (X' + Y + W) . (X' + Y' + Z')
  //   d.) (X + W + Z') . (X + Y' + Z') . (Y' + W + Z') . (Y' + W' + Z') . (X' + Y' + Z')
  //   e.) (X + Y' + W) . (X + Y' + Z) . (X + Y' + Z') . (X + Y' + W') . (Y' + W' + Z) . (Y' + W' + Z') . (X' + Y' + W')
endmodule

module Guia_0605 (
  input  X,
  input  Y,
  input  Z,
  output S,
  output S_2
);

  wire AND_2_out, AND_3_out, and_4_out, and_5_out, and_6_out, AND_out, NOT_2_out, NOT_3_out, NOT_4_out,
       NOT_5_out, not_6_out, not_7_out, not_8_out, NOT_9_out, NOT_out, OR_2_out, OR_out;

  not NOT (NOT_out, Y);
  not NOT_2 (NOT_2_out, Y);
  and AND (AND_out, Z, Y);
  not NOT_3 (NOT_3_out, X);
  or OR (OR_out, NOT_out, NOT_2_out);
  not NOT_4 (NOT_4_out, OR_out);
  and AND_2 (AND_2_out, Y, X);
  not NOT_5 (NOT_5_out, AND_2_out);
  or OR_2 (OR_2_out, AND_out, NOT_3_out);
  not not_6 (not_6_out, X);
  not not_7 (not_7_out, Y);
  not not_8 (not_8_out, Z);
  and AND_3 (AND_3_out, NOT_4_out, NOT_5_out);
  not NOT_9 (NOT_9_out, OR_2_out);
  and and_4 (and_4_out, not_6_out, Y);
  and and_5 (and_5_out, X, not_7_out);
  or or_3 (S_2, and_4_out, and_5_out, and_6_out);
  and and_6 (and_6_out, X, not_8_out);
  or OR_4 (S, AND_3_out, NOT_9_out);

  // Notes on the sheet:
  //   (x' . y) + (x . y') + (x . z')
endmodule

module Guia_0606 (
  input  X,
  input  Y,
  input  W,
  input  Z,
  output S,
  output S_2
);

  wire AND_2_out, AND_4_out, AND_out, NOT_2_out, NOT_3_out, NOT_4_out, not_5_out, not_6_out, not_7_out,
       NOT_8_out, NOT_9_out, NOT_10_out, NOT_out, OR_2_out, or_3_out, OR_out;

  not NOT (NOT_out, Y);
  not NOT_2 (NOT_2_out, X);
  not NOT_3 (NOT_3_out, W);
  and AND (AND_out, Z, W, Y);
  not NOT_4 (NOT_4_out, X);
  or OR (OR_out, NOT_out, W, NOT_2_out);
  and AND_2 (AND_2_out, Y, NOT_3_out, X);
  or OR_2 (OR_2_out, AND_out, NOT_4_out);
  not not_5 (not_5_out, Y);
  not not_6 (not_6_out, W);
  not not_7 (not_7_out, Z);
  not NOT_8 (NOT_8_out, OR_out);
  not NOT_9 (NOT_9_out, AND_2_out);
  not NOT_10 (NOT_10_out, OR_2_out);
  or or_3 (or_3_out, not_5_out, not_6_out, not_7_out);
  and and_3 (S_2, X, or_3_out);
  and AND_4 (AND_4_out, NOT_8_out, NOT_9_out);
  or OR_4 (S, AND_4_out, NOT_10_out);

  // Notes on the sheet:
  //   X(Y' + W' + Z')
endmodule
