// Logisim project GUIA0600.circ as structural Verilog: 7 circuits, main circuit main
module main (
  input  x,
  input  y,
  input  z,
  input  x_2,
  input  y_2,
  input  z_2,
  input  x_3,
  input  y_3,
  input  z_3,
  input  x_4,
  input  y_4,
  input  z_4,
  input  x_5,
  input  y_5,
  input  z_5,
  output out_16,
  output out_17,
  output out_18,
  output out_19,
  output out_20
);

  wire and_2_out, and_3_out, and_4_out, and_5_out, and_6_out, and_7_out, and_8_out, and_9_out, and_10_out,
       and_11_out, and_12_out, and_out, not_1_out, not_2_out, not_3_out, not_4_out, not_5_out, not_6_out,
       not_7_out, not_8_out, not_9_out, not_10_out, not_11_out;

  not not_1 (not_1_out, y);
  not not_2 (not_2_out, x_2);
  not not_3 (not_3_out, z_2);
  not not_4 (not_4_out, z_3);
  not not_5 (not_5_out, z_3);
  not not_6 (not_6_out, x_4);
  not not_7 (not_7_out, z_4);
  not not_8 (not_8_out, x_4);
  not not_9 (not_9_out, z_5);
  not not_10 (not_10_out, x_5);
  not not_11 (not_11_out, z_5);
  and \and  (and_out, z, z);
  and and_2 (and_2_out, not_1_out, z);
  and and_3 (and_3_out, not_2_out, y_2, y_2);
  and and_4 (and_4_out, y_2, not_3_out);
  and and_5 (and_5_out, y_3, not_4_out);
  and and_6 (and_6_out, x_3, not_5_out);
  and and_7 (and_7_out, y_3, x_3);
  and and_8 (and_8_out, not_6_out, y_4);
  and and_9 (and_9_out, y_4, y_4, not_7_out);
  and and_10 (and_10_out, not_8_out, not_8_out, x_4);
  and and_11 (and_11_out, not_9_out, not_9_out, not_9_out, not_10_out);
  and and_12 (and_12_out, x_5, x_5, not_11_out);
  or \or  (out_16, and_out, and_2_out);
  or or_2 (out_17, and_3_out, and_4_out);
  or or_3 (out_18, and_5_out, and_6_out, and_7_out);
  or or_4 (out_19, and_8_out, and_9_out, and_10_out);
  or or_5 (out_20, and_11_out, and_12_out);
endmodule

module QUEST01 (
  input  x,
  input  y,
  input  z,
  input  x_2,
  input  y_2,
  input  z_2,
  input  x_3,
  input  y_3,
  input  z_3,
  input  x_4,
  input  y_4,
  input  z_4,
  input  x_5,
  input  y_5,
  input  z_5,
  output out_16,
  output out_17,
  output out_18,
  output out_19,
  output out_20
);

  wire and_2_out, and_3_out, and_4_out, and_5_out, and_6_out, and_7_out, and_8_out, and_9_out, and_10_out,
       and_11_out, and_12_out, and_out, not_1_out, not_2_out, not_3_out, not_4_out, not_5_out, not_6_out,
       not_7_out, not_8_out, not_9_out, not_10_out, not_11_out;

  not not_1 (not_1_out, y);
  not not_2 (not_2_out, x_2);
  not not_3 (not_3_out, z_2);
  not not_4 (not_4_out, z_3);
  not not_5 (not_5_out, z_3);
  not not_6 (not_6_out, x_4);
  not not_7 (not_7_out, z_4);
  not not_8 (not_8_out, x_4);
  not not_9 (not_9_out, z_5);
  not not_10 (not_10_out, x_5);
  not not_11 (not_11_out, z_5);
  and \and  (and_out, x, z);
  and and_2 (and_2_out, not_1_out, z);
  and and_3 (and_3_out, not_2_out, y_2, y_2);
  and and_4 (and_4_out, y_2, not_3_out);
  and and_5 (and_5_out, y_3, not_4_out);
  and and_6 (and_6_out, x_3, not_5_out);
  and and_7 (and_7_out, y_3, x_3);
  and and_8 (and_8_out, not_6_out, y_4);
  and and_9 (and_9_out, y_4, y_4, not_7_out);
  and and_10 (and_10_out, not_8_out, not_8_out, x_4);
  and and_11 (and_11_out, not_9_out, not_9_out, not_10_out);
  and and_12 (and_12_out, x_5, x_5, not_11_out);
  or \or  (out_16, and_out, and_2_out);
  or or_2 (out_17, and_3_out, and_4_out);
  or or_3 (out_18, and_5_out, and_6_out, and_7_out);
  or or_4 (out_19, and_8_out, and_9_out, and_10_out);
  or or_5 (out_20, and_11_out, and_12_out);
endmodule

module QUEST02 (
  input  x,
  input  y,
  input  z,
  input  x_2,
  input  y_2,
  input  z_2,
  input  x_3,
  input  y_3,
  input  z_3,
  input  x_4,
  input  y_4,
  input  z_4,
  input  x_5,
  input  y_5,
  input  z_5,
  output out_16,
  output out_17,
  output out_18,
  output out_19,
  output out_20
);

  wire not_1_out, not_2_out, not_3_out, not_4_out, not_5_out, not_6_out, not_7_out, not_8_out, not_9_out,
       not_10_out, not_11_out, not_12_out, not_13_out, or_2_out, or_3_out, or_4_out, or_5_out, or_6_out,
       or_8_out, or_9_out, or_10_out, or_11_out, or_out;

  not not_1 (not_1_out, x);
  not not_2 (not_2_out, x);
  not not_3 (not_3_out, y);
  not not_4 (not_4_out, z_2);
  not not_5 (not_5_out, x_2);
  not not_6 (not_6_out, z_2);
  not not_7 (not_7_out, y_3);
  not not_8 (not_8_out, z_3);
  not not_9 (not_9_out, z_3);
  not not_10 (not_10_out, y_4);
  not not_11 (not_11_out, y_5);
  not not_12 (not_12_out, y_5);
  not not_13 (not_13_out, x_5);
  or \or  (or_out, not_1_out, z);
  or or_2 (or_2_out, not_2_out, not_3_out);
  or or_3 (or_3_out, not_4_out, y_2);
  or or_4 (or_4_out, not_5_out, not_6_out);
  or or_5 (or_5_out, not_7_out, x_3);
  or or_6 (or_6_out, not_8_out, y_3);
  or or_7 (or_6_out, x_3, not_9_out);
  or or_8 (or_8_out, y_4, z_4);
  or or_9 (or_9_out, not_10_out, z_4);
  or or_10 (or_10_out, not_11_out, z_5);
  or or_11 (or_11_out, not_12_out, not_13_out);
  and \and  (out_16, or_out, or_2_out);
  and and_2 (out_17, or_3_out, or_4_out);
  and and_3 (out_18, or_5_out, or_6_out);
  and and_4 (out_19, or_8_out, or_9_out);
  and and_5 (out_20, or_10_out, or_11_out);
endmodule

module QUEST03 (
  input  x,
  input  y,
  input  w,
  input  z,
  input  x_2,
  input  y_2,
  input  w_2,
  input  z_2,
  input  x_3,
  input  y_3,
  input  w_3,
  input  z_3,
  output out_13,
  output out_14,
  output out_15
);

  wire and_2_out, and_3_out, and_4_out, and_5_out, and_6_out, and_7_out, and_8_out, and_9_out, and_10_out,
       and_11_out, and_12_out, and_13_out, and_out, not_1_out, not_2_out, not_3_out, not_4_out, not_5_out,
       not_6_out, not_7_out, not_8_out, not_9_out, not_10_out, not_11_out, not_12_out, not_13_out,
       not_14_out, not_15_out, not_16_out, not_17_out, not_18_out, not_19_out, not_20_out, not_21_out,
       not_22_out, not_23_out, not_24_out, not_25_out, not_26_out;

  not not_1 (not_1_out, y);
  not not_2 (not_2_out, x);
  not not_3 (not_3_out, y);
  not not_4 (not_4_out, z);
  not not_5 (not_5_out, x);
  not not_6 (not_6_out, z);
  not not_7 (not_7_out, w_2);
  not not_8 (not_8_out, x_2);
  not not_9 (not_9_out, y_2);
  not not_10 (not_10_out, z_2);
  not not_11 (not_11_out, y_2);
  not not_12 (not_12_out, w_2);
  not not_13 (not_13_out, x_2);
  not not_14 (not_14_out, y_2);
  not not_15 (not_15_out, x_3);
  not not_16 (not_16_out, y_3);
  not not_17 (not_17_out, w_3);
  not not_18 (not_18_out, x_3);
  not not_19 (not_19_out, y_3);
  not not_20 (not_20_out, z_3);
  not not_21 (not_21_out, x_3);
  not not_22 (not_22_out, w_3);
  not not_23 (not_23_out, z_3);
  not not_24 (not_24_out, y_3);
  not not_25 (not_25_out, w_3);
  not not_26 (not_26_out, z_3);
  and \and  (and_out, x, not_1_out, w);
  and and_2 (and_2_out, not_2_out, y, w);
  and and_3 (and_3_out, not_3_out, w, not_4_out);
  and and_4 (and_4_out, not_5_out, w, not_6_out);
  and and_5 (and_5_out, y_2, not_7_out, not_7_out, z_2);
  and and_6 (and_6_out, not_8_out, not_9_out, not_10_out);
  and and_7 (and_7_out, x_2, not_11_out, not_12_out);
  and and_8 (and_8_out, not_13_out, not_14_out, w_2);
  and and_9 (and_9_out, not_15_out, not_16_out, not_16_out, not_17_out);
  and and_10 (and_10_out, not_18_out, not_19_out, not_20_out);
  and and_11 (and_11_out, not_21_out, not_21_out, not_22_out, not_23_out);
  and and_12 (and_12_out, not_24_out, not_25_out, not_26_out);
  and and_13 (and_13_out, y_3, y_3, w_3, w_3, z_3);
  or \or  (out_13, and_out, and_2_out, and_3_out, and_4_out);
  or or_2 (out_14, and_5_out, and_6_out, and_7_out, and_8_out);
  or or_3 (out_15, and_9_out, and_9_out, and_10_out, and_11_out, and_11_out, and_12_out, and_13_out);
endmodule

module QUEST4 (
  input  x,
  input  y,
  input  w,
  input  z,
  input  x_2,
  input  y_2,
  input  w_2,
  input  z_2,
  input  x_3,
  input  y_3,
  input  w_3,
  input  z_3,
  input  x_4,
  input  y_4,
  input  w_4,
  input  z_4,
  output out_17,
  output out_18,
  output out_19,
  output out_20
);

  wire not_1_out, not_2_out, not_3_out, not_4_out, not_5_out, not_6_out, not_7_out, not_8_out, not_9_out,
       not_10_out, not_11_out, not_12_out, not_13_out, not_14_out, not_15_out, not_16_out, not_17_out,
       not_18_out, not_19_out, not_20_out, not_21_out, not_22_out, not_23_out, not_24_out, not_25_out,
       or_2_out, or_3_out, or_4_out, or_5_out, or_6_out, or_7_out, or_8_out, or_9_out, or_10_out, or_11_out,
       or_12_out, or_13_out, or_14_out, or_15_out, or_out;

  not not_1 (not_1_out, x_2);
  not not_2 (not_2_out, x_2);
  not not_3 (not_3_out, x_2);
  not not_4 (not_4_out, y_2);
  not not_5 (not_5_out, y_3);
  not not_6 (not_6_out, y_3);
  not not_7 (not_7_out, x_3);
  not not_8 (not_8_out, z_3);
  not not_9 (not_9_out, y);
  not not_10 (not_10_out, z);
  not not_11 (not_11_out, y);
  not not_12 (not_12_out, z);
  not not_13 (not_13_out, x_3);
  not not_14 (not_14_out, x_3);
  not not_15 (not_15_out, y_3);
  not not_16 (not_16_out, y_4);
  not not_17 (not_17_out, z_4);
  not not_18 (not_18_out, y_4);
  not not_19 (not_19_out, z_4);
  not not_20 (not_20_out, y_4);
  not not_21 (not_21_out, w_4);
  not not_22 (not_22_out, z_4);
  not not_23 (not_23_out, x_4);
  not not_24 (not_24_out, y_4);
  not not_25 (not_25_out, z_4);
  or \or  (or_out, not_9_out, w, not_10_out);
  or or_2 (or_2_out, x, not_11_out, not_12_out);
  or or_3 (or_3_out, not_1_out, w_2, z_2);
  or or_4 (or_4_out, not_2_out, y_2, z_2);
  or or_5 (or_5_out, not_3_out, y_2, w_2);
  or or_6 (or_6_out, not_4_out, w_2, z_2);
  or or_7 (or_7_out, not_5_out, w_3, z_3);
  or or_8 (or_8_out, not_13_out, y_3, w_3);
  or or_9 (or_9_out, not_14_out, not_15_out, z_3);
  or or_10 (or_10_out, not_6_out, not_7_out, not_8_out);
  or or_11 (or_11_out, x_4, y_4, z_4);
  or or_12 (or_12_out, x_4, not_16_out, not_17_out);
  or or_13 (or_13_out, not_18_out, not_19_out, w_4);
  or or_14 (or_14_out, not_20_out, not_21_out, not_22_out);
  or or_15 (or_15_out, not_23_out, not_24_out, not_25_out);
  and \and  (out_17, or_out, or_2_out);
  and and_2 (out_18, or_3_out, or_4_out, or_5_out, or_6_out);
  and and_3 (out_19, or_7_out, or_8_out, or_9_out, or_10_out);
  and and_4 (out_20, or_11_out, or_11_out, or_12_out, or_13_out, or_14_out, or_15_out, or_15_out);
endmodule

module QUEST05 (
  input  x,
  input  y,
  input  z,
  output out_4
);

  wire and_1_out, and_2_out, not_1_out, not_2_out, not_3_out, not_4_out, not_5_out, not_6_out, or_2_out,
       or_3_out, or_out;

  not not_1 (not_1_out, x);
  not not_2 (not_2_out, y);
  or \or  (or_out, not_1_out, not_2_out);
  and and_1 (and_1_out, x, y);
  or or_2 (or_2_out, y, z);
  not not_3 (not_3_out, x);
  not not_4 (not_4_out, or_out);
  not not_5 (not_5_out, and_1_out);
  and and_2 (and_2_out, or_2_out, not_3_out);
  or or_3 (or_3_out, not_4_out, not_5_out);
  not not_6 (not_6_out, and_2_out);
  and and_3 (out_4, or_3_out, not_6_out);
endmodule

module QUEST06 (
  input  x,
  input  y,
  input  w,
  input  z,
  output out_5
);

  wire and_1_out, and_2_out, and_3_out, not_1_out, not_2_out, not_3_out, not_4_out, not_5_out, not_6_out,
       not_7_out, or_1_out, or_2_out;

  not not_1 (not_1_out, z);
  not not_2 (not_2_out, x);
  not not_3 (not_3_out, y);
  not not_4 (not_4_out, or_1_out);
  or or_1 (or_1_out, not_2_out, not_3_out, w);
  not not_5 (not_5_out, and_1_out);
  and and_1 (and_1_out, x, y, not_1_out);
  and and_2 (and_2_out, y, w, z);
  not not_6 (not_6_out, z);
  and and_3 (and_3_out, not_4_out, not_5_out);
  or or_2 (or_2_out, and_2_out, not_6_out);
  not not_7 (not_7_out, or_2_out);
  or or_3 (out_5, and_3_out, not_7_out);
endmodule
