// Logisim project Guia06-01a.circ as structural Verilog: 10 circuits, main circuit letra a
module letra_a (
  input  x,
  input  y,
  input  z,
  output out_4
);

  wire and_1_out, and_2_out, and_3_out, not_1_out, not_2_out, not_3_out;

  not not_1 (not_1_out, x);
  and and_1 (and_1_out, not_1_out, not_2_out, z);
  not not_2 (not_2_out, y);
  not not_3 (not_3_out, y);
  and and_2 (and_2_out, x, not_3_out, z);
  and and_3 (and_3_out, x, y, z);
  or or_1 (out_4, and_1_out, and_2_out, and_3_out);

  // Notes on the sheet:
  //   x
  //   y
  //   z
endmodule

module letra_b (
  input  x,
  input  y,
  input  z,
  output out_4
);

  wire and_1_out, and_2_out, and_3_out, not_1_out, not_2_out, not_3_out, not_4_out;

  not not_1 (not_1_out, x);
  and and_1 (and_1_out, not_1_out, y, not_2_out);
  not not_2 (not_2_out, z);
  not not_3 (not_3_out, x);
  and and_2 (and_2_out, not_3_out, y, z);
  and and_3 (and_3_out, x, y, not_4_out);
  not not_4 (not_4_out, z);
  or or_1 (out_4, and_1_out, and_2_out, and_3_out);
endmodule

module letra_c (
  input  x,
  input  y,
  input  z,
  output out_4
);

  wire and_1_out, and_2_out, and_3_out, and_4_out, not_1_out, not_2_out, not_3_out, not_4_out, not_5_out;

  not not_1 (not_1_out, x);
  and and_1 (and_1_out, not_1_out, y, not_2_out);
  not not_2 (not_2_out, z);
  not not_3 (not_3_out, y);
  and and_2 (and_2_out, x, not_3_out, not_4_out);
  not not_4 (not_4_out, z);
  and and_3 (and_3_out, x, y, not_5_out);
  not not_5 (not_5_out, z);
  and and_4 (and_4_out, x, y, z);
  or or_1 (out_4, and_1_out, and_2_out, and_3_out, and_4_out);
endmodule

module letra_d (
  input  x,
  input  y,
  input  z,
  output out_4
);

  wire and_1_out, and_2_out, and_3_out, and_4_out, not_1_out, not_2_out, not_3_out, not_4_out, not_5_out,
       not_6_out;

  not not_1 (not_1_out, x);
  and and_1 (and_1_out, not_1_out, not_2_out, z);
  not not_2 (not_2_out, y);
  not not_3 (not_3_out, x);
  and and_2 (and_2_out, not_3_out, y, not_4_out);
  not not_4 (not_4_out, z);
  not not_5 (not_5_out, x);
  and and_3 (and_3_out, not_5_out, y, z);
  and and_4 (and_4_out, x, y, not_6_out);
  not not_6 (not_6_out, z);
  or or_1 (out_4, and_1_out, and_2_out, and_3_out, and_4_out);
endmodule

module letra_e (
  input  x,
  input  y,
  input  z,
  output out_4
);

  wire and_1_out, and_2_out, and_3_out, and_4_out, not_1_out, not_2_out, not_3_out, not_4_out, not_5_out,
       not_6_out;

  not not_1 (not_1_out, x);
  and and_1 (and_1_out, not_1_out, not_2_out, not_3_out);
  not not_2 (not_2_out, y);
  not not_3 (not_3_out, z);
  not not_4 (not_4_out, x);
  and and_2 (and_2_out, not_4_out, y, not_5_out);
  not not_5 (not_5_out, z);
  and and_3 (and_3_out, x, not_6_out, z);
  not not_6 (not_6_out, y);
  and and_4 (and_4_out, x, y, z);
  or or_1 (out_4, and_1_out, and_2_out, and_3_out, and_4_out);
endmodule

module letra_e_simp (
  input  x,
  input  y,
  input  z,
  output u
);

  wire and_1_out, and_2_out, not_1_out, not_2_out;

  not not_1 (not_1_out, x);
  not not_2 (not_2_out, z);
  and and_1 (and_1_out, not_1_out, not_2_out);
  and and_2 (and_2_out, x, z);
  or or_1 (u, and_1_out, and_2_out);
endmodule

module letra_d_simp (
  input  x,
  input  y,
  input  z,
  output u
);

  wire and_1_out, and_2_out, not_1_out, not_2_out;

  not not_1 (not_1_out, x);
  not not_2 (not_2_out, z);
  and and_1 (and_1_out, not_1_out, z);
  and and_2 (and_2_out, y, not_2_out);
  or or_1 (u, and_1_out, and_2_out);
endmodule

module letra_c_simp (
  input  x,
  input  y,
  input  z,
  output u
);

  wire and_1_out, and_2_out, and_3_out, not_1_out, not_2_out;

  not not_1 (not_1_out, z);
  not not_2 (not_2_out, z);
  and and_1 (and_1_out, y, not_1_out);
  and and_2 (and_2_out, x, not_2_out);
  and and_3 (and_3_out, x, y);
  or or_1 (u, and_1_out, and_2_out, and_3_out);
endmodule

module letra_b_simp (
  input  x,
  input  y,
  input  z,
  output u
);

  wire and_1_out, and_2_out, not_1_out, not_2_out;

  not not_1 (not_1_out, x);
  not not_2 (not_2_out, z);
  and and_1 (and_1_out, not_1_out, y);
  and and_2 (and_2_out, y, not_2_out);
  or or_1 (u, and_1_out, and_2_out);
endmodule

module letra_a_simp (
  input  x,
  input  y,
  input  z,
  output u
);

  wire and_1_out, and_2_out, not_1_out;

  not not_1 (not_1_out, y);
  and and_1 (and_1_out, not_1_out, z);
  and and_2 (and_2_out, x, z);
  or or_1 (u, and_1_out, and_2_out);
endmodule
