// Logisim project Guia06-02.circ as structural Verilog: 10 circuits, main circuit letra a
module letra_a (
  input  x,
  input  y,
  input  z,
  output out_4
);

  wire not_1_out, not_2_out, not_3_out, not_4_out, not_5_out, not_6_out, or_1_out, or_2_out, or_3_out;

  not not_1 (not_1_out, x);
  or or_1 (or_1_out, not_1_out, y, z);
  not not_2 (not_2_out, x);
  or or_2 (or_2_out, not_2_out, not_3_out, z);
  not not_3 (not_3_out, y);
  not not_4 (not_4_out, x);
  or or_3 (or_3_out, not_4_out, not_5_out, not_6_out);
  not not_5 (not_5_out, y);
  not not_6 (not_6_out, z);
  and and_1 (out_4, or_1_out, or_2_out, or_3_out);
endmodule

module letra_a_simp (
  input  x,
  input  y,
  input  z,
  output u
);

  wire not_1_out, not_2_out, not_3_out, or_1_out, or_2_out;

  not not_1 (not_1_out, x);
  not not_2 (not_2_out, x);
  not not_3 (not_3_out, y);
  or or_1 (or_1_out, not_1_out, z);
  or or_2 (or_2_out, not_2_out, not_3_out);
  and and_1 (u, or_1_out, or_2_out);
endmodule

module letra_b (
  input  x,
  input  y,
  input  z,
  output out_4
);

  wire not_1_out, not_2_out, not_3_out, not_4_out, not_5_out, not_6_out, or_1_out, or_2_out, or_3_out;

  or or_1 (or_1_out, x, y, not_1_out);
  not not_1 (not_1_out, z);
  not not_2 (not_2_out, x);
  or or_2 (or_2_out, not_2_out, y, not_3_out);
  not not_3 (not_3_out, z);
  not not_4 (not_4_out, x);
  or or_3 (or_3_out, not_4_out, not_5_out, not_6_out);
  not not_5 (not_5_out, y);
  not not_6 (not_6_out, z);
  and and_1 (out_4, or_1_out, or_2_out, or_3_out);
endmodule

module letra_b_simp (
  input  x,
  input  y,
  input  z,
  output u
);

  wire not_1_out, not_2_out, not_3_out, or_1_out, or_2_out;

  not not_1 (not_1_out, z);
  not not_2 (not_2_out, x);
  not not_3 (not_3_out, z);
  or or_1 (or_1_out, y, not_1_out);
  or or_2 (or_2_out, not_2_out, not_3_out);
  and and_1 (u, or_1_out, or_2_out);
endmodule

module letra_c (
  input  x,
  input  y,
  input  z,
  output out_4
);

  wire not_1_out, not_2_out, not_3_out, not_4_out, not_5_out, not_6_out, or_1_out, or_2_out, or_3_out,
       or_4_out;

  or or_1 (or_1_out, x, y, not_1_out);
  not not_1 (not_1_out, z);
  not not_2 (not_2_out, y);
  or or_2 (or_2_out, x, not_2_out, z);
  or or_3 (or_3_out, x, not_3_out, not_4_out);
  not not_3 (not_3_out, y);
  not not_4 (not_4_out, z);
  not not_5 (not_5_out, x);
  or or_4 (or_4_out, not_5_out, y, not_6_out);
  not not_6 (not_6_out, z);
  and and_1 (out_4, or_1_out, or_2_out, or_3_out, or_4_out);
endmodule

module letra_c_simp (
  input  x,
  input  y,
  input  z,
  output u
);

  wire not_1_out, not_2_out, or_1_out, or_2_out;

  not not_1 (not_1_out, z);
  not not_2 (not_2_out, y);
  or or_1 (or_1_out, y, not_1_out);
  or or_2 (or_2_out, x, not_2_out);
  and and_1 (u, or_1_out, or_2_out);
endmodule

module letra_d (
  input  x,
  input  y,
  input  z,
  output out_4
);

  wire not_1_out, not_2_out, not_3_out, not_4_out, not_5_out, not_6_out, or_1_out, or_2_out, or_3_out,
       or_4_out;

  or or_1 (or_1_out, x, y, z);
  or or_2 (or_2_out, x, not_1_out, not_2_out);
  not not_1 (not_1_out, y);
  not not_2 (not_2_out, z);
  not not_3 (not_3_out, x);
  or or_3 (or_3_out, not_3_out, y, z);
  not not_4 (not_4_out, x);
  or or_4 (or_4_out, not_4_out, not_5_out, not_6_out);
  not not_5 (not_5_out, y);
  not not_6 (not_6_out, z);
  and and_1 (out_4, or_1_out, or_2_out, or_3_out, or_4_out);
endmodule

module letra_d_simp (
  input  x,
  input  y,
  input  z,
  output u
);

  wire not_1_out, not_2_out, or_1_out, or_2_out;

  not not_1 (not_1_out, y);
  not not_2 (not_2_out, z);
  or or_1 (or_1_out, y, z);
  or or_2 (or_2_out, not_1_out, not_2_out);
  and and_1 (u, or_1_out, or_2_out);
endmodule

module letra_e (
  input  x,
  input  y,
  input  z,
  output out_4
);

  wire not_1_out, not_2_out, not_3_out, not_4_out, not_5_out, not_6_out, not_7_out, or_1_out, or_2_out,
       or_3_out, or_4_out;

  or or_1 (or_1_out, x, y, not_1_out);
  not not_1 (not_1_out, z);
  or or_2 (or_2_out, x, not_2_out, z);
  not not_2 (not_2_out, y);
  not not_3 (not_3_out, x);
  or or_3 (or_3_out, not_3_out, not_4_out, z);
  not not_4 (not_4_out, y);
  not not_5 (not_5_out, x);
  not not_6 (not_6_out, y);
  or or_4 (or_4_out, not_5_out, not_6_out, not_7_out);
  not not_7 (not_7_out, z);
  and and_1 (out_4, or_1_out, or_2_out, or_3_out, or_4_out);
endmodule

module letra_e_simp (
  input  x,
  input  y,
  input  z,
  output u
);

  wire not_1_out, not_2_out, not_3_out, not_4_out, or_1_out, or_2_out, or_3_out;

  not not_1 (not_1_out, z);
  not not_2 (not_2_out, y);
  not not_3 (not_3_out, x);
  not not_4 (not_4_out, y);
  or or_1 (or_1_out, x, y, not_1_out);
  or or_2 (or_2_out, not_2_out, z);
  or or_3 (or_3_out, not_3_out, not_4_out);
  and and_1 (u, or_1_out, or_2_out, or_3_out);
endmodule
