// Logisim project Guia06-03.circ as structural Verilog: 9 circuits, main circuit letra a
module letra_a (
  input  x,
  input  y,
  input  w,
  input  z,
  output out_5
);

  wire and_1_out, and_2_out, and_3_out, and_4_out, and_5_out, and_6_out, not_1_out, not_2_out, not_3_out,
       not_4_out, not_5_out, not_6_out, not_7_out, not_8_out, not_9_out, not_10_out, not_11_out, not_12_out;

  not not_1 (not_1_out, x);
  not not_2 (not_2_out, y);
  not not_3 (not_3_out, w);
  not not_4 (not_4_out, x);
  not not_5 (not_5_out, y);
  not not_6 (not_6_out, z);
  not not_7 (not_7_out, x);
  not not_8 (not_8_out, z);
  not not_9 (not_9_out, x);
  not not_10 (not_10_out, y);
  not not_11 (not_11_out, z);
  not not_12 (not_12_out, y);
  and and_1 (and_1_out, not_1_out, not_2_out, not_3_out, z);
  and and_2 (and_2_out, not_4_out, not_5_out, w, not_6_out);
  and and_3 (and_3_out, not_7_out, y, w, not_8_out);
  and and_4 (and_4_out, not_9_out, y, w, z);
  and and_5 (and_5_out, x, not_10_out, w, not_11_out);
  and and_6 (and_6_out, x, not_12_out, w, z);
  or or_1 (out_5, and_1_out, and_2_out, and_3_out, and_4_out, and_5_out, and_6_out);
endmodule

module letra_a_simp (
  input  x,
  input  y,
  input  w,
  input  z,
  output u
);

  wire and_1_out, and_2_out, and_3_out, and_4_out, not_1_out, not_2_out, not_3_out, not_4_out, not_5_out,
       not_6_out, not_7_out;

  not not_1 (not_1_out, x);
  not not_2 (not_2_out, y);
  not not_3 (not_3_out, w);
  not not_4 (not_4_out, x);
  not not_5 (not_5_out, z);
  not not_6 (not_6_out, x);
  not not_7 (not_7_out, y);
  and and_1 (and_1_out, not_1_out, not_2_out, not_3_out, z);
  and and_2 (and_2_out, not_4_out, w, not_5_out);
  and and_3 (and_3_out, not_6_out, y, w);
  and and_4 (and_4_out, x, not_7_out, w);
  or or_1 (u, and_1_out, and_2_out, and_3_out, and_4_out);
endmodule

module letra_b (
  input  x,
  input  y,
  input  w,
  input  z,
  output out_5
);

  wire and_1_out, and_2_out, and_3_out, and_4_out, and_5_out, and_6_out, and_7_out, not_1_out, not_2_out,
       not_3_out, not_4_out, not_5_out, not_6_out, not_7_out, not_8_out, not_9_out, not_10_out, not_11_out,
       not_12_out, not_13_out, not_14_out, not_15_out, not_16_out, not_17_out, not_18_out;

  not not_1 (not_1_out, x);
  not not_2 (not_2_out, y);
  not not_3 (not_3_out, w);
  not not_4 (not_4_out, z);
  not not_5 (not_5_out, x);
  not not_6 (not_6_out, y);
  not not_7 (not_7_out, z);
  not not_8 (not_8_out, x);
  not not_9 (not_9_out, y);
  not not_10 (not_10_out, x);
  not not_11 (not_11_out, w);
  not not_12 (not_12_out, y);
  not not_13 (not_13_out, w);
  not not_14 (not_14_out, z);
  not not_15 (not_15_out, y);
  not not_16 (not_16_out, w);
  not not_17 (not_17_out, y);
  not not_18 (not_18_out, w);
  and and_1 (and_1_out, not_1_out, not_2_out, not_3_out, not_4_out);
  and and_2 (and_2_out, not_5_out, not_6_out, w, not_7_out);
  and and_3 (and_3_out, not_8_out, not_9_out, w, z);
  and and_4 (and_4_out, not_10_out, y, not_11_out, z);
  and and_5 (and_5_out, x, not_12_out, not_13_out, not_14_out);
  and and_6 (and_6_out, x, not_15_out, not_16_out, z);
  and and_7 (and_7_out, x, not_17_out, not_18_out, z);
  or or_1 (out_5, and_1_out, and_2_out, and_3_out, and_4_out, and_5_out, and_6_out, and_7_out);
endmodule

module letra_b_simp (
  input  x,
  input  y,
  input  w,
  input  z,
  output u
);

  wire and_1_out, and_2_out, and_3_out, and_4_out, not_1_out, not_2_out, not_3_out, not_4_out, not_5_out,
       not_6_out, not_7_out, not_8_out, not_9_out;

  not not_1 (not_1_out, x);
  not not_2 (not_2_out, y);
  not not_3 (not_3_out, z);
  not not_4 (not_4_out, x);
  not not_5 (not_5_out, y);
  not not_6 (not_6_out, x);
  not not_7 (not_7_out, w);
  not not_8 (not_8_out, y);
  not not_9 (not_9_out, w);
  and and_1 (and_1_out, not_1_out, not_2_out, not_3_out);
  and and_2 (and_2_out, not_4_out, not_5_out, w);
  and and_3 (and_3_out, not_6_out, y, not_7_out, z);
  and and_4 (and_4_out, x, not_8_out, not_9_out);
  or or_1 (u, and_1_out, and_2_out, and_3_out, and_4_out);
endmodule

module letra_c (
  input  x,
  input  y,
  input  w,
  input  z,
  output out_5
);

  wire and_1_out, and_2_out, and_3_out, and_4_out, and_5_out, and_6_out, and_7_out, and_8_out, not_1_out,
       not_2_out, not_3_out, not_4_out, not_5_out, not_6_out, not_7_out, not_8_out, not_9_out, not_10_out,
       not_11_out, not_12_out, not_13_out, not_14_out, not_15_out, not_16_out, not_17_out, not_18_out;

  not not_1 (not_1_out, x);
  not not_2 (not_2_out, y);
  not not_3 (not_3_out, w);
  not not_4 (not_4_out, z);
  not not_5 (not_5_out, x);
  not not_6 (not_6_out, y);
  not not_7 (not_7_out, w);
  not not_8 (not_8_out, x);
  not not_9 (not_9_out, y);
  not not_10 (not_10_out, z);
  not not_11 (not_11_out, x);
  not not_12 (not_12_out, w);
  not not_13 (not_13_out, z);
  not not_14 (not_14_out, x);
  not not_15 (not_15_out, y);
  not not_16 (not_16_out, w);
  not not_17 (not_17_out, z);
  not not_18 (not_18_out, y);
  and and_1 (and_1_out, not_1_out, not_2_out, not_3_out, not_4_out);
  and and_2 (and_2_out, not_5_out, not_6_out, not_7_out, z);
  and and_3 (and_3_out, not_8_out, not_9_out, w, not_10_out);
  and and_4 (and_4_out, not_11_out, y, not_12_out, not_13_out);
  and and_5 (and_5_out, not_14_out, y, w, z);
  and and_6 (and_6_out, x, not_15_out, not_16_out, not_17_out);
  and and_7 (and_7_out, x, not_18_out, w, z);
  and and_8 (and_8_out, x, y, w, z);
  or or_1 (out_5, and_1_out, and_2_out, and_3_out, and_4_out, and_5_out, and_6_out, and_7_out, and_8_out);
endmodule

module letra_c_simp (
  input  x,
  input  y,
  input  w,
  input  z,
  output u
);

  wire and_1_out, and_2_out, and_3_out, and_4_out, and_5_out, and_6_out, not_1_out, not_2_out, not_3_out,
       not_4_out, not_5_out, not_6_out, not_7_out, not_8_out, not_9_out, not_10_out, not_11_out, not_12_out;

  not not_1 (not_1_out, x);
  and and_1 (and_1_out, not_1_out, not_2_out, not_3_out);
  not not_2 (not_2_out, y);
  not not_3 (not_3_out, w);
  not not_4 (not_4_out, x);
  and and_2 (and_2_out, not_4_out, not_5_out, not_6_out);
  not not_5 (not_5_out, y);
  not not_6 (not_6_out, z);
  not not_7 (not_7_out, x);
  and and_3 (and_3_out, not_7_out, not_8_out, not_9_out);
  not not_8 (not_8_out, w);
  not not_9 (not_9_out, z);
  not not_10 (not_10_out, y);
  not not_11 (not_11_out, w);
  and and_4 (and_4_out, not_10_out, not_11_out, not_12_out);
  not not_12 (not_12_out, z);
  and and_5 (and_5_out, y, w, z);
  and and_6 (and_6_out, x, w, z);
  or or_1 (u, and_1_out, and_2_out, and_3_out, and_4_out, and_5_out, and_6_out);
endmodule

module letra_d (
  input  x,
  input  y,
  input  w,
  input  z,
  output out_5
);

  wire and_1_out, and_2_out, and_3_out, and_4_out, and_5_out, and_6_out, and_7_out, not_1_out, not_2_out,
       not_3_out, not_4_out, not_5_out, not_6_out, not_7_out, not_8_out, not_9_out, not_10_out, not_11_out,
       not_12_out, not_13_out, not_14_out;

  not not_1 (not_1_out, x);
  not not_2 (not_2_out, y);
  not not_3 (not_3_out, z);
  not not_4 (not_4_out, x);
  not not_5 (not_5_out, w);
  not not_6 (not_6_out, z);
  not not_7 (not_7_out, x);
  not not_8 (not_8_out, w);
  not not_9 (not_9_out, x);
  not not_10 (not_10_out, y);
  not not_11 (not_11_out, z);
  not not_12 (not_12_out, w);
  not not_13 (not_13_out, z);
  not not_14 (not_14_out, z);
  and and_1 (and_1_out, not_1_out, not_2_out, w, not_3_out);
  and and_2 (and_2_out, not_4_out, y, not_5_out, not_6_out);
  and and_3 (and_3_out, not_7_out, y, not_8_out, z);
  and and_4 (and_4_out, not_9_out, y, w, z);
  and and_5 (and_5_out, x, not_10_out, w, not_11_out);
  and and_6 (and_6_out, x, y, not_12_out, not_13_out);
  and and_7 (and_7_out, x, y, w, not_14_out);
  or or_1 (out_5, and_1_out, and_2_out, and_3_out, and_4_out, and_5_out, and_6_out, and_7_out);
endmodule

module letra_d_simp (
  input  x,
  input  y,
  input  w,
  input  z,
  output u
);

  wire and_1_out, and_2_out, and_3_out, and_4_out, not_1_out, not_2_out, not_3_out, not_4_out, not_5_out,
       not_6_out;

  not not_1 (not_1_out, y);
  and and_1 (and_1_out, not_1_out, w, not_2_out);
  not not_2 (not_2_out, z);
  not not_3 (not_3_out, w);
  and and_2 (and_2_out, y, not_3_out, not_4_out);
  not not_4 (not_4_out, z);
  not not_5 (not_5_out, x);
  and and_3 (and_3_out, not_5_out, y, z);
  and and_4 (and_4_out, x, y, not_6_out);
  not not_6 (not_6_out, z);
  or or_1 (u, and_1_out, and_2_out, and_3_out, and_4_out);
endmodule

module letra_e (
  input  x,
  input  y,
  input  w,
  input  z,
  output out_5
);

  wire and_1_out, and_2_out, and_3_out, and_4_out, and_5_out, and_6_out, and_7_out, and_8_out, not_1_out,
       not_2_out, not_3_out, not_4_out, not_5_out, not_6_out, not_7_out, not_8_out, not_9_out, not_10_out,
       not_11_out, not_12_out, not_13_out, not_14_out, not_15_out, not_16_out, not_17_out, not_18_out,
       not_19_out, not_20_out;

  not not_1 (not_1_out, x);
  not not_2 (not_2_out, y);
  not not_3 (not_3_out, w);
  not not_4 (not_4_out, z);
  not not_5 (not_5_out, x);
  not not_6 (not_6_out, y);
  not not_7 (not_7_out, w);
  not not_8 (not_8_out, x);
  not not_9 (not_9_out, y);
  not not_10 (not_10_out, z);
  not not_11 (not_11_out, x);
  not not_12 (not_12_out, z);
  not not_13 (not_13_out, y);
  not not_14 (not_14_out, w);
  not not_15 (not_15_out, z);
  not not_16 (not_16_out, y);
  not not_17 (not_17_out, w);
  not not_18 (not_18_out, z);
  not not_19 (not_19_out, y);
  not not_20 (not_20_out, w);
  and and_1 (and_1_out, not_1_out, not_2_out, not_3_out, not_4_out);
  and and_2 (and_2_out, not_5_out, not_6_out, not_7_out, z);
  and and_3 (and_3_out, not_8_out, not_9_out, w, not_10_out);
  and and_4 (and_4_out, not_11_out, y, w, not_12_out);
  and and_5 (and_5_out, x, not_13_out, not_14_out, not_15_out);
  and and_6 (and_6_out, x, not_16_out, not_17_out, not_18_out);
  and and_7 (and_7_out, x, not_19_out, not_20_out, z);
  and and_8 (and_8_out, x, y, w, z);
  or or_1 (out_5, and_1_out, and_2_out, and_3_out, and_4_out, and_5_out, and_6_out, and_7_out, and_8_out);
endmodule
