// Logisim project Guia06-04.circ as structural Verilog: 10 circuits, main circuit letra a
module letra_a (
  input  x,
  input  y,
  input  w,
  input  z,
  output out_5
);

  wire not_1_out, not_2_out, not_3_out, not_4_out, not_5_out, not_6_out, not_7_out, or_1_out, or_2_out,
       or_3_out, or_4_out;

  or or_1 (or_1_out, x, y, not_1_out, z);
  not not_1 (not_1_out, w);
  not not_2 (not_2_out, y);
  or or_2 (or_2_out, x, not_2_out, w, not_3_out);
  not not_3 (not_3_out, z);
  not not_4 (not_4_out, y);
  or or_3 (or_3_out, x, not_4_out, not_5_out, not_6_out);
  not not_5 (not_5_out, w);
  not not_6 (not_6_out, z);
  not not_7 (not_7_out, x);
  or or_4 (or_4_out, not_7_out, y, w, z);
  and and_1 (out_5, or_1_out, or_2_out, or_3_out, or_4_out);
endmodule

module letra_a_simp (
  input  x,
  input  y,
  input  w,
  input  z,
  output u
);

  wire not_1_out, not_2_out, not_3_out, not_4_out, or_1_out, or_2_out, or_3_out;

  not not_1 (not_1_out, w);
  not not_2 (not_2_out, y);
  not not_3 (not_3_out, z);
  not not_4 (not_4_out, x);
  or or_1 (or_1_out, x, y, not_1_out, z);
  or or_2 (or_2_out, x, not_2_out, not_3_out);
  and and_1 (u, or_1_out, or_2_out, or_3_out);
  or or_3 (or_3_out, not_4_out, y, w, z);
endmodule

module letra_b (
  input  x,
  input  y,
  input  w,
  input  z,
  output out_5
);

  wire not_1_out, not_2_out, not_3_out, not_4_out, not_5_out, not_6_out, not_7_out, not_8_out, not_9_out,
       or_1_out, or_2_out, or_3_out, or_4_out, or_5_out;

  not not_1 (not_1_out, y);
  or or_1 (or_1_out, x, not_1_out, w, z);
  not not_2 (not_2_out, x);
  or or_2 (or_2_out, not_2_out, y, w, z);
  not not_3 (not_3_out, x);
  or or_3 (or_3_out, not_3_out, y, w, not_4_out);
  not not_4 (not_4_out, z);
  not not_5 (not_5_out, x);
  or or_4 (or_4_out, not_5_out, y, not_6_out, not_7_out);
  not not_6 (not_6_out, w);
  not not_7 (not_7_out, z);
  not not_8 (not_8_out, x);
  not not_9 (not_9_out, y);
  or or_5 (or_5_out, not_8_out, not_9_out, w, z);
  and and_1 (out_5, or_1_out, or_2_out, or_3_out, or_4_out, or_5_out);
endmodule

module letra_b_simp (
  input  x,
  input  y,
  input  w,
  input  z,
  output u
);

  wire not_1_out, not_2_out, not_3_out, not_4_out, or_1_out, or_2_out, or_3_out;

  not not_1 (not_1_out, y);
  or or_1 (or_1_out, not_1_out, w, z);
  not not_2 (not_2_out, x);
  or or_2 (or_2_out, not_2_out, y, w);
  not not_3 (not_3_out, x);
  or or_3 (or_3_out, not_3_out, y, not_4_out);
  not not_4 (not_4_out, z);
  and and_1 (u, or_1_out, or_2_out, or_3_out);
endmodule

module letra_c (
  input  x,
  input  y,
  input  w,
  input  z,
  output out_5
);

  wire not_1_out, not_2_out, not_3_out, not_4_out, not_5_out, not_6_out, not_7_out, not_8_out, not_9_out,
       not_10_out, not_11_out, or_1_out, or_2_out, or_3_out, or_4_out, or_5_out;

  not not_1 (not_1_out, y);
  or or_1 (or_1_out, x, not_1_out, w, z);
  not not_2 (not_2_out, x);
  or or_2 (or_2_out, not_2_out, y, w, z);
  not not_3 (not_3_out, x);
  not not_4 (not_4_out, y);
  or or_3 (or_3_out, not_3_out, not_4_out, w, z);
  not not_5 (not_5_out, x);
  not not_6 (not_6_out, y);
  or or_4 (or_4_out, not_5_out, not_6_out, w, not_7_out);
  not not_7 (not_7_out, z);
  not not_8 (not_8_out, x);
  not not_9 (not_9_out, y);
  or or_5 (or_5_out, not_8_out, not_9_out, not_10_out, not_11_out);
  not not_10 (not_10_out, w);
  not not_11 (not_11_out, z);
  and and_1 (out_5, or_1_out, or_2_out, or_3_out, or_4_out, or_5_out);
endmodule

module letra_c_simp (
  input  x,
  input  y,
  input  w,
  input  z,
  output u
);

  wire not_1_out, not_2_out, not_3_out, not_4_out, not_5_out, or_1_out, or_2_out, or_3_out;

  not not_1 (not_1_out, y);
  or or_1 (or_1_out, not_1_out, w, z);
  not not_2 (not_2_out, x);
  or or_2 (or_2_out, not_2_out, w, z);
  not not_3 (not_3_out, x);
  not not_4 (not_4_out, y);
  or or_3 (or_3_out, not_3_out, not_4_out, not_5_out);
  not not_5 (not_5_out, z);
  and and_1 (u, or_1_out, or_2_out, or_3_out);
endmodule

module letra_d (
  input  x,
  input  y,
  input  w,
  input  z,
  output out_5
);

  wire not_1_out, not_2_out, not_3_out, not_4_out, not_5_out, not_6_out, not_7_out, not_8_out, not_9_out,
       not_10_out, not_11_out, not_12_out, not_13_out, not_14_out, or_1_out, or_2_out, or_3_out, or_4_out,
       or_5_out, or_6_out;

  or or_1 (or_1_out, x, y, w, not_1_out);
  not not_1 (not_1_out, z);
  or or_2 (or_2_out, x, y, not_2_out, z);
  not not_2 (not_2_out, w);
  not not_3 (not_3_out, y);
  or or_3 (or_3_out, x, not_3_out, w, not_4_out);
  not not_4 (not_4_out, z);
  not not_5 (not_5_out, y);
  or or_4 (or_4_out, x, not_5_out, not_6_out, not_7_out);
  not not_6 (not_6_out, w);
  not not_7 (not_7_out, z);
  not not_8 (not_8_out, x);
  not not_9 (not_9_out, y);
  or or_5 (or_5_out, not_8_out, not_9_out, w, not_10_out);
  not not_10 (not_10_out, z);
  not not_11 (not_11_out, x);
  not not_12 (not_12_out, y);
  or or_6 (or_6_out, not_11_out, not_12_out, not_13_out, not_14_out);
  not not_13 (not_13_out, w);
  not not_14 (not_14_out, z);
  and and_1 (out_5, or_1_out, or_2_out, or_3_out, or_4_out, or_5_out, or_6_out);
endmodule

module letra_d_simp (
  input  x,
  input  y,
  input  w,
  input  z,
  output u
);

  wire not_1_out, not_2_out, not_3_out, not_4_out, or_1_out, or_2_out, or_3_out;

  not not_1 (not_1_out, z);
  not not_2 (not_2_out, w);
  not not_3 (not_3_out, y);
  not not_4 (not_4_out, z);
  or or_1 (or_1_out, x, w, not_1_out);
  and and_1 (u, or_1_out, or_2_out, or_3_out);
  or or_2 (or_2_out, x, y, not_2_out, z);
  or or_3 (or_3_out, not_3_out, not_4_out);
endmodule

module letra_e (
  input  x,
  input  y,
  input  w,
  input  z,
  output out_5
);

  wire not_1_out, not_2_out, not_3_out, not_4_out, not_5_out, not_6_out, not_7_out, not_8_out, not_9_out,
       not_10_out, not_11_out, not_12_out, not_13_out, not_14_out, not_15_out, or_1_out, or_2_out, or_3_out,
       or_4_out, or_5_out, or_6_out;

  not not_1 (not_1_out, y);
  or or_1 (or_1_out, x, not_1_out, w, z);
  not not_2 (not_2_out, y);
  or or_2 (or_2_out, x, not_2_out, w, not_3_out);
  not not_3 (not_3_out, z);
  not not_4 (not_4_out, y);
  or or_3 (or_3_out, x, not_4_out, not_5_out, z);
  not not_5 (not_5_out, w);
  not not_6 (not_6_out, y);
  or or_4 (or_4_out, x, not_6_out, not_7_out, not_8_out);
  not not_7 (not_7_out, w);
  not not_8 (not_8_out, z);
  not not_9 (not_9_out, x);
  not not_10 (not_10_out, y);
  or or_5 (or_5_out, not_9_out, not_10_out, not_11_out, z);
  not not_11 (not_11_out, w);
  not not_12 (not_12_out, x);
  not not_13 (not_13_out, y);
  or or_6 (or_6_out, not_12_out, not_13_out, not_14_out, not_15_out);
  not not_14 (not_14_out, w);
  not not_15 (not_15_out, z);
  and and_1 (out_5, or_1_out, or_2_out, or_3_out, or_4_out, or_5_out, or_6_out);
endmodule

module letra_e_simp (
  input  x,
  input  y,
  input  w,
  input  z,
  output u
);

  wire not_1_out, not_2_out, not_3_out, or_1_out, or_2_out;

  or or_1 (or_1_out, x, not_1_out);
  not not_1 (not_1_out, y);
  not not_2 (not_2_out, y);
  or or_2 (or_2_out, not_2_out, not_3_out);
  not not_3 (not_3_out, w);
  and and_1 (u, or_1_out, or_2_out);
endmodule
