// Logisim project Guia06-06.circ as structural Verilog: 2 circuits, main circuit main
module main (
  input  in_1,
  input  in_2,
  input  in_3,
  input  in_4,
  output out_5
);

  wire and_1_out, and_2_out, and_3_out, not_1_out, not_2_out, not_3_out, not_4_out, not_5_out, not_6_out,
       not_7_out, or_1_out, or_2_out;

  not not_1 (not_1_out, in_2);
  not not_2 (not_2_out, in_1);
  not not_3 (not_3_out, in_3);
  or or_1 (or_1_out, not_1_out, in_3, not_2_out);
  and and_1 (and_1_out, in_2, not_3_out, in_1);
  and and_2 (and_2_out, in_4, in_3, in_2);
  or or_2 (or_2_out, and_2_out, not_4_out);
  not not_4 (not_4_out, in_1);
  not not_5 (not_5_out, or_1_out);
  and and_3 (and_3_out, not_5_out, not_6_out);
  not not_6 (not_6_out, and_1_out);
  or or_3 (out_5, and_3_out, not_7_out);
  not not_7 (not_7_out, or_2_out);
endmodule

module simplificado (
  input  a,
  input  b,
  input  c,
  input  d,
  output x
);

  wire not_1_out, not_2_out, not_3_out, or_1_out;

  not not_1 (not_1_out, b);
  not not_2 (not_2_out, c);
  or or_1 (or_1_out, not_1_out, not_2_out, not_3_out);
  not not_3 (not_3_out, d);
  and and_1 (x, a, or_1_out);
endmodule
