// Logisim project Exercicio01.circ as structural Verilog: 1 circuit, main circuit main
module main (
  input  y,
  input  x,
  input  z,
  input  y_2,
  input  x_2,
  input  z_2,
  input  z_3,
  input  z_4,
  input  x_3,
  input  y_3,
  input  x_4,
  input  y_4,
  input  y_5,
  input  x_5,
  input  z_5,
  input  y_6,
  input  x_6,
  input  y_7,
  input  z_6,
  output out_20,
  output out_21,
  output out_22,
  output out_23,
  output out_24
);

  wire AND_2_out, AND_3_out, AND_4_out, AND_5_out, AND_6_out, AND_7_out, AND_8_out, AND_9_out, AND_10_out,
       AND_11_out, AND_12_out, AND_out, not_1_out, not_2_out, not_3_out, not_4_out, not_5_out, not_6_out,
       not_7_out, not_8_out, OR_3_out, OR_5_out;

  not not_1 (not_1_out, y);
  and AND (AND_out, not_1_out, z);
  and AND_2 (AND_2_out, x_2, z_3);
  not not_2 (not_2_out, x_3);
  not not_3 (not_3_out, z_5);
  not not_4 (not_4_out, z_6);
  and AND_3 (AND_3_out, not_2_out, y_3);
  and AND_4 (AND_4_out, y_4, not_3_out);
  and AND_5 (AND_5_out, x_6, not_4_out);
  and AND_6 (AND_6_out, not_4_out, y_7);
  and AND_7 (AND_7_out, y_7, x_6);
  or OR (out_20, AND_out, AND_2_out);
  or OR_2 (out_22, AND_3_out, AND_4_out);
  or OR_3 (OR_3_out, AND_5_out, AND_6_out);
  or OR_4 (out_24, OR_3_out, AND_7_out);
  not not_5 (not_5_out, x);
  not not_6 (not_6_out, z_4);
  not not_7 (not_7_out, x_5);
  not not_8 (not_8_out, y_6);
  and AND_8 (AND_8_out, not_5_out, z_2);
  and AND_9 (AND_9_out, not_5_out, y_2);
  and AND_10 (AND_10_out, y_2, not_6_out);
  and AND_11 (AND_11_out, x_4, x_4, y_5);
  and AND_12 (AND_12_out, not_7_out, not_8_out);
  or OR_5 (OR_5_out, AND_8_out, AND_9_out);
  or OR_6 (out_23, AND_11_out, AND_12_out);
  or OR_7 (out_21, OR_5_out, AND_10_out);

  // Notes on the sheet:
  //   LETRA A
  //   LETRA C
  //   LETRA B
  //   LETRA D
  //   LETRA E
  //   Nome: Luisa Nogueira C. S. Souza
  //   Matricula:747560
endmodule
