// Logisim project Exercicio02.circ as structural Verilog: 1 circuit, main circuit main
module main (
  input  Y,
  input  Y_2,
  input  X,
  input  Z,
  input  Z_2,
  input  X_2,
  input  Z_3,
  input  X_3,
  input  Y_3,
  input  Y_4,
  input  Z_4,
  input  X_4,
  input  Y_5,
  input  Y_6,
  input  Z_5,
  output out_16,
  output out_17,
  output out_18,
  output out_19,
  output out_20
);

  wire AND_3_out, not_1_out, not_2_out, not_3_out, not_4_out, not_5_out, not_6_out, not_7_out, not_8_out,
       not_9_out, not_10_out, OR_2_out, OR_3_out, OR_4_out, OR_5_out, OR_6_out, OR_7_out, OR_8_out, OR_9_out,
       OR_10_out, OR_11_out, OR_out;

  not not_1 (not_1_out, Y);
  not not_2 (not_2_out, X);
  not not_3 (not_3_out, X_2);
  not not_4 (not_4_out, Z_3);
  not not_5 (not_5_out, Y_5);
  not not_6 (not_6_out, Z_5);
  or OR (OR_out, not_1_out, not_2_out);
  or OR_2 (OR_2_out, not_2_out, Z_2);
  or OR_3 (OR_3_out, not_3_out, not_4_out);
  or OR_4 (OR_4_out, not_4_out, Y_3);
  or OR_5 (OR_5_out, X_4, not_6_out);
  or OR_6 (OR_6_out, not_5_out, X_4);
  or OR_7 (OR_7_out, Y_6, not_6_out);
  and AND (out_16, OR_out, OR_2_out);
  and AND_2 (out_18, OR_3_out, OR_4_out);
  and AND_3 (AND_3_out, OR_5_out, OR_6_out);
  and AND_4 (out_20, AND_3_out, OR_7_out);
  not not_7 (not_7_out, Y_2);
  not not_8 (not_8_out, Z);
  not not_9 (not_9_out, X_3);
  not not_10 (not_10_out, Y_4);
  or OR_8 (OR_8_out, not_7_out, not_8_out);
  or OR_9 (OR_9_out, Y_2, Z);
  or OR_10 (OR_10_out, not_9_out, not_10_out);
  or OR_11 (OR_11_out, not_10_out, Z_4);
  and AND_5 (out_17, OR_8_out, OR_9_out);
  and AND_6 (out_19, OR_10_out, OR_11_out);

  // Notes on the sheet:
  //   LETRA A 
  //   LETRA B
  //   LETRA C 
  //   LETRA E 
  //   LETRA D
  //   Nome: Luisa Nogueira
  //   Matricula:747560
endmodule
