// Logisim project Exercicio03.circ as structural Verilog: 1 circuit, main circuit main
module main (
  input  x,
  input  x_2,
  input  y,
  input  y_2,
  input  w,
  input  z,
  input  z_2,
  input  x_3,
  input  w_2,
  input  y_3,
  input  z_3,
  input  w_3,
  input  x_4,
  input  x_5,
  input  y_4,
  input  y_5,
  input  w_4,
  input  z_4,
  input  w_5,
  input  z_5,
  output out_21,
  output out_22,
  output out_23,
  output out_24,
  output out_25
);

  wire AND_2_out, AND_3_out, AND_4_out, AND_5_out, AND_6_out, AND_7_out, AND_8_out, AND_9_out, AND_10_out,
       AND_11_out, AND_12_out, AND_13_out, AND_14_out, AND_15_out, AND_16_out, AND_17_out, AND_18_out,
       AND_19_out, AND_20_out, AND_21_out, AND_22_out, AND_23_out, AND_24_out, AND_25_out, AND_out,
       not_1_out, not_2_out, not_3_out, not_4_out, not_5_out, not_6_out, not_8_out, not_9_out, not_10_out,
       not_11_out, not_12_out, not_13_out, not_14_out, not_15_out, not_16_out, not_17_out, OR_2_out,
       OR_3_out, OR_4_out, OR_5_out, OR_6_out, OR_11_out, OR_12_out, OR_out;

  not not_1 (not_1_out, x);
  not not_2 (not_2_out, y);
  not not_3 (not_3_out, z);
  not not_4 (not_4_out, x_3);
  not not_5 (not_5_out, y_3);
  not not_6 (not_6_out, z_3);
  not not_7 (not_5_out, w_3);
  not not_8 (not_8_out, x_5);
  not not_9 (not_9_out, y_5);
  not not_10 (not_10_out, w_5);
  not not_11 (not_11_out, y_5);
  and AND (AND_out, not_1_out, w, not_3_out);
  and AND_2 (AND_2_out, not_2_out, not_3_out, w);
  and AND_3 (AND_3_out, not_1_out, y, w);
  and AND_4 (AND_4_out, not_4_out, not_4_out, not_5_out, not_6_out);
  and AND_5 (AND_5_out, not_5_out, not_6_out, not_5_out);
  and AND_6 (AND_6_out, not_4_out, not_5_out, w_3);
  and AND_7 (AND_7_out, y_3, not_5_out, z_3);
  and AND_8 (AND_8_out, x_3, not_5_out, not_5_out);
  and AND_9 (AND_9_out, x_3, not_5_out, not_5_out);
  or OR (OR_out, AND_out, AND_2_out);
  and AND_10 (AND_10_out, not_8_out, not_10_out, not_9_out);
  and AND_11 (AND_11_out, not_8_out, not_10_out, not_11_out);
  and AND_12 (AND_12_out, not_8_out, not_10_out, not_11_out);
  and AND_13 (AND_13_out, not_9_out, not_10_out, not_11_out);
  and AND_14 (AND_14_out, w_5, y_5, y_5);
  and AND_15 (AND_15_out, x_5, y_5, w_5);
  or OR_2 (OR_2_out, AND_4_out, AND_5_out);
  or OR_3 (OR_3_out, OR_2_out, OR_4_out, OR_4_out);
  or OR_4 (OR_4_out, AND_6_out, AND_7_out);
  or OR_5 (OR_5_out, AND_8_out, AND_9_out);
  or OR_6 (OR_6_out, AND_14_out, AND_15_out);
  or OR_7 (out_21, OR_out, AND_3_out);
  or OR_8 (out_23, OR_3_out, OR_5_out);
  or OR_9 (out_25, AND_10_out, AND_11_out, AND_12_out, AND_13_out, OR_6_out);
  not not_12 (not_12_out, x_2);
  not not_13 (not_13_out, x_4);
  not not_14 (not_14_out, y_4);
  not not_15 (not_15_out, w_4);
  not not_16 (not_16_out, z_4);
  not not_17 (not_17_out, w_2);
  and AND_16 (AND_16_out, not_12_out, y_2, not_17_out);
  and AND_17 (AND_17_out, not_12_out, z_2, y_2);
  and AND_18 (AND_18_out, y_2, w_2, z_2);
  and AND_19 (AND_19_out, not_13_out, not_14_out, not_15_out);
  and AND_20 (AND_20_out, not_13_out, not_14_out, not_16_out);
  and AND_21 (AND_21_out, not_14_out, not_15_out, not_16_out);
  and AND_22 (AND_22_out, not_14_out, not_15_out, z_4);
  and AND_23 (AND_23_out, not_13_out, w_4, not_16_out);
  and AND_24 (AND_24_out, x_4, not_14_out, not_15_out);
  and AND_25 (AND_25_out, x_4, not_15_out, not_16_out);
  or OR_10 (out_22, AND_16_out, AND_17_out, AND_18_out);
  or OR_11 (OR_11_out, AND_19_out, AND_20_out);
  or OR_12 (OR_12_out, AND_24_out, AND_25_out);
  or OR_13 (out_24, OR_11_out, AND_21_out, AND_22_out, AND_23_out, OR_12_out);

  assign z_5 = y_5;

  // Notes on the sheet:
  //   LETRA A
  //   LETRA B
  //   LETRA C
  //   LETRA D
  //   Nome: Luisa Nogueira
  //   Matricula: 747560
  //   LETRA E
endmodule
