// Logisim project Exercicio04.circ as structural Verilog: 1 circuit, main circuit main
module main (
  input  X,
  input  X_2,
  input  Y,
  input  Y_2,
  input  W,
  input  Z,
  input  Z_2,
  input  W_2,
  input  X_3,
  input  Y_3,
  input  W_3,
  input  X_4,
  input  Z_3,
  input  Y_4,
  input  X_5,
  input  Y_5,
  input  W_4,
  input  Z_4,
  input  W_5,
  input  Z_5,
  output out_21,
  output out_22,
  output out_23,
  output out_24,
  output out_25
);

  wire AND_5_out, AND_6_out, ND_out, not_1_out, not_2_out, not_3_out, not_4_out, not_5_out, not_6_out,
       not_7_out, not_8_out, not_9_out, not_10_out, not_11_out, not_12_out, not_13_out, not_14_out,
       not_15_out, OR_2_out, OR_3_out, OR_4_out, OR_5_out, OR_6_out, OR_7_out, OR_8_out, OR_9_out, OR_10_out,
       OR_11_out, OR_12_out, OR_13_out, OR_14_out, OR_15_out, OR_16_out, OR_17_out, OR_18_out, OR_19_out,
       OR_20_out, OR_21_out, OR_22_out, OR_out;

  not not_1 (not_1_out, Y);
  not not_2 (not_2_out, Z_2);
  not not_3 (not_3_out, X_3);
  not not_4 (not_4_out, Y_3);
  not not_5 (not_5_out, X_5);
  not not_6 (not_6_out, Y_5);
  not not_7 (not_7_out, Z_4);
  or OR (OR_out, X, not_2_out, not_1_out);
  or OR_2 (OR_2_out, not_1_out, not_2_out, W);
  or OR_3 (OR_3_out, Z_3, not_4_out, W_3);
  or OR_4 (OR_4_out, not_3_out, Y_3, W_3);
  or OR_5 (OR_5_out, not_3_out, Y_3, Z_3);
  or OR_6 (OR_6_out, not_3_out, W_3, Z_3);
  or OR_7 (OR_7_out, Z_4, W_5, not_6_out);
  or OR_8 (OR_8_out, not_5_out, Z_4, W_5);
  or OR_9 (OR_9_out, not_5_out, not_6_out, W_5);
  or OR_10 (OR_10_out, not_5_out, not_6_out, not_7_out);
  and AND (out_21, OR_out, OR_2_out);
  and AND_2 (out_23, OR_3_out, OR_4_out, OR_5_out, OR_6_out);
  and and_3 (out_25, OR_7_out, OR_8_out, OR_9_out, OR_10_out);
  not not_8 (not_8_out, X_2);
  not not_9 (not_9_out, Y_2);
  not not_10 (not_10_out, Z);
  not not_11 (not_11_out, W_2);
  not not_12 (not_12_out, X_4);
  not not_13 (not_13_out, Y_4);
  not not_14 (not_14_out, W_4);
  not not_15 (not_15_out, Z_5);
  or OR_11 (OR_11_out, X_2, Y_2, not_10_out);
  or OR_12 (OR_12_out, X_2, not_9_out, not_10_out);
  or OR_13 (OR_13_out, not_9_out, not_10_out, not_11_out);
  or OR_14 (OR_14_out, not_9_out, W_2, not_10_out);
  or OR_15 (OR_15_out, not_8_out, not_9_out, not_10_out);
  or OR_16 (OR_16_out, X_4, not_13_out, W_4);
  or OR_17 (OR_17_out, X_4, not_13_out, not_15_out);
  or OR_18 (OR_18_out, X_4, not_13_out, Z_5);
  or OR_19 (OR_19_out, X_4, not_13_out, not_14_out);
  or OR_20 (OR_20_out, not_13_out, not_14_out, Z_5);
  or OR_21 (OR_21_out, not_13_out, not_14_out, not_15_out);
  or OR_22 (OR_22_out, not_12_out, not_13_out, not_14_out);
  and AND_4 (out_22, OR_11_out, OR_12_out, OR_13_out, OR_14_out, OR_15_out);
  and AND_5 (AND_5_out, OR_16_out, OR_17_out);
  and AND_6 (AND_6_out, OR_18_out, OR_19_out);
  and ND (ND_out, OR_20_out, OR_21_out, OR_22_out);
  and AND_7 (out_24, AND_5_out, AND_6_out, ND_out);

  // Notes on the sheet:
  //   LETRA A 
  //   LETRA B
  //   LETRA C
  //   LETRA D
  //   LETRA E
  //   Nome: Luisa Nogueira
  //   Matricula: 747560
endmodule
