// Logisim project Guia_0605.circ as structural Verilog: 1 circuit, main circuit main
module main (
  input  x,
  input  y,
  input  z,
  output out_4
);

  wire and_1_out;

  and and_1 (and_1_out, y, z);
  or or_1 (out_4, x, x, and_1_out, and_1_out);

  // Notes on the sheet:
  //   s=x+(y.z)
endmodule
