// Logisim project Guia_0606.circ as structural Verilog: 1 circuit, main circuit main
module main (
  input  X,
  input  Y,
  input  Z,
  input  W,
  output out_5
);

  wire and_1_out, or_1_out;

  or or_1 (or_1_out, Y, Y, Y, W, W);
  and and_1 (and_1_out, X, X, X, or_1_out);
  not not_1 (out_5, and_1_out);

  assign Z = Y;

  // Notes on the sheet:
  //   S= X.(Y+Z+W)
endmodule
