// Logisim project Guia06.circ as structural Verilog: 8 circuits, main circuit Guia0605
module Guia0605 (
  input  x,
  input  y,
  input  z,
  output o1,
  output o2
);

  wire and_1_out, and_2_out, and_3_out, and_4_out, and_5_out, not_1_out, not_2_out, not_3_out, not_4_out,
       not_5_out, not_6_out, not_7_out, not_8_out, or_1_out, or_2_out;

  not not_1 (not_1_out, y);
  not not_2 (not_2_out, z);
  not not_3 (not_3_out, y);
  not not_4 (not_4_out, x);
  and and_1 (and_1_out, z, y);
  not not_5 (not_5_out, x);
  and and_2 (and_2_out, x, not_1_out);
  and and_3 (and_3_out, x, not_2_out);
  not not_6 (not_6_out, or_1_out);
  or or_1 (or_1_out, not_3_out, not_4_out);
  not not_7 (not_7_out, and_4_out);
  and and_4 (and_4_out, y, x);
  not not_8 (not_8_out, or_2_out);
  or or_2 (or_2_out, and_1_out, not_5_out);
  or or_3 (o2, and_2_out, and_3_out);
  and and_5 (and_5_out, not_6_out, not_7_out);
  or or_4 (o1, and_5_out, not_8_out);

  // Notes on the sheet:
  //   circuito nao otimizado
  //   circuito otimizado
endmodule

module Guia0606 (
  input  x,
  input  y,
  input  w,
  input  z,
  output out_5,
  output out_6
);

  wire and_1_out, and_2_out, and_3_out, and_4_out, and_5_out, and_6_out, not_1_out, not_2_out, not_3_out,
       not_4_out, not_5_out, not_6_out, not_7_out, not_8_out, not_9_out, not_10_out, or_1_out, or_2_out;

  not not_1 (not_1_out, y);
  not not_2 (not_2_out, w);
  not not_3 (not_3_out, z);
  not not_4 (not_4_out, y);
  not not_5 (not_5_out, x);
  not not_6 (not_6_out, w);
  and and_1 (and_1_out, z, w, y);
  not not_7 (not_7_out, x);
  and and_2 (and_2_out, x, not_1_out);
  and and_3 (and_3_out, x, not_2_out);
  and and_4 (and_4_out, x, not_3_out);
  not not_8 (not_8_out, or_1_out);
  or or_1 (or_1_out, not_4_out, w, not_5_out);
  and and_5 (and_5_out, y, not_6_out, x);
  not not_9 (not_9_out, and_5_out);
  or or_2 (or_2_out, and_1_out, not_7_out);
  not not_10 (not_10_out, or_2_out);
  or or_3 (out_6, and_2_out, and_3_out, and_4_out);
  and and_6 (and_6_out, not_8_out, not_9_out);
  or or_4 (out_5, and_6_out, not_10_out);

  // Notes on the sheet:
  //   circuito nao otimizado
  //   circuito otimizado
endmodule

module Guia0604 (
  input  x,
  input  x_2,
  input  y,
  input  y_2,
  input  w,
  input  w_2,
  input  z,
  input  z_2,
  input  x_3,
  input  x_4,
  input  y_3,
  input  y_4,
  input  w_3,
  input  w_4,
  input  z_3,
  input  z_4,
  input  x_5,
  input  y_5,
  input  w_5,
  input  z_5,
  output a,
  output b,
  output c,
  output d,
  output e
);

  wire not_1_out, not_2_out, not_3_out, not_4_out, not_5_out, not_6_out, not_7_out, not_8_out, not_9_out,
       not_10_out, not_11_out, not_12_out, not_13_out, not_14_out, not_15_out, not_16_out, not_17_out,
       not_18_out, not_19_out, not_20_out, not_21_out, or_1_out, or_2_out, or_3_out, or_4_out, or_5_out,
       or_6_out, or_7_out, or_8_out, or_9_out, or_10_out, or_11_out, or_12_out, or_13_out, or_14_out;

  not not_1 (not_1_out, w);
  not not_2 (not_2_out, y);
  not not_3 (not_3_out, z);
  not not_4 (not_4_out, y);
  not not_5 (not_5_out, z);
  not not_6 (not_6_out, y_3);
  not not_7 (not_7_out, x_3);
  not not_8 (not_8_out, x_3);
  not not_9 (not_9_out, y_3);
  not not_10 (not_10_out, z_3);
  or or_1 (or_1_out, x, y, not_1_out, z);
  or or_2 (or_2_out, x, not_2_out, not_3_out);
  or or_3 (or_3_out, not_4_out, w, not_5_out);
  or or_4 (or_4_out, not_6_out, w_3, z_3);
  or or_5 (or_5_out, not_7_out, w_3, z_3);
  or or_6 (or_6_out, not_8_out, not_9_out, not_10_out);
  and and_1 (a, or_1_out, or_2_out, or_3_out);
  and and_2 (c, or_4_out, or_5_out, or_6_out);
  not not_11 (not_11_out, y_5);
  not not_12 (not_12_out, y_5);
  not not_13 (not_13_out, w_5);
  or or_7 (or_7_out, x_5, not_11_out);
  or or_8 (or_8_out, not_12_out, not_13_out);
  and and_3 (e, or_7_out, or_8_out);
  not not_14 (not_14_out, y_2);
  not not_15 (not_15_out, x_2);
  not not_16 (not_16_out, x_2);
  not not_17 (not_17_out, z_4);
  not not_18 (not_18_out, w_4);
  not not_19 (not_19_out, y_4);
  not not_20 (not_20_out, w_4);
  not not_21 (not_21_out, z_4);
  or or_9 (or_9_out, not_14_out, w_2, z_2);
  or or_10 (or_10_out, not_15_out, y_2, w_2);
  or or_11 (or_11_out, not_16_out, y_2, z_2);
  or or_12 (or_12_out, x_4, w_4, not_17_out);
  or or_13 (or_13_out, x_4, y_4, not_18_out, z_4);
  or or_14 (or_14_out, not_19_out, not_20_out, not_21_out);
  and and_4 (b, or_9_out, or_10_out, or_11_out);
  and and_5 (d, or_12_out, or_13_out, or_14_out);
endmodule

module Guia0603 (
  input  x,
  input  x_2,
  input  y,
  input  y_2,
  input  w,
  input  w_2,
  input  z,
  input  z_2,
  input  x_3,
  input  y_3,
  input  x_4,
  input  w_3,
  input  y_4,
  input  z_3,
  input  w_4,
  input  z_4,
  input  x_5,
  input  y_5,
  input  w_5,
  input  z_5,
  output b,
  output a,
  output d,
  output c,
  output e
);

  wire and_1_out, and_2_out, and_3_out, and_4_out, and_5_out, and_6_out, and_7_out, and_8_out, and_9_out,
       and_10_out, and_11_out, and_12_out, and_13_out, and_14_out, and_15_out, and_16_out, and_17_out,
       and_18_out, and_19_out, and_20_out, and_21_out, not_1_out, not_2_out, not_3_out, not_4_out, not_5_out,
       not_6_out, not_7_out, not_8_out, not_9_out, not_10_out, not_11_out, not_12_out, not_13_out,
       not_14_out, not_15_out, not_16_out, not_17_out, not_18_out, not_19_out, not_20_out, not_21_out,
       not_22_out, not_23_out, not_24_out, not_25_out, not_26_out, not_27_out, not_28_out, not_29_out,
       not_30_out, not_31_out, not_32_out, not_33_out, not_34_out, not_35_out, not_36_out;

  not not_1 (not_1_out, x);
  not not_2 (not_2_out, y);
  not not_3 (not_3_out, w);
  not not_4 (not_4_out, x);
  not not_5 (not_5_out, z);
  not not_6 (not_6_out, x);
  not not_7 (not_7_out, y);
  not not_8 (not_8_out, x_3);
  not not_9 (not_9_out, y_3);
  not not_10 (not_10_out, w_3);
  not not_11 (not_11_out, x_3);
  not not_12 (not_12_out, y_3);
  not not_13 (not_13_out, z_3);
  not not_14 (not_14_out, y_3);
  not not_15 (not_15_out, w_3);
  not not_16 (not_16_out, z_3);
  not not_17 (not_17_out, y_5);
  not not_18 (not_18_out, w_5);
  not not_19 (not_19_out, x_5);
  not not_20 (not_20_out, z_5);
  not not_21 (not_21_out, w_5);
  not not_22 (not_22_out, z_5);
  and and_1 (and_1_out, not_1_out, not_2_out, not_3_out, z);
  and and_2 (and_2_out, not_4_out, w, not_5_out);
  and and_3 (and_3_out, not_6_out, y, w);
  and and_4 (and_4_out, x, not_7_out, w);
  and and_5 (and_5_out, not_8_out, not_9_out, not_10_out);
  and and_6 (and_6_out, not_11_out, not_12_out, not_13_out);
  and and_7 (and_7_out, not_14_out, not_15_out, not_16_out);
  and and_8 (and_8_out, y_3, w_3, z_3);
  and and_9 (and_9_out, x_3, w_3, z_3);
  and and_10 (and_10_out, not_17_out, not_18_out);
  and and_11 (and_11_out, not_19_out, w_5, not_20_out);
  and and_12 (and_12_out, x_5, not_21_out, not_22_out);
  and and_13 (and_13_out, x_5, y_5, w_5, z_5);
  or or_1 (a, and_1_out, and_2_out, and_3_out, and_4_out);
  or or_2 (c, and_5_out, and_6_out, and_7_out, and_8_out, and_9_out);
  or or_3 (e, and_10_out, and_11_out, and_12_out, and_13_out);
  not not_23 (not_23_out, y_2);
  and and_14 (and_14_out, not_23_out, not_24_out, not_25_out);
  not not_24 (not_24_out, w_2);
  not not_25 (not_25_out, z_2);
  not not_26 (not_26_out, x_2);
  and and_15 (and_15_out, not_26_out, not_27_out, w_2);
  not not_27 (not_27_out, y_2);
  and and_16 (and_16_out, y_2, not_28_out, z_2);
  not not_28 (not_28_out, w_2);
  and and_17 (and_17_out, x_2, not_29_out, not_30_out);
  not not_29 (not_29_out, y_2);
  not not_30 (not_30_out, w_2);
  not not_31 (not_31_out, y_4);
  not not_32 (not_32_out, z_4);
  not not_33 (not_33_out, w_4);
  not not_34 (not_34_out, z_4);
  not not_35 (not_35_out, x_4);
  not not_36 (not_36_out, z_4);
  or or_4 (b, and_14_out, and_15_out, and_16_out, and_17_out);
  and and_18 (and_18_out, not_31_out, w_4, not_32_out);
  and and_19 (and_19_out, y_4, not_33_out, not_34_out);
  and and_20 (and_20_out, not_35_out, y_4, z_4);
  and and_21 (and_21_out, x_4, y_4, not_36_out);
  or or_5 (d, and_18_out, and_19_out, and_20_out, and_21_out);
endmodule

module Guia0602 (
  input  X,
  input  X_2,
  input  Y,
  input  Y_2,
  input  Z,
  input  Z_2,
  input  X_3,
  input  X_4,
  input  Y_3,
  input  Y_4,
  input  Z_3,
  input  Z_4,
  input  X_5,
  input  Y_5,
  input  Z_5,
  output out_16,
  output out_17,
  output out_18,
  output out_19,
  output out_20
);

  wire not_1_out, not_2_out, not_3_out, not_4_out, not_5_out, not_6_out, not_7_out, not_8_out, not_9_out,
       not_10_out, not_11_out, not_12_out, not_13_out, or_1_out, or_2_out, or_3_out, or_4_out, or_5_out,
       or_6_out, or_7_out, or_8_out, or_9_out, or_10_out, or_11_out, or_12_out, or_13_out;

  not not_1 (not_1_out, X);
  not not_2 (not_2_out, Z);
  not not_3 (not_3_out, Z_5);
  or or_1 (or_1_out, not_1_out, Y);
  or or_2 (or_2_out, not_1_out, not_2_out);
  not not_4 (not_4_out, X_3);
  or or_3 (or_3_out, not_4_out, Y_3);
  not not_5 (not_5_out, Y_3);
  or or_4 (or_4_out, X_3, not_5_out, Z_3);
  or or_5 (or_5_out, Y_3, not_6_out);
  not not_6 (not_6_out, Z_3);
  not not_7 (not_7_out, X_5);
  not not_8 (not_8_out, Y_5);
  and and_1 (out_16, or_1_out, or_2_out);
  and and_2 (out_18, or_3_out, or_4_out, or_5_out);
  or or_6 (or_6_out, not_7_out, not_3_out);
  or or_7 (or_7_out, X_5, not_8_out, Z_5);
  or or_8 (or_8_out, Y_5, not_3_out);
  and and_3 (out_20, or_6_out, or_7_out, or_8_out);
  not not_9 (not_9_out, Y_2);
  not not_10 (not_10_out, Z_2);
  not not_11 (not_11_out, Y_4);
  or or_9 (or_9_out, X_2, not_10_out);
  or or_10 (or_10_out, not_9_out, not_10_out);
  not not_12 (not_12_out, X_4);
  not not_13 (not_13_out, Z_4);
  and and_4 (out_17, or_9_out, or_10_out);
  or or_11 (or_11_out, not_12_out, not_11_out);
  or or_12 (or_12_out, X_4, Y_4, Z_4);
  or or_13 (or_13_out, not_11_out, not_13_out);
  and and_5 (out_19, or_11_out, or_12_out, or_13_out);

  // Notes on the sheet:
  //   A:
  //   C:
  //   E:
  //   B:
  //   D:
endmodule

module Guia0601 (
  input  x,
  input  x_2,
  input  y,
  input  y_2,
  input  z,
  input  z_2,
  input  x_3,
  input  x_4,
  input  y_3,
  input  y_4,
  input  z_3,
  input  z_4,
  input  x_5,
  input  y_5,
  input  z_5,
  output o,
  output o_2,
  output o_3,
  output o_4,
  output out_20
);

  wire and_1_out, and_2_out, and_3_out, and_4_out, and_5_out, and_6_out, and_7_out, and_8_out, and_9_out,
       and_10_out, nand_1_out, not_1_out, not_2_out, not_3_out, not_4_out, not_5_out, not_6_out, not_7_out,
       not_8_out;

  not not_1 (not_1_out, z);
  not not_2 (not_2_out, x_3);
  not not_3 (not_3_out, x_3);
  not not_4 (not_4_out, x_5);
  not not_5 (not_5_out, z_5);
  and and_1 (and_1_out, x, not_1_out);
  and and_2 (and_2_out, x, y);
  and and_3 (and_3_out, not_2_out, z_4);
  and and_4 (and_4_out, y_3, z_4);
  and and_5 (and_5_out, not_3_out, y_3);
  and and_6 (and_6_out, not_4_out, not_5_out);
  or or_1 (out_20, and_6_out, and_7_out);
  and and_7 (and_7_out, x_5, z_5);
  or or_2 (o, and_1_out, and_2_out);
  or or_3 (o_3, and_3_out, and_4_out, and_5_out);
  not not_6 (not_6_out, x_4);
  not not_7 (not_7_out, y_4);
  not not_8 (not_8_out, x_2);
  and and_8 (and_8_out, not_6_out, y_4);
  and and_9 (and_9_out, not_7_out, z_3);
  nand nand_1 (nand_1_out, x_2, y_2);
  or or_4 (o_2, nand_1_out, and_10_out);
  and and_10 (and_10_out, not_8_out, z_2);
  or or_5 (o_4, and_8_out, and_9_out);

  // Notes on the sheet:
  //   A:
  //   C:
  //   E:
  //   B:
  //   D:
endmodule

module Guia0607 (
  input  X,
  input  Y,
  input  Z,
  output O
);

  wire not_1_out, not_2_out, not_3_out, not_4_out, or_1_out, or_2_out, or_3_out;

  not not_1 (not_1_out, Y);
  not not_2 (not_2_out, Z);
  not not_3 (not_3_out, X);
  not not_4 (not_4_out, Y);
  or or_1 (or_1_out, X, not_1_out, not_2_out);
  or or_2 (or_2_out, not_3_out, Y, Z);
  and and_1 (O, or_1_out, or_2_out, or_3_out);
  or or_3 (or_3_out, X, not_4_out, Z);

  // Notes on the sheet:
  //   MINIMIZADO PARA X'Y' + Y'Z + XY
endmodule

module Guia0608 (
  input  w,
  input  x,
  input  y,
  input  z,
  output o
);

  wire and_1_out, and_2_out, and_3_out, not_1_out, not_2_out, not_3_out, not_4_out, not_5_out;

  not not_1 (not_1_out, w);
  not not_2 (not_2_out, x);
  not not_3 (not_3_out, z);
  not not_4 (not_4_out, y);
  not not_5 (not_5_out, z);
  and and_1 (and_1_out, not_1_out, not_2_out, y, not_3_out);
  and and_2 (and_2_out, w, not_4_out, not_5_out);
  and and_3 (and_3_out, w, x, y, z);
  or or_1 (o, and_1_out, and_2_out, and_3_out);

  // Notes on the sheet:
  //   minimizado para w'x'yz' + wy'z'+wxyz
endmodule
