// Logisim project Guia0601.circ as structural Verilog: 1 circuit, main circuit main
module main (
  input  x,
  input  y,
  input  z,
  input  x_2,
  input  y_2,
  input  z_2,
  input  x_3,
  input  y_3,
  input  z_3,
  input  x_4,
  input  y_4,
  input  z_4,
  input  x_5,
  input  y_5,
  input  z_5,
  output s,
  output s_2,
  output s_3,
  output s_4,
  output s_5
);

  wire And_2_out, And_3_out, And_4_out, And_5_out, And_6_out, And_7_out, And_8_out, And_9_out, And_10_out,
       And_11_out, And_12_out, And_out, not_1_out, not_2_out, not_3_out, not_4_out, not_5_out, not_6_out,
       not_7_out, not_8_out, not_9_out, Or_3_out, Or_4_out;

  not not_1 (not_1_out, y);
  and And (And_out, not_1_out, z);
  and And_2 (And_2_out, x, z);
  not not_2 (not_2_out, x_2);
  and And_3 (And_3_out, not_2_out, y_2);
  and And_4 (And_4_out, y_2, not_3_out);
  not not_3 (not_3_out, z_2);
  and And_5 (And_5_out, y_3, not_4_out);
  not not_4 (not_4_out, z_3);
  and And_6 (And_6_out, x_3, not_5_out);
  not not_5 (not_5_out, z_3);
  and And_7 (And_7_out, x_3, y_3);
  not not_6 (not_6_out, x_4);
  and And_8 (And_8_out, not_6_out, z_4);
  not not_7 (not_7_out, x_4);
  and And_9 (And_9_out, not_7_out, y_4);
  and And_10 (And_10_out, y_4, z_4);
  not not_8 (not_8_out, x_5);
  and And_11 (And_11_out, not_8_out, not_9_out);
  not not_9 (not_9_out, z_5);
  and And_12 (And_12_out, x_5, z_5);
  or Or (s, And_out, And_2_out);
  or Or_2 (s_2, And_3_out, And_4_out);
  or Or_3 (Or_3_out, And_5_out, And_6_out);
  or Or_4 (Or_4_out, And_8_out, And_9_out);
  or Or_5 (s_5, And_11_out, And_12_out);
  or Or_6 (s_3, Or_3_out, And_7_out);
  or Or_7 (s_4, Or_4_out, And_10_out);

  // Notes on the sheet:
  //   a)
  //   b)
  //   c)
  //   d)
  //   e)
  //   -------------------------- Exercício 1 ---------------------------
endmodule
