// Logisim project Guia0602.circ as structural Verilog: 1 circuit, main circuit main
module main (
  input  X,
  input  Y,
  input  Z,
  input  X_2,
  input  Y_2,
  input  Z_2,
  input  X_3,
  input  Y_3,
  input  Z_3,
  input  X_4,
  input  Y_4,
  input  Z_4,
  input  X_5,
  input  Y_5,
  input  Z_5,
  output s,
  output s_2,
  output s_3,
  output s_4,
  output s_5
);

  wire And_3_out, not_1_out, not_2_out, not_3_out, not_4_out, not_5_out, not_6_out, not_7_out, not_8_out,
       not_9_out, not_10_out, not_11_out, not_12_out, not_13_out, not_14_out, Or_2_out, Or_3_out, Or_4_out,
       Or_5_out, Or_6_out, Or_7_out, Or_8_out, Or_9_out, Or_10_out, Or_11_out, Or_out;

  not not_1 (not_1_out, X);
  or Or (Or_out, not_1_out, Z);
  not not_2 (not_2_out, X);
  or Or_2 (Or_2_out, not_2_out, not_3_out);
  not not_3 (not_3_out, Y);
  or Or_3 (Or_3_out, Y_2, not_4_out);
  not not_4 (not_4_out, Z_2);
  not not_5 (not_5_out, X_2);
  or Or_4 (Or_4_out, not_5_out, not_6_out);
  not not_6 (not_6_out, Z_2);
  or Or_5 (Or_5_out, X_3, not_7_out);
  not not_7 (not_7_out, Z_3);
  or Or_6 (Or_6_out, Y_3, not_8_out);
  not not_8 (not_8_out, Z_3);
  or Or_7 (Or_7_out, X_3, not_9_out);
  not not_9 (not_9_out, Y_3);
  or Or_8 (Or_8_out, Y_4, Z_4);
  not not_10 (not_10_out, Y_4);
  or Or_9 (Or_9_out, not_10_out, not_11_out);
  not not_11 (not_11_out, Z_4);
  not not_12 (not_12_out, Y_5);
  or Or_10 (Or_10_out, not_12_out, Z_5);
  not not_13 (not_13_out, X_5);
  or Or_11 (Or_11_out, not_13_out, not_14_out);
  not not_14 (not_14_out, Y_5);
  and And (s, Or_out, Or_2_out);
  and And_2 (s_2, Or_3_out, Or_4_out);
  and And_3 (And_3_out, Or_5_out, Or_6_out);
  and And_4 (s_4, Or_8_out, Or_9_out);
  and And_5 (s_5, Or_10_out, Or_11_out);
  and And_6 (s_3, And_3_out, Or_7_out);

  // Notes on the sheet:
  //   a)
  //   b)
  //   c)
  //   d)
  //   e)
  //   -------------------------- Exercício 2 ---------------------------
endmodule
