// Logisim project Guia0603.circ as structural Verilog: 1 circuit, main circuit main
module main (
  input  x,
  input  y,
  input  w,
  input  z,
  input  x_2,
  input  y_2,
  input  w_2,
  input  z_2,
  input  x_3,
  input  y_3,
  input  w_3,
  input  z_3,
  input  x_4,
  input  y_4,
  input  w_4,
  input  z_4,
  input  x_5,
  input  y_5,
  input  w_5,
  input  z_5,
  output s,
  output s_2,
  output s_3,
  output s_4,
  output s_5
);

  wire and_2_out, and_3_out, and_4_out, and_5_out, and_6_out, and_7_out, and_8_out, and_9_out, and_10_out,
       and_11_out, and_12_out, and_13_out, and_14_out, and_15_out, and_16_out, and_17_out, and_18_out,
       and_19_out, and_20_out, and_21_out, and_22_out, and_23_out, and_24_out, and_25_out, and_26_out,
       and_27_out, and_28_out, and_29_out, and_out, not_1_out, not_2_out, not_3_out, not_4_out, not_5_out,
       not_6_out, not_7_out, not_8_out, not_9_out, not_10_out, not_11_out, not_12_out, not_13_out,
       not_14_out, not_15_out, not_16_out, not_17_out, not_18_out, not_19_out, not_20_out, not_21_out,
       not_22_out, not_23_out, not_24_out, not_25_out, not_26_out, not_27_out, not_28_out, not_29_out,
       not_30_out, not_31_out, not_32_out, not_33_out, not_34_out, not_35_out, not_36_out, not_37_out,
       not_38_out, not_39_out, not_40_out, not_41_out, not_42_out, not_43_out, not_44_out, not_45_out,
       not_46_out, not_47_out, not_48_out, not_49_out, not_50_out, not_51_out, not_52_out, not_53_out,
       not_54_out, or_2_out, or_3_out, or_4_out, or_5_out, or_6_out, or_7_out, or_8_out, or_9_out, or_10_out,
       or_12_out, or_13_out, or_14_out, or_15_out, or_16_out, or_17_out, or_18_out, or_19_out, or_23_out,
       or_out;

  not not_1 (not_1_out, x);
  not not_2 (not_2_out, z);
  not not_3 (not_3_out, y);
  not not_4 (not_4_out, z);
  not not_5 (not_5_out, x);
  not not_6 (not_6_out, y);
  not not_7 (not_7_out, x_2);
  not not_8 (not_8_out, y_2);
  not not_9 (not_9_out, z_2);
  not not_10 (not_10_out, y_2);
  not not_11 (not_11_out, w_2);
  not not_12 (not_12_out, z_2);
  not not_13 (not_13_out, x_2);
  not not_14 (not_14_out, y_2);
  not not_15 (not_15_out, w_2);
  not not_16 (not_16_out, y_2);
  not not_17 (not_17_out, w_2);
  not not_18 (not_18_out, w_2);
  not not_19 (not_19_out, x_3);
  not not_20 (not_20_out, w_3);
  not not_21 (not_21_out, w_3);
  not not_22 (not_22_out, x_3);
  not not_23 (not_23_out, z_3);
  not not_24 (not_24_out, x_3);
  not not_25 (not_25_out, w_3);
  not not_26 (not_26_out, z_3);
  not not_27 (not_27_out, w_3);
  not not_28 (not_28_out, z_3);
  not not_29 (not_29_out, y_4);
  not not_30 (not_30_out, z_4);
  not not_31 (not_31_out, w_4);
  not not_32 (not_32_out, w_4);
  not not_33 (not_33_out, w_4);
  not not_34 (not_34_out, z_4);
  not not_35 (not_35_out, w_4);
  not not_36 (not_36_out, z_4);
  not not_37 (not_37_out, z_4);
  not not_38 (not_38_out, x_5);
  not not_39 (not_39_out, y_5);
  not not_40 (not_40_out, w_5);
  not not_41 (not_41_out, x_5);
  not not_42 (not_42_out, y_5);
  not not_43 (not_43_out, z_5);
  not not_44 (not_44_out, y_5);
  not not_45 (not_45_out, w_5);
  not not_46 (not_46_out, z_5);
  not not_47 (not_47_out, y_5);
  not not_48 (not_48_out, w_5);
  not not_49 (not_49_out, x_5);
  not not_50 (not_50_out, z_5);
  not not_51 (not_51_out, y_5);
  not not_52 (not_52_out, w_5);
  not not_53 (not_53_out, w_5);
  not not_54 (not_54_out, z_5);
  and \and  (and_out, not_1_out, not_2_out);
  and and_2 (and_2_out, not_3_out, not_4_out);
  and and_3 (and_3_out, not_5_out, w);
  and and_4 (and_4_out, x, w);
  and and_5 (and_5_out, not_7_out, not_9_out);
  and and_6 (and_6_out, not_10_out, not_12_out);
  and and_7 (and_7_out, not_13_out, w_2);
  and and_8 (and_8_out, y_2, z_2);
  and and_9 (and_9_out, x_2, not_17_out);
  and and_10 (and_10_out, x_2, z_2);
  and and_11 (and_11_out, not_19_out, not_21_out);
  and and_12 (and_12_out, not_22_out, not_23_out);
  and and_13 (and_13_out, not_24_out, not_26_out);
  and and_14 (and_14_out, w_3, not_28_out);
  and and_15 (and_15_out, w_3, z_3);
  and and_16 (and_16_out, x_3, z_3);
  and and_17 (and_17_out, not_29_out, not_30_out);
  and and_18 (and_18_out, not_31_out, not_32_out);
  and and_19 (and_19_out, y_4, not_34_out);
  and and_20 (and_20_out, not_35_out, z_4);
  and and_21 (and_21_out, w_4, not_36_out);
  and and_22 (and_22_out, w_4, not_37_out);
  and and_23 (and_23_out, not_38_out, not_40_out);
  and and_24 (and_24_out, not_41_out, not_43_out);
  and and_25 (and_25_out, not_44_out, not_46_out);
  and and_26 (and_26_out, not_47_out, z_5);
  and and_27 (and_27_out, not_49_out, not_50_out);
  and and_28 (and_28_out, x_5, not_52_out);
  and and_29 (and_29_out, x_5, not_54_out);
  or \or  (or_out, and_out, and_2_out);
  or or_2 (or_2_out, or_out, and_3_out);
  or or_3 (or_3_out, and_5_out, and_6_out);
  or or_4 (or_4_out, or_3_out, and_7_out);
  or or_5 (or_5_out, and_11_out, and_12_out);
  or or_6 (or_6_out, or_5_out, and_13_out);
  or or_7 (or_7_out, and_17_out, and_18_out);
  or or_8 (or_8_out, or_7_out, and_19_out);
  or or_9 (or_9_out, and_23_out, and_24_out);
  or or_10 (or_10_out, or_9_out, and_25_out);
  or or_11 (s, or_2_out, and_4_out);
  or or_12 (or_12_out, or_4_out, and_8_out);
  or or_13 (or_13_out, or_6_out, and_14_out);
  or or_14 (or_14_out, or_8_out, and_20_out);
  or or_15 (or_15_out, or_10_out, and_26_out);
  or or_16 (or_16_out, or_12_out, and_9_out);
  or or_17 (or_17_out, or_13_out, and_15_out);
  or or_18 (or_18_out, or_14_out, and_21_out);
  or or_19 (or_19_out, or_15_out, and_27_out);
  or or_20 (s_2, or_16_out, and_10_out);
  or or_21 (s_3, or_17_out, and_16_out);
  or or_22 (s_4, or_18_out, and_22_out);
  or or_23 (or_23_out, or_19_out, and_28_out);
  or or_24 (s_5, or_23_out, and_29_out);

  assign x_4 = w_4;
  assign y_3 = w_3;

  // Notes on the sheet:
  //   a)
  //   b)
  //   c)
  //   d)
  //   e)
  //   -------------------------- Exercício 3 ---------------------------
endmodule
