// Logisim project Guia0604.circ as structural Verilog: 1 circuit, main circuit main
module main (
  input  X,
  input  Y,
  input  W,
  input  Z,
  input  X_2,
  input  Y_2,
  input  W_2,
  input  Z_2,
  input  X_3,
  input  Y_3,
  input  W_3,
  input  Z_3,
  input  X_4,
  input  Y_4,
  input  W_4,
  input  Z_4,
  input  X_5,
  input  Y_5,
  input  W_5,
  input  Z_5,
  output s,
  output s_2,
  output s_3,
  output s_4,
  output s_5
);

  wire and_2_out, and_3_out, and_4_out, and_6_out, and_7_out, and_8_out, and_9_out, and_11_out, and_12_out,
       and_14_out, and_15_out, not_1_out, not_2_out, not_3_out, not_4_out, not_5_out, not_6_out, not_7_out,
       not_8_out, not_9_out, not_10_out, not_11_out, not_12_out, not_13_out, not_14_out, not_15_out,
       not_16_out, not_17_out, not_18_out, not_19_out, not_20_out, not_21_out, not_22_out, not_23_out,
       not_24_out, not_25_out, not_26_out, not_27_out, not_29_out, not_30_out, not_31_out, not_32_out,
       not_33_out, not_34_out, not_35_out, not_36_out, not_37_out, or_2_out, or_3_out, or_4_out, or_5_out,
       or_6_out, or_7_out, or_8_out, or_9_out, or_10_out, or_11_out, or_12_out, or_13_out, or_14_out,
       or_15_out, or_16_out, or_17_out, or_18_out, or_19_out, or_20_out, or_21_out, or_out;

  not not_1 (not_1_out, Y);
  not not_2 (not_2_out, Z);
  not not_3 (not_3_out, Y);
  not not_4 (not_4_out, Z);
  not not_5 (not_5_out, Y_2);
  not not_6 (not_6_out, X_2);
  not not_7 (not_7_out, X_2);
  not not_8 (not_8_out, X_2);
  not not_9 (not_9_out, Y_3);
  not not_10 (not_10_out, X_3);
  not not_11 (not_11_out, Y_3);
  not not_12 (not_12_out, X_3);
  not not_13 (not_13_out, Y_3);
  not not_14 (not_14_out, Z_3);
  not not_15 (not_15_out, Z_4);
  not not_16 (not_16_out, Y_4);
  not not_17 (not_17_out, Z_4);
  not not_18 (not_18_out, Y_4);
  not not_19 (not_19_out, Z_4);
  not not_20 (not_20_out, Y_4);
  not not_21 (not_21_out, W_4);
  not not_22 (not_22_out, Z_4);
  not not_23 (not_23_out, X_4);
  not not_24 (not_24_out, Y_4);
  not not_25 (not_25_out, Z_4);
  not not_26 (not_26_out, Y_5);
  not not_27 (not_27_out, Y_5);
  not not_28 (not_27_out, Z_5);
  not not_29 (not_29_out, Y_5);
  not not_30 (not_30_out, W_5);
  not not_31 (not_31_out, Y_5);
  not not_32 (not_32_out, Y_5);
  not not_33 (not_33_out, W_5);
  not not_34 (not_34_out, Z_5);
  not not_35 (not_35_out, X_5);
  not not_36 (not_36_out, Y_5);
  not not_37 (not_37_out, W_5);
  or \or  (or_out, X, not_2_out);
  or or_2 (or_2_out, not_3_out, not_4_out);
  or or_3 (or_3_out, not_5_out, Z_2);
  or or_4 (or_4_out, not_6_out, W_2);
  or or_5 (or_5_out, not_7_out, Z_2);
  or or_6 (or_6_out, not_8_out, Z_2);
  or or_7 (or_7_out, not_9_out, Z_3);
  or or_8 (or_8_out, not_10_out, W_3);
  or or_9 (or_9_out, not_12_out, not_14_out);
  or or_10 (or_10_out, X_4, not_15_out);
  or or_11 (or_11_out, X_4, not_17_out);
  or or_12 (or_12_out, not_18_out, not_19_out);
  or or_13 (or_13_out, not_20_out, not_22_out);
  or or_14 (or_14_out, not_23_out, not_25_out);
  or or_15 (or_15_out, X_5, W_5);
  or or_16 (or_16_out, X_5, Z_5);
  or or_17 (or_17_out, X_5, not_27_out);
  or or_18 (or_18_out, X_5, not_30_out);
  or or_19 (or_19_out, X_5, Z_5);
  or or_20 (or_20_out, not_32_out, not_34_out);
  or or_21 (or_21_out, not_35_out, not_37_out);
  and \and  (s, or_out, or_2_out);
  and and_2 (and_2_out, or_3_out, or_4_out);
  and and_3 (and_3_out, and_2_out, or_5_out);
  and and_4 (and_4_out, or_7_out, or_8_out);
  and and_5 (s_3, and_4_out, or_9_out);
  and and_6 (and_6_out, or_10_out, or_11_out);
  and and_7 (and_7_out, and_6_out, or_12_out);
  and and_8 (and_8_out, or_15_out, or_16_out);
  and and_9 (and_9_out, and_8_out, or_17_out);
  and and_10 (s_2, and_3_out, or_6_out);
  and and_11 (and_11_out, and_7_out, or_13_out);
  and and_12 (and_12_out, and_9_out, or_18_out);
  and and_13 (s_4, and_11_out, or_14_out);
  and and_14 (and_14_out, and_12_out, or_19_out);
  and and_15 (and_15_out, and_14_out, or_20_out);
  and and_16 (s_5, and_15_out, or_21_out);

  // Notes on the sheet:
  //   a)
  //   b)
  //   c)
  //   d)
  //   e)
  //   -------------------------- Exercício 3 ---------------------------
endmodule
