// Logisim project Guia_0606.circ as structural Verilog: 1 circuit, main circuit main
module main (
  input  x,
  input  y,
  input  w,
  input  z,
  output s
);

  wire not_1_out, not_2_out, not_3_out, or_1_out;

  not not_1 (not_1_out, y);
  not not_2 (not_2_out, w);
  or or_1 (or_1_out, not_1_out, not_2_out, not_3_out);
  not not_3 (not_3_out, z);
  and and_1 (s, x, or_1_out);
endmodule
