// Logisim project Guia_06.circ as structural Verilog: 6 circuits, main circuit Guia_0601
module Guia_0601 (
  input  X,
  input  Y,
  input  Z,
  input  X_2,
  input  Y_2,
  input  Z_2,
  input  X_3,
  input  Y_3,
  input  Z_3,
  input  X_4,
  input  Y_4,
  input  Z_4,
  input  X_5,
  input  Y_5,
  input  Z_5,
  output out_16,
  output out_17,
  output out_18,
  output out_19,
  output out_20
);

  wire and_1_out, and_2_out, and_3_out, and_4_out, and_5_out, and_6_out, and_7_out, and_8_out, and_9_out,
       and_10_out, and_11_out, and_12_out, not_1_out, not_2_out, not_3_out, not_4_out, not_5_out, not_6_out,
       not_7_out, not_8_out, not_9_out, not_10_out;

  not not_1 (not_1_out, Y);
  not not_2 (not_2_out, X_2);
  not not_3 (not_3_out, Z_2);
  not not_4 (not_4_out, Z_3);
  not not_5 (not_5_out, Z_3);
  not not_6 (not_6_out, X_4);
  not not_7 (not_7_out, X_4);
  not not_8 (not_8_out, Z_4);
  not not_9 (not_9_out, X_5);
  not not_10 (not_10_out, Z_5);
  and and_1 (and_1_out, not_1_out, Z);
  and and_2 (and_2_out, X, Z);
  and and_3 (and_3_out, not_2_out, Y_2);
  and and_4 (and_4_out, Y_2, not_3_out);
  and and_5 (and_5_out, Y_3, not_4_out);
  and and_6 (and_6_out, X_3, not_5_out);
  and and_7 (and_7_out, X_3, Y_3);
  and and_8 (and_8_out, not_6_out, Z_4);
  and and_9 (and_9_out, not_7_out, Y_4);
  and and_10 (and_10_out, Y_4, not_8_out);
  and and_11 (and_11_out, not_9_out, not_10_out);
  and and_12 (and_12_out, X_5, Z_5);
  or or_1 (out_16, and_1_out, and_2_out);
  or or_2 (out_17, and_3_out, and_4_out);
  or or_3 (out_18, and_5_out, and_6_out, and_7_out);
  or or_4 (out_19, and_8_out, and_9_out, and_10_out);
  or or_5 (out_20, and_11_out, and_12_out);

  // Notes on the sheet:
  //   a) (y' . z) + (x . z)  
  //   b) (x' . y) + (y . z')  
  //   c) (y . z') + (x . z') + (x . y)  
  //   d) (x' . z) + (x' . y) + (y . z')  
  //   e) (x' . z') + (x . z)  
endmodule

module Guia_0602 (
  input  X,
  input  Y,
  input  Z,
  input  X_2,
  input  Y_2,
  input  Z_2,
  input  X_3,
  input  Y_3,
  input  Z_3,
  input  X_4,
  input  Y_4,
  input  Z_4,
  input  X_5,
  input  Y_5,
  input  Z_5,
  output out_16,
  output out_17,
  output out_18,
  output out_19,
  output out_20
);

  wire not_1_out, not_2_out, not_3_out, not_4_out, not_5_out, not_6_out, not_7_out, not_8_out, not_9_out,
       not_10_out, not_11_out, not_12_out, not_13_out, not_14_out, or_1_out, or_2_out, or_3_out, or_4_out,
       or_5_out, or_6_out, or_7_out, or_8_out, or_9_out, or_10_out, or_11_out;

  not not_1 (not_1_out, X);
  not not_2 (not_2_out, X);
  not not_3 (not_3_out, Y);
  not not_4 (not_4_out, Z_2);
  not not_5 (not_5_out, X_2);
  not not_6 (not_6_out, Z_2);
  not not_7 (not_7_out, Z_3);
  not not_8 (not_8_out, Z_3);
  not not_9 (not_9_out, Y_3);
  not not_10 (not_10_out, Y_4);
  not not_11 (not_11_out, Z_4);
  not not_12 (not_12_out, Y_5);
  not not_13 (not_13_out, X_5);
  not not_14 (not_14_out, Y_5);
  or or_1 (or_1_out, not_1_out, Z);
  or or_2 (or_2_out, not_2_out, not_3_out);
  or or_3 (or_3_out, Y_2, not_4_out);
  or or_4 (or_4_out, not_5_out, not_6_out);
  or or_5 (or_5_out, X_3, not_7_out);
  or or_6 (or_6_out, Y_3, not_8_out);
  or or_7 (or_7_out, X_3, not_9_out);
  or or_8 (or_8_out, Y_4, Z_4);
  or or_9 (or_9_out, not_10_out, not_11_out);
  or or_10 (or_10_out, not_12_out, Z_5);
  or or_11 (or_11_out, not_13_out, not_14_out);
  and and_1 (out_16, or_1_out, or_2_out);
  and and_2 (out_17, or_3_out, or_4_out);
  and and_3 (out_18, or_5_out, or_6_out, or_7_out);
  and and_4 (out_19, or_8_out, or_9_out);
  and and_5 (out_20, or_10_out, or_11_out);

  // Notes on the sheet:
  //   a) (X' + Z) . (X' + Y')  
  //   b) (Y + Z') . (X' + Z')  
  //   c) (X + Z') . (Y + Z') . (X + Y')
  //   d) (Y + Z) . (Y' + Z')
  //   e) (Y' + Z) . (X' + Y')
endmodule

module Guia_0603 (
  input  X,
  input  Y,
  input  W,
  input  Z,
  input  X_2,
  input  Y_2,
  input  W_2,
  input  Z_2,
  input  X_3,
  input  Y_3,
  input  W_3,
  input  Z_3,
  input  X_4,
  input  Y_4,
  input  W_4,
  input  Z_4,
  input  X_5,
  input  Y_5,
  input  W_5,
  input  Z_5,
  output out_21,
  output out_22,
  output out_23,
  output out_24,
  output out_25
);

  wire and_1_out, and_2_out, and_3_out, and_4_out, and_5_out, and_6_out, and_7_out, and_8_out, and_9_out,
       and_10_out, and_11_out, and_12_out, and_13_out, and_14_out, and_15_out, and_16_out, and_17_out,
       and_18_out, and_19_out, and_20_out, and_21_out, and_22_out, and_23_out, and_24_out, and_25_out,
       and_26_out, and_27_out, and_28_out, and_29_out, not_1_out, not_2_out, not_3_out, not_4_out, not_5_out,
       not_6_out, not_7_out, not_8_out, not_9_out, not_10_out, not_11_out, not_12_out, not_13_out,
       not_14_out, not_15_out, not_16_out, not_17_out, not_18_out, not_19_out, not_20_out, not_21_out,
       not_22_out, not_23_out, not_24_out, not_25_out, not_26_out, not_27_out, not_28_out, not_29_out,
       not_30_out, not_31_out, not_32_out, not_33_out, not_34_out, not_35_out, not_36_out, not_37_out,
       not_38_out, not_39_out, not_40_out, not_41_out, not_42_out, not_43_out, not_44_out, not_45_out,
       not_46_out, not_47_out, not_48_out, not_49_out, not_50_out, not_51_out, not_52_out, not_53_out,
       not_54_out, not_55_out, not_56_out;

  not not_1 (not_1_out, X);
  not not_2 (not_2_out, Z);
  not not_3 (not_3_out, Y);
  not not_4 (not_4_out, Z);
  not not_5 (not_5_out, X);
  not not_6 (not_6_out, Y);
  not not_7 (not_7_out, X_2);
  not not_8 (not_8_out, Y_2);
  not not_9 (not_9_out, Z_2);
  not not_10 (not_10_out, Y_2);
  not not_11 (not_11_out, W_2);
  not not_12 (not_12_out, Z_2);
  not not_13 (not_13_out, X_2);
  not not_14 (not_14_out, Y_2);
  not not_15 (not_15_out, W_2);
  not not_16 (not_16_out, Y_2);
  not not_17 (not_17_out, W_2);
  not not_18 (not_18_out, W_2);
  not not_19 (not_19_out, X_3);
  not not_20 (not_20_out, Y_3);
  not not_21 (not_21_out, W_3);
  not not_22 (not_22_out, X_3);
  not not_23 (not_23_out, Y_3);
  not not_24 (not_24_out, Z_3);
  not not_25 (not_25_out, X_3);
  not not_26 (not_26_out, W_3);
  not not_27 (not_27_out, Z_3);
  not not_28 (not_28_out, Y_3);
  not not_29 (not_29_out, W_3);
  not not_30 (not_30_out, Z_3);
  not not_31 (not_31_out, Y_4);
  not not_32 (not_32_out, Z_4);
  not not_33 (not_33_out, X_4);
  not not_34 (not_34_out, W_4);
  not not_35 (not_35_out, W_4);
  not not_36 (not_36_out, Z_4);
  not not_37 (not_37_out, X_4);
  not not_38 (not_38_out, Z_4);
  not not_39 (not_39_out, Z_4);
  not not_40 (not_40_out, X_5);
  not not_41 (not_41_out, Y_5);
  not not_42 (not_42_out, W_5);
  not not_43 (not_43_out, X_5);
  not not_44 (not_44_out, Y_5);
  not not_45 (not_45_out, Z_5);
  not not_46 (not_46_out, Y_5);
  not not_47 (not_47_out, W_5);
  not not_48 (not_48_out, Z_5);
  not not_49 (not_49_out, Y_5);
  not not_50 (not_50_out, W_5);
  not not_51 (not_51_out, X_5);
  not not_52 (not_52_out, Z_5);
  not not_53 (not_53_out, Y_5);
  not not_54 (not_54_out, W_5);
  not not_55 (not_55_out, W_5);
  not not_56 (not_56_out, Z_5);
  and and_1 (and_1_out, not_7_out, not_8_out, not_9_out);
  and and_2 (and_2_out, not_10_out, not_11_out, not_12_out);
  and and_3 (and_3_out, not_13_out, not_14_out, W_2);
  and and_4 (and_4_out, Y_2, not_15_out, Z_2);
  and and_5 (and_5_out, X_2, not_16_out, not_17_out);
  and and_6 (and_6_out, X_2, not_18_out, Z_2);
  and and_7 (and_7_out, not_19_out, not_20_out, not_21_out);
  and and_8 (and_8_out, not_22_out, not_23_out, not_24_out);
  and and_9 (and_9_out, not_25_out, not_26_out, not_27_out);
  and and_10 (and_10_out, not_28_out, not_29_out, not_30_out);
  and and_11 (and_11_out, Y_3, W_3, Z_3);
  and and_12 (and_12_out, X_3, W_3, Z_3);
  and and_13 (and_13_out, not_31_out, W_4, not_32_out);
  and and_14 (and_14_out, not_33_out, Y_4, not_34_out);
  and and_15 (and_15_out, Y_4, not_35_out, not_36_out);
  and and_16 (and_16_out, not_37_out, Y_4, Z_4);
  and and_17 (and_17_out, X_4, W_4, not_38_out);
  and and_18 (and_18_out, X_4, Y_4, not_39_out);
  and and_19 (and_19_out, not_40_out, not_41_out, not_42_out);
  and and_20 (and_20_out, not_43_out, not_44_out, not_45_out);
  and and_21 (and_21_out, not_46_out, not_47_out, not_48_out);
  and and_22 (and_22_out, not_49_out, not_50_out, Z_5);
  and and_23 (and_23_out, not_51_out, W_5, not_52_out);
  and and_24 (and_24_out, X_5, not_53_out, not_54_out);
  and and_25 (and_25_out, X_5, not_55_out, not_56_out);
  and and_26 (and_26_out, not_1_out, W, not_2_out);
  and and_27 (and_27_out, not_3_out, W, not_4_out);
  and and_28 (and_28_out, not_5_out, Y, W);
  and and_29 (and_29_out, X, not_6_out, W);
  or or_1 (out_21, and_26_out, and_27_out, and_28_out, and_29_out);
  or or_2 (out_22, and_1_out, and_2_out, and_3_out, and_4_out, and_5_out, and_6_out);
  or or_3 (out_23, and_7_out, and_8_out, and_9_out, and_10_out, and_11_out, and_12_out);
  or or_4 (out_24, and_13_out, and_14_out, and_15_out, and_16_out, and_17_out, and_18_out);
  or or_5 (out_25, and_19_out, and_20_out, and_21_out, and_22_out, and_23_out, and_24_out, and_25_out);

  // Notes on the sheet:
  //   a) (x' . w . z') + (y' . w . z') + (x' . y . w) + (x . y' . w)
  //   b) (x' . y' . z') + (y' . w'. z') + (x' . y' . w) + (y . w' . z) + (x . y' . w') + (x . w' . z)
  //   c) (x' . y' . w') + (x' . y' . z') + (x' . w' . z') + (y' . w' . z') + (y . w . z) + (x . w . z)
  //   d) (y' . w . z') + (x' . y . w') + (y . w' . z') + (x' . y . z) + (x . w . z') + (x . y . z')
  //   e) (x' . y' . w') + (x' . y' . z') + (y' . w' . z') + (y' . w' . z) + (x' . w . z') + (x . y' . w') + (x . w' . z')
endmodule

module Guia_0604 (
  input  X,
  input  Y,
  input  W,
  input  Z,
  input  X_2,
  input  Y_2,
  input  W_2,
  input  Z_2,
  input  X_3,
  input  Y_3,
  input  W_3,
  input  Z_3,
  input  X_4,
  input  Y_4,
  input  W_4,
  input  Z_4,
  input  X_5,
  input  Y_5,
  input  W_5,
  input  Z_5,
  output out_21,
  output out_22,
  output out_23,
  output out_24,
  output out_25
);

  wire not_1_out, not_2_out, not_3_out, not_4_out, not_5_out, not_6_out, not_7_out, not_8_out, not_9_out,
       not_10_out, not_11_out, not_12_out, not_13_out, not_14_out, not_15_out, not_16_out, not_17_out,
       not_18_out, not_19_out, not_20_out, not_21_out, not_22_out, not_23_out, not_24_out, not_25_out,
       not_26_out, not_27_out, not_28_out, not_29_out, not_30_out, not_31_out, not_32_out, not_33_out,
       not_34_out, not_35_out, not_36_out, not_37_out, not_38_out, not_39_out, not_40_out, or_1_out,
       or_2_out, or_3_out, or_4_out, or_5_out, or_6_out, or_7_out, or_8_out, or_9_out, or_10_out, or_11_out,
       or_12_out, or_13_out, or_14_out, or_15_out, or_16_out, or_17_out, or_18_out, or_19_out, or_20_out,
       or_21_out, or_22_out;

  not not_1 (not_1_out, Y);
  not not_2 (not_2_out, Z);
  not not_3 (not_3_out, Y);
  not not_4 (not_4_out, Z);
  not not_5 (not_5_out, Y_2);
  not not_6 (not_6_out, X_2);
  not not_7 (not_7_out, X_2);
  not not_8 (not_8_out, X_2);
  not not_9 (not_9_out, Y_3);
  not not_10 (not_10_out, X_3);
  not not_11 (not_11_out, X_3);
  not not_12 (not_12_out, Y_3);
  not not_13 (not_13_out, X_3);
  not not_14 (not_14_out, Y_3);
  not not_15 (not_15_out, Z_3);
  not not_16 (not_16_out, Z_4);
  not not_17 (not_17_out, Y_4);
  not not_18 (not_18_out, Z_4);
  not not_19 (not_19_out, Y_4);
  not not_20 (not_20_out, Z_4);
  not not_21 (not_21_out, Y_4);
  not not_22 (not_22_out, W_4);
  not not_23 (not_23_out, Z_4);
  not not_24 (not_24_out, X_4);
  not not_25 (not_25_out, Y_4);
  not not_26 (not_26_out, Z_4);
  not not_27 (not_27_out, Y_5);
  not not_28 (not_28_out, Y_5);
  not not_29 (not_29_out, Y_5);
  not not_30 (not_30_out, Z_5);
  not not_31 (not_31_out, Y_5);
  not not_32 (not_32_out, W_5);
  not not_33 (not_33_out, Y_5);
  not not_34 (not_34_out, W_5);
  not not_35 (not_35_out, Y_5);
  not not_36 (not_36_out, W_5);
  not not_37 (not_37_out, Z_5);
  not not_38 (not_38_out, X_5);
  not not_39 (not_39_out, Y_5);
  not not_40 (not_40_out, W_5);
  or or_1 (or_1_out, X, not_1_out, not_2_out);
  or or_2 (or_2_out, not_3_out, W, not_4_out);
  or or_3 (or_3_out, not_5_out, W_2, Z_2);
  or or_4 (or_4_out, not_6_out, Y_2, W_2);
  or or_5 (or_5_out, not_7_out, Y_2, Z_2);
  or or_6 (or_6_out, not_8_out, W_2, Z_2);
  or or_7 (or_7_out, not_9_out, W_3, Z_3);
  or or_8 (or_8_out, not_10_out, W_3, Z_3);
  or or_9 (or_9_out, not_11_out, not_12_out, W_3);
  or or_10 (or_10_out, not_13_out, not_14_out, not_15_out);
  or or_11 (or_11_out, X_4, W_4, not_16_out);
  or or_12 (or_12_out, X_4, not_17_out, not_18_out);
  or or_13 (or_13_out, not_19_out, W_4, not_20_out);
  or or_14 (or_14_out, not_21_out, not_22_out, not_23_out);
  or or_15 (or_15_out, not_24_out, not_25_out, not_26_out);
  or or_16 (or_16_out, X_5, not_27_out, W_5);
  or or_17 (or_17_out, X_5, not_28_out, Z_5);
  or or_18 (or_18_out, X_5, not_29_out, not_30_out);
  or or_19 (or_19_out, X_5, not_31_out, not_32_out);
  or or_20 (or_20_out, not_33_out, not_34_out, Z_5);
  or or_21 (or_21_out, not_35_out, not_36_out, not_37_out);
  or or_22 (or_22_out, not_38_out, not_39_out, not_40_out);
  and and_1 (out_21, or_1_out, or_2_out);
  and and_2 (out_22, or_3_out, or_4_out, or_5_out, or_6_out);
  and and_3 (out_23, or_7_out, or_8_out, or_9_out, or_10_out);
  and and_4 (out_24, or_11_out, or_12_out, or_13_out, or_14_out, or_15_out);
  and and_5 (out_25, or_16_out, or_17_out, or_18_out, or_19_out, or_20_out, or_21_out, or_22_out);

  // Notes on the sheet:
  //   a) (X + Y' + Z') . (Y' + W + Z')
  //   b) (Y' + W + Z) . (X' + Y + W) . (X' + Y + Z) . (X' + W + Z)
  //   c) (Y' + W + Z) . (X' + W + Z) . (X' + Y' + W) . (X' + Y' + Z')
  //   d) (X + W + Z') . (X + Y' + Z') . (Y' + W + Z') . (Y' + W' + Z') . (X' + Y' + Z')
  //   e) (X + Y' + W) . (X + Y' + Z) . (X + Y' + Z') . (X + Y' + W') . (Y' + W' + Z) . (Y' + W' + Z') . (X' + Y' + W')
endmodule

module Guia_0605 (
  input  X,
  input  Y,
  input  Z,
  input  X_2,
  input  Y_2,
  input  Z_2,
  output x_3,
  output out_8
);

  wire and_1_out, and_2_out, and_3_out, and_4_out, and_5_out, not_1_out, not_2_out, not_3_out, not_4_out,
       not_5_out, not_6_out, not_7_out, not_8_out, or_1_out, or_2_out;

  not not_1 (not_1_out, Y);
  not not_2 (not_2_out, X);
  or or_1 (or_1_out, not_1_out, not_2_out);
  and and_1 (and_1_out, Y, X);
  and and_2 (and_2_out, Z, Y);
  not not_3 (not_3_out, X);
  not not_4 (not_4_out, or_1_out);
  not not_5 (not_5_out, and_1_out);
  or or_2 (or_2_out, and_2_out, not_3_out);
  not not_6 (not_6_out, or_2_out);
  and and_3 (and_3_out, not_4_out, not_5_out);
  or or_3 (out_8, and_3_out, not_6_out);
  not not_7 (not_7_out, Y_2);
  not not_8 (not_8_out, Z_2);
  and and_4 (and_4_out, X_2, not_7_out);
  or or_4 (x_3, and_4_out, and_5_out);
  and and_5 (and_5_out, X_2, not_8_out);

  // Notes on the sheet:
  //   Minimized
endmodule

module Guia_0606 (
  input  X,
  input  Y,
  input  W,
  input  Z,
  input  X_2,
  input  Y_2,
  input  W_2,
  input  Z_2,
  output x_3,
  output out_10
);

  wire and_1_out, and_2_out, and_3_out, and_4_out, and_5_out, and_6_out, not_1_out, not_2_out, not_3_out,
       not_4_out, not_5_out, not_6_out, not_7_out, not_8_out, not_9_out, not_10_out, or_1_out, or_2_out;

  not not_1 (not_1_out, Y);
  not not_2 (not_2_out, X);
  not not_3 (not_3_out, W);
  and and_1 (and_1_out, Z, W, Y);
  not not_4 (not_4_out, X);
  or or_1 (or_1_out, not_1_out, W, not_2_out);
  and and_2 (and_2_out, Y, not_3_out, X);
  or or_2 (or_2_out, and_1_out, not_4_out);
  not not_5 (not_5_out, or_1_out);
  not not_6 (not_6_out, and_2_out);
  not not_7 (not_7_out, or_2_out);
  and and_3 (and_3_out, not_5_out, not_6_out);
  or or_3 (out_10, and_3_out, not_7_out);
  not not_8 (not_8_out, Y_2);
  not not_9 (not_9_out, W_2);
  not not_10 (not_10_out, Z_2);
  and and_4 (and_4_out, X_2, not_8_out);
  and and_5 (and_5_out, X_2, not_9_out);
  and and_6 (and_6_out, X_2, not_10_out);
  or or_4 (x_3, and_4_out, and_5_out, and_6_out);

  // Notes on the sheet:
  //   Minimized
endmodule
