// Logisim project questao06.circ as structural Verilog: 1 circuit, main circuit main
module main (
  input  in_1,
  input  in_2,
  input  in_3,
  input  in_4,
  output out_5
);

  wire and_1_out, and_2_out, and_3_out, not_1_out, not_2_out, not_3_out, not_4_out, not_5_out, not_6_out,
       not_7_out, or_1_out, or_2_out, or_3_out, or_4_out, or_5_out, or_6_out, or_7_out, or_8_out, or_9_out,
       or_10_out;

  or or_1 (or_1_out, in_1, in_3);
  or or_2 (or_2_out, in_1, in_3);
  not not_1 (not_1_out, in_4);
  or or_3 (or_3_out, in_1, not_2_out);
  not not_2 (not_2_out, in_3);
  not not_3 (not_3_out, in_4);
  or or_4 (or_4_out, in_1, not_4_out);
  not not_4 (not_4_out, in_3);
  not not_5 (not_5_out, in_1);
  or or_5 (or_5_out, not_5_out, not_6_out);
  not not_6 (not_6_out, in_2);
  not not_7 (not_7_out, in_4);
  or or_6 (or_6_out, or_1_out, in_4);
  and and_1 (and_1_out, or_6_out, or_7_out);
  or or_7 (or_7_out, or_2_out, not_1_out);
  or or_8 (or_8_out, or_3_out, not_3_out);
  or or_9 (or_9_out, or_4_out, in_4);
  or or_10 (or_10_out, or_5_out, not_7_out);
  and and_2 (and_2_out, and_1_out, or_8_out);
  and and_3 (and_3_out, and_2_out, or_9_out);
  and and_4 (out_5, and_3_out, or_10_out);
endmodule
