// Logisim project Guia0601c.circ as structural Verilog: 1 circuit, main circuit main
module main (
  input  x,
  input  y,
  input  z,
  output s
);

  wire and_1_out, and_2_out, and_3_out, not_1_out, not_2_out;

  not not_1 (not_1_out, z);
  not not_2 (not_2_out, z);
  and and_1 (and_1_out, x, y);
  and and_2 (and_2_out, x, not_1_out);
  and and_3 (and_3_out, y, not_2_out);
  or or_1 (s, and_1_out, and_2_out, and_3_out);

  // Notes on the sheet:
  //   01
  //   c)
  //   Arquitetura de Computadores I - Guia_06
  //   Nome: Larissa Valadares Silqueira
  //   Matricula: 754065-5
endmodule
