// Logisim project Guia0602d.circ as structural Verilog: 1 circuit, main circuit main
module main (
  input  x,
  input  y,
  input  z,
  output s
);

  wire not_1_out, not_2_out, or_1_out, or_2_out;

  not not_1 (not_1_out, y);
  not not_2 (not_2_out, z);
  or or_1 (or_1_out, y, z);
  or or_2 (or_2_out, not_1_out, not_2_out);
  and and_1 (s, or_1_out, or_2_out);

  // Notes on the sheet:
  //   02
  //   d)
  //   Arquitetura de Computadores I - Guia_06
  //   Nome: Larissa Valadares Silqueira
  //   Matricula: 754065-5
  //   s
endmodule
