// Logisim project Guia0603a.circ as structural Verilog: 1 circuit, main circuit main
module main (
  input  x,
  input  y,
  input  w,
  input  z,
  output out_5
);

  wire and_1_out, and_2_out, and_3_out, and_4_out, not_1_out, not_2_out, not_3_out, not_4_out, not_5_out,
       not_6_out, not_7_out;

  not not_1 (not_1_out, x);
  not not_2 (not_2_out, y);
  not not_3 (not_3_out, w);
  not not_4 (not_4_out, x);
  not not_5 (not_5_out, z);
  not not_6 (not_6_out, x);
  not not_7 (not_7_out, y);
  and and_1 (and_1_out, not_1_out, not_2_out, not_3_out, z);
  and and_2 (and_2_out, not_4_out, w, not_5_out);
  and and_3 (and_3_out, not_6_out, y, w);
  and and_4 (and_4_out, x, not_7_out, w);
  or or_1 (out_5, and_1_out, and_2_out, and_3_out, and_4_out);

  // Notes on the sheet:
  //   03
  //   a)
  //   Arquitetura de Computadores I - Guia_06
  //   Nome: Larissa Valadares Silqueira
  //   Matricula: 754065-5
endmodule
