// Logisim project Guia0604c.circ as structural Verilog: 1 circuit, main circuit main
module main (
  input  x,
  input  y,
  input  w,
  input  z,
  output out_5
);

  wire not_1_out, not_2_out, not_3_out, not_4_out, not_5_out, or_1_out, or_2_out, or_3_out;

  not not_1 (not_1_out, x);
  not not_2 (not_2_out, x);
  not not_3 (not_3_out, y);
  not not_4 (not_4_out, z);
  not not_5 (not_5_out, y);
  or or_1 (or_1_out, not_1_out, w, z);
  or or_2 (or_2_out, not_2_out, not_3_out, not_4_out);
  or or_3 (or_3_out, not_5_out, w, z);
  and and_1 (out_5, or_1_out, or_2_out, or_3_out);

  // Notes on the sheet:
  //   04
  //   c)
  //   Arquitetura de Computadores I - Guia_06
  //   Nome: Larissa Valadares Silqueira
  //   Matricula: 754065-5
endmodule
