// Logisim project Guia0604e.circ as structural Verilog: 1 circuit, main circuit main
module main (
  input  x,
  input  y,
  input  w,
  input  z,
  output out_5
);

  wire not_1_out, not_2_out, not_3_out, or_1_out, or_2_out;

  not not_1 (not_1_out, y);
  not not_2 (not_2_out, y);
  not not_3 (not_3_out, w);
  or or_1 (or_1_out, x, not_1_out);
  or or_2 (or_2_out, not_2_out, not_3_out);
  and and_1 (out_5, or_1_out, or_2_out);

  // Notes on the sheet:
  //   04
  //   e)
  //   Arquitetura de Computadores I - Guia_06
  //   Nome: Larissa Valadares Silqueira
  //   Matricula: 754065-5
endmodule
