// Logisim project Guia0606.circ as structural Verilog: 1 circuit, main circuit main
module main (
  input  x,
  input  y,
  input  w,
  input  z,
  output out_5
);

  wire not_1_out, not_2_out, not_3_out, or_1_out;

  not not_1 (not_1_out, y);
  not not_2 (not_2_out, w);
  not not_3 (not_3_out, z);
  or or_1 (or_1_out, not_1_out, not_2_out, not_3_out);
  and and_1 (out_5, x, or_1_out);

  // Notes on the sheet:
  //   06
  //   Arquitetura de Computadores I - Guia_06
  //   Nome: Larissa Valadares Silqueira
  //   Matricula: 754065-5
endmodule
