// Logisim project Guia06.circ as structural Verilog
module _1a (
  input  x,
  input  y,
  input  z,
  output out_4
);

  wire and_1_out, and_2_out, not_1_out;

  not not_1 (not_1_out, y);
  and and_1 (and_1_out, not_1_out, z);
  or or_1 (out_4, and_1_out, and_2_out);
  and and_2 (and_2_out, x, z);
endmodule

module _1b (
  input  x,
  input  y,
  input  z,
  output out_4
);

  wire and_1_out, and_2_out, not_1_out, not_2_out;

  not not_1 (not_1_out, x);
  not not_2 (not_2_out, z);
  and and_1 (and_1_out, not_1_out, y);
  or or_1 (out_4, and_1_out, and_2_out);
  and and_2 (and_2_out, y, not_2_out);
endmodule

module _1c (
  input  x,
  input  y,
  input  z,
  output out_4
);

  wire and_1_out, and_2_out, and_3_out, not_1_out, not_2_out;

  and and_1 (and_1_out, x, not_1_out);
  not not_1 (not_1_out, z);
  and and_2 (and_2_out, x, y);
  and and_3 (and_3_out, y, not_2_out);
  not not_2 (not_2_out, z);
  or or_1 (out_4, and_1_out, and_2_out, and_3_out);
endmodule

module _1d (
  input  x,
  input  y,
  input  z,
  output out_4
);

  wire and_1_out, and_2_out, not_1_out, not_2_out;

  not not_1 (not_1_out, x);
  not not_2 (not_2_out, z);
  and and_1 (and_1_out, not_1_out, z);
  or or_1 (out_4, and_1_out, and_2_out);
  and and_2 (and_2_out, y, not_2_out);
endmodule

module _1e (
  input  x,
  input  y,
  input  z,
  output out_4
);

  wire and_1_out, and_2_out, not_1_out, not_2_out;

  not not_1 (not_1_out, x);
  and and_1 (and_1_out, not_1_out, not_2_out);
  not not_2 (not_2_out, z);
  and and_2 (and_2_out, x, z);
  or or_1 (out_4, and_1_out, and_2_out);
endmodule

module _2a (
  input  x,
  input  y,
  input  z,
  output out_4
);

  wire not_1_out, not_2_out, not_3_out, or_1_out, or_2_out;

  not not_1 (not_1_out, x);
  or or_1 (or_1_out, not_1_out, z);
  not not_2 (not_2_out, x);
  or or_2 (or_2_out, not_2_out, not_3_out);
  not not_3 (not_3_out, y);
  and and_1 (out_4, or_1_out, or_2_out);
endmodule

module _2b (
  input  x,
  input  y,
  input  z,
  output out_4
);

  wire not_1_out, not_2_out, not_3_out, or_1_out, or_2_out;

  not not_1 (not_1_out, z);
  not not_2 (not_2_out, x);
  not not_3 (not_3_out, z);
  or or_1 (or_1_out, y, not_1_out);
  and and_1 (out_4, or_1_out, or_2_out);
  or or_2 (or_2_out, not_2_out, not_3_out);
endmodule

module _2c (
  input  x,
  input  y,
  input  z,
  output out_4
);

  wire not_1_out, not_2_out, or_1_out, or_2_out;

  not not_1 (not_1_out, z);
  not not_2 (not_2_out, y);
  or or_1 (or_1_out, y, not_1_out);
  and and_1 (out_4, or_1_out, or_2_out);
  or or_2 (or_2_out, x, not_2_out);
endmodule

module _2d (
  input  x,
  input  y,
  input  z,
  output out_4
);

  wire not_1_out, not_2_out, or_1_out, or_2_out;

  not not_1 (not_1_out, y);
  not not_2 (not_2_out, z);
  or or_1 (or_1_out, y, z);
  and and_1 (out_4, or_1_out, or_2_out);
  or or_2 (or_2_out, not_1_out, not_2_out);
endmodule

module _2e (
  input  x,
  input  y,
  input  z,
  output out_4
);

  wire not_1_out, not_2_out, not_3_out, not_4_out, or_1_out, or_2_out, or_3_out;

  not not_1 (not_1_out, z);
  not not_2 (not_2_out, x);
  not not_3 (not_3_out, y);
  not not_4 (not_4_out, y);
  or or_1 (or_1_out, x, y, not_1_out);
  and and_1 (out_4, or_1_out, or_2_out, or_3_out);
  or or_2 (or_2_out, not_2_out, not_3_out);
  or or_3 (or_3_out, not_4_out, z);
endmodule

module _3a (
  input  x,
  input  y,
  input  w,
  input  z,
  output out_5
);

  wire and_1_out, and_2_out, and_3_out, and_4_out, not_1_out, not_2_out, not_3_out, not_4_out, not_5_out,
       not_6_out, not_7_out;

  not not_1 (not_1_out, x);
  not not_2 (not_2_out, y);
  not not_3 (not_3_out, w);
  not not_4 (not_4_out, x);
  not not_5 (not_5_out, x);
  not not_6 (not_6_out, z);
  not not_7 (not_7_out, y);
  and and_1 (and_1_out, not_1_out, not_2_out, not_3_out, z);
  and and_2 (and_2_out, not_4_out, y, w);
  and and_3 (and_3_out, not_5_out, w, not_6_out);
  and and_4 (and_4_out, x, not_7_out, w);
  or or_1 (out_5, and_1_out, and_2_out, and_3_out, and_4_out);
endmodule

module _3b (
  input  x,
  input  y,
  input  w,
  input  z,
  output out_5
);

  wire and_1_out, and_2_out, and_3_out, and_4_out, not_1_out, not_2_out, not_3_out, not_4_out, not_5_out,
       not_6_out, not_7_out, not_8_out;

  not not_1 (not_1_out, y);
  not not_2 (not_2_out, w);
  not not_3 (not_3_out, z);
  not not_4 (not_4_out, x);
  not not_5 (not_5_out, y);
  not not_6 (not_6_out, w);
  not not_7 (not_7_out, y);
  not not_8 (not_8_out, w);
  and and_1 (and_1_out, not_1_out, not_2_out, not_3_out);
  and and_2 (and_2_out, not_4_out, not_5_out, w);
  and and_3 (and_3_out, y, not_6_out, z);
  and and_4 (and_4_out, x, not_7_out, not_8_out);
  or or_1 (out_5, and_1_out, and_2_out, and_3_out, and_4_out);
endmodule

module _3c (
  input  x,
  input  y,
  input  w,
  input  z,
  output out_5
);

  wire and_1_out, and_2_out, and_3_out, and_4_out, and_5_out, and_6_out, not_1_out, not_2_out, not_3_out,
       not_4_out, not_5_out, not_6_out, not_7_out, not_8_out, not_9_out, not_10_out, not_11_out, not_12_out;

  not not_1 (not_1_out, x);
  not not_2 (not_2_out, y);
  not not_3 (not_3_out, w);
  not not_4 (not_4_out, x);
  not not_5 (not_5_out, y);
  not not_6 (not_6_out, z);
  not not_7 (not_7_out, x);
  not not_8 (not_8_out, w);
  not not_9 (not_9_out, z);
  not not_10 (not_10_out, y);
  not not_11 (not_11_out, w);
  not not_12 (not_12_out, z);
  and and_1 (and_1_out, not_1_out, not_2_out, not_3_out);
  and and_2 (and_2_out, not_4_out, not_5_out, not_6_out);
  and and_3 (and_3_out, not_7_out, not_8_out, not_9_out);
  and and_4 (and_4_out, y, w, z);
  and and_5 (and_5_out, not_10_out, not_11_out, not_12_out);
  and and_6 (and_6_out, x, w, z);
  or or_1 (out_5, and_1_out, and_2_out, and_3_out, and_4_out, and_5_out, and_6_out);
endmodule

module _3d (
  input  x,
  input  y,
  input  w,
  input  z,
  output out_5
);

  wire and_1_out, and_2_out, and_3_out, and_4_out, not_1_out, not_2_out, not_3_out, not_4_out, not_5_out,
       not_6_out;

  not not_1 (not_1_out, y);
  not not_2 (not_2_out, z);
  not not_3 (not_3_out, w);
  not not_4 (not_4_out, z);
  not not_5 (not_5_out, x);
  not not_6 (not_6_out, z);
  and and_1 (and_1_out, not_1_out, w, not_2_out);
  and and_2 (and_2_out, y, not_3_out, not_4_out);
  and and_3 (and_3_out, not_5_out, y, z);
  and and_4 (and_4_out, x, w, not_6_out);
  or or_1 (out_5, and_1_out, and_2_out, and_3_out, and_4_out);
endmodule

module _3e (
  input  x,
  input  y,
  input  w,
  input  z,
  output out_5
);

  wire and_1_out, and_2_out, and_3_out, and_4_out, not_1_out, not_2_out, not_3_out, not_4_out, not_5_out,
       not_6_out;

  not not_1 (not_1_out, y);
  not not_2 (not_2_out, w);
  not not_3 (not_3_out, x);
  not not_4 (not_4_out, z);
  not not_5 (not_5_out, w);
  not not_6 (not_6_out, z);
  and and_1 (and_1_out, not_1_out, not_2_out);
  and and_2 (and_2_out, not_3_out, w, not_4_out);
  and and_3 (and_3_out, x, not_5_out, not_6_out);
  and and_4 (and_4_out, x, y, w, z);
  or or_1 (out_5, and_1_out, and_2_out, and_3_out, and_4_out);
endmodule

module _4a (
  input  x,
  input  y,
  input  w,
  input  z,
  output out_5
);

  wire not_1_out, not_2_out, not_3_out, not_4_out, not_5_out, or_1_out, or_2_out, or_3_out;

  not not_1 (not_1_out, w);
  not not_2 (not_2_out, y);
  not not_3 (not_3_out, z);
  not not_4 (not_4_out, y);
  not not_5 (not_5_out, z);
  or or_1 (or_1_out, x, y, not_1_out, z);
  or or_2 (or_2_out, x, not_2_out, not_3_out);
  or or_3 (or_3_out, not_4_out, w, not_5_out);
  and and_1 (out_5, or_1_out, or_2_out, or_3_out);
endmodule

module _4b (
  input  x,
  input  y,
  input  w,
  input  z,
  output out_5
);

  wire not_1_out, not_2_out, not_3_out, or_1_out, or_2_out, or_3_out;

  not not_1 (not_1_out, y);
  not not_2 (not_2_out, x);
  not not_3 (not_3_out, x);
  or or_1 (or_1_out, not_1_out, w, z);
  or or_2 (or_2_out, not_2_out, y, w);
  and and_1 (out_5, or_1_out, or_2_out, or_3_out);
  or or_3 (or_3_out, not_3_out, y, z);
endmodule

module _4c (
  input  x,
  input  y,
  input  w,
  input  z,
  output out_5
);

  wire not_1_out, not_2_out, not_3_out, not_4_out, not_5_out, or_1_out, or_2_out, or_3_out;

  not not_1 (not_1_out, y);
  not not_2 (not_2_out, x);
  not not_3 (not_3_out, y);
  not not_4 (not_4_out, z);
  not not_5 (not_5_out, x);
  or or_1 (or_1_out, not_1_out, w, z);
  or or_2 (or_2_out, not_2_out, not_3_out, not_4_out);
  and and_1 (out_5, or_1_out, or_2_out, or_3_out);
  or or_3 (or_3_out, not_5_out, w, z);
endmodule

module _4d (
  input  x,
  input  y,
  input  w,
  input  z,
  output out_5
);

  wire not_1_out, not_2_out, not_3_out, not_4_out, or_1_out, or_2_out, or_3_out;

  not not_1 (not_1_out, z);
  not not_2 (not_2_out, w);
  not not_3 (not_3_out, y);
  not not_4 (not_4_out, z);
  or or_1 (or_1_out, x, w, not_1_out);
  or or_2 (or_2_out, x, y, not_2_out, z);
  or or_3 (or_3_out, not_3_out, not_4_out);
  and and_1 (out_5, or_1_out, or_2_out, or_3_out);
endmodule

module _4e (
  input  x,
  input  y,
  input  w,
  input  z,
  output out_5
);

  wire not_1_out, not_2_out, not_3_out, or_1_out, or_2_out;

  not not_1 (not_1_out, y);
  not not_2 (not_2_out, y);
  not not_3 (not_3_out, w);
  or or_1 (or_1_out, x, not_1_out);
  and and_1 (out_5, or_1_out, or_2_out);
  or or_2 (or_2_out, not_2_out, not_3_out);
endmodule

module _5 (
  input  x,
  input  y,
  input  z,
  output out_4,
  output out_5
);

  wire and_1_out, and_2_out, and_3_out, and_4_out, and_5_out, not_1_out, not_2_out, not_3_out, not_4_out,
       not_5_out, not_6_out, not_7_out, not_8_out, or_1_out, or_2_out;

  not not_1 (not_1_out, y);
  or or_1 (or_1_out, not_1_out, not_2_out);
  not not_2 (not_2_out, x);
  and and_1 (and_1_out, y, x);
  and and_2 (and_2_out, z, y);
  or or_2 (or_2_out, and_2_out, not_3_out);
  not not_3 (not_3_out, x);
  and and_3 (and_3_out, x, not_4_out);
  not not_4 (not_4_out, y);
  and and_4 (and_4_out, x, not_5_out);
  not not_5 (not_5_out, z);
  not not_6 (not_6_out, or_1_out);
  and and_5 (and_5_out, not_6_out, not_7_out);
  not not_7 (not_7_out, and_1_out);
  not not_8 (not_8_out, or_2_out);
  or or_3 (out_5, and_3_out, and_4_out);
  or or_4 (out_4, and_5_out, not_8_out);
endmodule

module _6 (
  input  x,
  input  y,
  input  w,
  input  z,
  output out_5,
  output out_6
);

  wire and_1_out, and_2_out, and_4_out, not_1_out, not_2_out, not_3_out, not_4_out, not_5_out, not_6_out,
       not_7_out, not_8_out, not_9_out, not_10_out, or_1_out, or_2_out, or_3_out;

  not not_1 (not_1_out, y);
  not not_2 (not_2_out, x);
  not not_3 (not_3_out, w);
  and and_1 (and_1_out, z, w, y);
  not not_4 (not_4_out, x);
  not not_5 (not_5_out, y);
  not not_6 (not_6_out, w);
  not not_7 (not_7_out, z);
  not not_8 (not_8_out, or_1_out);
  or or_1 (or_1_out, not_1_out, w, not_2_out);
  and and_2 (and_2_out, y, not_3_out, x);
  not not_9 (not_9_out, and_2_out);
  not not_10 (not_10_out, or_2_out);
  or or_2 (or_2_out, and_1_out, not_4_out);
  or or_3 (or_3_out, not_5_out, not_6_out, not_7_out);
  and and_3 (out_6, or_3_out, x);
  and and_4 (and_4_out, not_8_out, not_9_out);
  or or_4 (out_5, and_4_out, not_10_out);
endmodule
