// Logisim project Exemplo_0503.circ as structural Verilog: 1 circuit, main circuit main
module main (
  input  a,
  input  b,
  output out_3
);

  wire not_1_out;

  not not_1 (not_1_out, b);
  or or_1 (out_3, a, not_1_out);

  // Notes on the sheet:
  //   S=(a|~b)
endmodule
