// Logisim project Exemplo_0505.circ as structural Verilog: 1 circuit, main circuit main
module main (
  input  a,
  input  b,
  output out_3
);

  wire not_1_out, not_2_out;

  not not_1 (not_1_out, a);
  not not_2 (not_2_out, b);
  and and_1 (out_3, not_1_out, not_1_out, not_1_out, not_2_out, not_2_out);

  // Notes on the sheet:
  //   s=(~a&~b)
endmodule
