// Logisim project Exemplo_0506.circ as structural Verilog: 1 circuit, main circuit main
module main (
  input  a,
  input  b,
  output out_3
);

  xnor xnor_1 (out_3, a, b);

  // Notes on the sheet:
  //   s=a xnor b
endmodule
