// Logisim project Exemplo_0507.circ as structural Verilog: 1 circuit, main circuit main
module main (
  input  a,
  input  b,
  output out_3
);

  wire xor_1_out;

  xor xor_1 (xor_1_out, a, b);
  not not_1 (out_3, xor_1_out);

  // Notes on the sheet:
  //   s=~(a^b)=a xor b
endmodule
