// Logisim project Exemplo_0509.circ as structural Verilog: 1 circuit, main circuit main
module main (
  input  A,
  input  B,
  output out_3
);

  wire and_1_out;

  and and_1 (and_1_out, A, A, B, B);
  not not_1 (out_3, and_1_out);

  // Notes on the sheet:
  //   s=~(a&b)
endmodule
