// Logisim project Circuito.circ as structural Verilog: 2 circuits, main circuit main
module main (
);

  // AND_Gate and_1 is placed but not wired
endmodule

module Registro0502 (
  input  in_1,
  input  in_2,
  input  in_3,
  output out_4,
  output out_5
);

  D_Flip_Flop d_ff_1 (.clk(in_2));  // open: D, Q, Qn, preset, en, reset
  D_Flip_Flop d_ff_2 (.D(in_1));  // open: clk, Q, Qn, preset, en, reset
endmodule
