// Logisim project Exemplo_0502.circ as structural Verilog: 1 circuit, main circuit main
module main (
);

  wire a_out, b_out, nand_1_out, nand_2_out, nand_3_out;

  Button a (.out(a_out));
  nand nand_1 (nand_1_out, a_out, a_out);
  Button b (.out(b_out));
  nand nand_2 (nand_2_out, nand_1_out, b_out);
  nand nand_3 (nand_3_out, nand_2_out, nand_2_out);
  LED s (.in(nand_3_out));
endmodule
