// Logisim project Exemplo_0504.circ as structural Verilog: 1 circuit, main circuit main
module main (
);

  wire a_out, b_out, nand_1_out, nand_2_out, nand_3_out, nand_4_out, nand_5_out;

  Button a (.out(a_out));
  Button b (.out(b_out));
  nand nand_1 (nand_1_out, a_out, a_out);
  nand nand_2 (nand_2_out, b_out, b_out);
  nand nand_3 (nand_3_out, nand_1_out, nand_1_out);
  nand nand_4 (nand_4_out, nand_2_out, nand_2_out);
  LED s (.in(nand_5_out));
  nand nand_5 (nand_5_out, nand_3_out, nand_4_out);
endmodule
