// Logisim project Exemplo_0505.circ as structural Verilog: 1 circuit, main circuit main
module main (
);

  wire a_out, b_out, nor_1_out, nor_2_out, nor_3_out, nor_4_out, nor_5_out;

  Button a (.out(a_out));
  Button b (.out(b_out));
  nor nor_1 (nor_1_out, a_out, a_out);
  nor nor_2 (nor_2_out, b_out, b_out);
  nor nor_3 (nor_3_out, nor_1_out, nor_1_out);
  nor nor_4 (nor_4_out, nor_2_out, nor_2_out);
  nor nor_5 (nor_5_out, nor_3_out, nor_4_out);
  LED s (.in(nor_5_out));
endmodule
