// Logisim project Guia-08_circuitos.circ as structural Verilog: 12 circuits, main circuit meio_somador
module meio_somador (
  input  in_1,
  input  in_2,
  output Resultado,
  output Vai
);

  wire and_1_out, and_2_out, not_1_out, not_2_out;

  not not_1 (not_1_out, in_1);
  not not_2 (not_2_out, in_2);
  and and_1 (and_1_out, not_1_out, in_2);
  and and_2 (and_2_out, in_1, not_2_out);
  and and_3 (Vai, in_1, in_2);
  or or_1 (Resultado, and_1_out, and_2_out);
endmodule

module somador_completo (
  input  x,
  input  y,
  input  Vem,
  output Resultado,
  output Vai
);

  wire and_1_out, and_2_out, and_3_out, and_4_out, and_5_out, and_6_out, and_7_out, and_8_out, not_1_out,
       not_2_out, not_3_out, or_1_out, or_2_out, or_3_out, or_4_out;

  not not_1 (not_1_out, y);
  not not_2 (not_2_out, x);
  not not_3 (not_3_out, Vem);
  and and_1 (and_1_out, not_2_out, not_1_out, Vem);
  or or_1 (or_1_out, and_1_out, and_2_out);
  and and_2 (and_2_out, not_2_out, y, not_3_out);
  and and_3 (and_3_out, x, not_1_out, not_3_out);
  or or_2 (or_2_out, and_3_out, and_4_out);
  and and_4 (and_4_out, x, y, Vem);
  and and_5 (and_5_out, not_2_out, y, Vem);
  or or_3 (or_3_out, and_5_out, and_6_out);
  and and_6 (and_6_out, x, not_1_out, Vem);
  and and_7 (and_7_out, x, y, not_3_out);
  or or_4 (or_4_out, and_7_out, and_8_out);
  and and_8 (and_8_out, x, y, Vem);
  or or_5 (Resultado, or_1_out, or_2_out);
  or or_6 (Vai, or_3_out, or_4_out);
endmodule

module \questão_1  (
  input  in_1,
  input  A,
  input  in_3,
  input  in_4,
  input  in_5,
  input  B,
  input  in_7,
  input  in_8,
  output out_9,
  output out_10,
  output out_11,
  output out_12,
  output out_13
);

  wire somador_completo_2_vai, somador_completo_3_vai, somador_completo_4_vai;

  somador_completo somador_completo_1 (
    .x(in_1), .y(in_5), .Vem(somador_completo_2_vai), .Resultado(out_10), .Vai(out_9));
  somador_completo somador_completo_2 (
    .x(A), .y(B), .Vem(somador_completo_3_vai), .Resultado(out_11), .Vai(somador_completo_2_vai));
  somador_completo somador_completo_3 (
    .x(in_3), .y(in_7), .Vem(somador_completo_4_vai), .Resultado(out_12), .Vai(somador_completo_3_vai));
  somador_completo somador_completo_4 (
    .x(in_4), .y(in_8), .Vem(1'b0), .Resultado(out_13), .Vai(somador_completo_4_vai));
endmodule

module meio_subtrador (
  input  in_1,
  input  in_2,
  output out_3,
  output out_4
);

  wire not_1_out, not_2_out;

  not not_1 (not_1_out, in_1);
  not not_2 (not_2_out, in_2);
  xor xor_1 (out_3, in_2, in_1);
  and and_1 (out_4, not_2_out, in_1);
endmodule

module subtrador_completo (
  input  x,
  input  y,
  input  in_3,
  output out_4,
  output out_5
);

  wire and_1_out, and_2_out, and_3_out, not_1_out, xor_1_out;

  not not_1 (not_1_out, y);
  xor xor_1 (xor_1_out, y, x);
  and and_1 (and_1_out, not_1_out, x);
  and and_2 (and_2_out, not_1_out, in_3);
  and and_3 (and_3_out, x, in_3);
  xor xor_2 (out_4, xor_1_out, in_3);
  or or_1 (out_5, and_1_out, and_2_out, and_3_out);
endmodule

module \questão_2  (
  input  a6,
  input  a5,
  input  a4,
  input  a3,
  input  a2,
  input  a1,
  input  b6,
  input  b5,
  input  b4,
  input  b3,
  input  b2,
  input  b1,
  output out_13,
  output out_14,
  output out_15,
  output out_16,
  output out_17,
  output out_18,
  output out_19
);

  wire subtrador_completo_2_out_5, subtrador_completo_3_out_5, subtrador_completo_4_out_5,
       subtrador_completo_5_out_5, subtrador_completo_6_out_5;

  subtrador_completo subtrador_completo_1 (
    .in_3(subtrador_completo_2_out_5), .x(a6), .y(b6), .out_4(out_14), .out_5(out_13));
  subtrador_completo subtrador_completo_2 (
    .in_3(subtrador_completo_3_out_5), .x(a5), .y(b5), .out_4(out_15), .out_5(subtrador_completo_2_out_5));
  subtrador_completo subtrador_completo_3 (
    .in_3(subtrador_completo_4_out_5), .x(a4), .y(b4), .out_4(out_16), .out_5(subtrador_completo_3_out_5));
  subtrador_completo subtrador_completo_4 (
    .in_3(subtrador_completo_5_out_5), .x(a3), .y(b3), .out_4(out_17), .out_5(subtrador_completo_4_out_5));
  subtrador_completo subtrador_completo_5 (
    .in_3(subtrador_completo_6_out_5), .x(a2), .y(b2), .out_4(out_18), .out_5(subtrador_completo_5_out_5));
  subtrador_completo subtrador_completo_6 (
    .in_3(1'b0), .x(a1), .y(b1), .out_4(out_19), .out_5(subtrador_completo_6_out_5));

  // Notes on the sheet:
  //   A
  //   B
endmodule

module comparador_igualdade (
  input  x,
  input  y,
  output out_3
);

  xnor xnor_1 (out_3, x, y);
endmodule

module \questão_3  (
  input  a1,
  input  a2,
  input  a3,
  input  a4,
  input  a5,
  input  b1,
  input  b2,
  input  b3,
  input  b4,
  input  b5,
  output out_11
);

  wire comparador_igualdade_1_out_3, comparador_igualdade_2_out_3, comparador_igualdade_3_out_3,
       comparador_igualdade_4_out_3, comparador_igualdade_5_out_3;

  comparador_igualdade comparador_igualdade_1 (.x(a1), .y(b1), .out_3(comparador_igualdade_1_out_3));
  comparador_igualdade comparador_igualdade_2 (.x(a2), .y(b2), .out_3(comparador_igualdade_2_out_3));
  comparador_igualdade comparador_igualdade_3 (.x(a3), .y(b3), .out_3(comparador_igualdade_3_out_3));
  comparador_igualdade comparador_igualdade_4 (.x(a4), .y(b4), .out_3(comparador_igualdade_4_out_3));
  comparador_igualdade comparador_igualdade_5 (.x(a5), .y(b5), .out_3(comparador_igualdade_5_out_3));
  and and_1 (out_11, comparador_igualdade_1_out_3, comparador_igualdade_2_out_3, comparador_igualdade_3_out_3, comparador_igualdade_4_out_3, comparador_igualdade_5_out_3);

  // Notes on the sheet:
  //   A
  //   B
endmodule

module comparador_disigualdade (
  input  x,
  input  y,
  output out_3
);

  xor xor_1 (out_3, x, y);
endmodule

module calcula_complemento (
  input  in_1,
  input  in_2,
  output out_3,
  output out_4
);

  wire and_1_out, and_2_out, not_1_out, xor_2_out;

  xor xor_1 (out_3, and_1_out, and_2_out);
  and and_1 (and_1_out, in_2, not_1_out);
  and and_2 (and_2_out, xor_2_out, in_2);
  not not_1 (not_1_out, in_1);
  xor xor_2 (xor_2_out, not_1_out, in_2);
  xor xor_3 (out_4, in_2, xor_2_out);
endmodule

module \questão_4  (
  input  a1,
  input  a2,
  input  a3,
  input  a4,
  input  a5,
  input  b1,
  input  b2,
  input  b3,
  input  b4,
  input  b5,
  output out_11
);

  wire comparador_disigualdade_1_out_3, comparador_disigualdade_2_out_3, comparador_disigualdade_3_out_3,
       comparador_disigualdade_4_out_3, comparador_disigualdade_5_out_3;

  comparador_disigualdade comparador_disigualdade_1 (.x(a1), .y(b1), .out_3(comparador_disigualdade_1_out_3));
  comparador_disigualdade comparador_disigualdade_2 (.x(a2), .y(b2), .out_3(comparador_disigualdade_2_out_3));
  comparador_disigualdade comparador_disigualdade_3 (.x(a3), .y(b3), .out_3(comparador_disigualdade_3_out_3));
  comparador_disigualdade comparador_disigualdade_4 (.x(a4), .y(b4), .out_3(comparador_disigualdade_4_out_3));
  comparador_disigualdade comparador_disigualdade_5 (.x(a5), .y(b5), .out_3(comparador_disigualdade_5_out_3));
  and and_1 (out_11, comparador_disigualdade_1_out_3, comparador_disigualdade_2_out_3, comparador_disigualdade_3_out_3, comparador_disigualdade_4_out_3, comparador_disigualdade_5_out_3);

  // Notes on the sheet:
  //   A
  //   B
endmodule

module \questão_5  (
  input  in_1,
  input  in_2,
  input  in_3,
  input  in_4,
  output out_5,
  output out_6,
  output out_7,
  output out_8
);

  wire calcula_complemento_1_out_3, calcula_complemento_3_out_3, calcula_complemento_4_out_3;

  calcula_complemento calcula_complemento_1 (
    .out_3(calcula_complemento_1_out_3), .in_1(in_2), .in_2(calcula_complemento_3_out_3), .out_4(out_6));
  calcula_complemento calcula_complemento_2 (
    .in_1(in_1), .in_2(calcula_complemento_1_out_3), .out_4(out_5));  // open: out_3
  calcula_complemento calcula_complemento_3 (
    .out_3(calcula_complemento_3_out_3), .in_1(in_3), .in_2(calcula_complemento_4_out_3), .out_4(out_7));
  calcula_complemento calcula_complemento_4 (
    .out_3(calcula_complemento_4_out_3), .in_1(in_4), .in_2(1'b0), .out_4(out_8));
endmodule
