// Logisim project Circuitos.circ as structural Verilog: 1 circuit, main circuit main
module main (
  input  D,
  input  CLR,
  input  D_2,
  input  CLR_2,
  input  D_3,
  input  CLR_3,
  input  D_4,
  input  CLR_4,
  input  D_5,
  input  CLR_5,
  input  D_6,
  input  CLR_6,
  input  D_7,
  input  CLR_7,
  input  D_8,
  input  CLR_8,
  output \Saída ,
  output \Saída_2 ,
  output \Saída_do_Moore ,
  output \Saída_do_Mealy ,
  output \Saída_do_FSM ,
  output \Saída_do_Mealy_com_2_sequências ,
  output \Saída_do_Mealy_a_cada_sequência ,
  output \Saída_do_Moore_com_3_sequências ,
  output \Saída_do_Moore_a_cada_sequência ,
  output \Saída_do_FSM_2 ,
  output \Saída_do_FSM_3 
);

  wire and_1_out, and_2_out, and_4_out, and_8_out, and_9_out, and_10_out, and_14_out, and_15_out,
       clock_1_out, clock_2_out, clock_3_out, clock_4_out, clock_5_out, clock_6_out, clock_7_out,
       clock_8_out, controlled_buffer_1_out, controlled_buffer_2_out, controlled_buffer_3_out,
       controlled_buffer_4_out, controlled_buffer_5_out, counter_1_carry, counter_2_carry, d_ff_1_q,
       d_ff_2_q, d_ff_3_q, d_ff_4_q, d_ff_5_q, d_ff_6_q, d_ff_7_q, d_ff_8_q, d_ff_9_q, d_ff_10_q, d_ff_11_q,
       d_ff_12_q, d_ff_13_q, d_ff_14_q, d_ff_15_q, d_ff_16_q, d_ff_17_q, d_ff_18_q, d_ff_19_q, d_ff_20_q,
       d_ff_21_q, d_ff_22_q, d_ff_23_q, d_ff_24_q, d_ff_25_q, d_ff_26_q, d_ff_27_q, d_ff_28_q, d_ff_29_q,
       d_ff_30_q, d_ff_31_q, d_ff_32_q, not_1_out, not_2_out, not_3_out, not_4_out, not_5_out, not_6_out,
       not_7_out, not_8_out, not_9_out, not_10_out, not_11_out, not_12_out, not_13_out, not_14_out,
       not_15_out, not_16_out, not_17_out, not_18_out, not_19_out, not_20_out, not_21_out, or_1_out,
       or_2_out, or_3_out, or_4_out, or_5_out, t_ff_1_q, t_ff_2_q, t_ff_3_q, t_ff_4_q, t_ff_5_q, undriven,
       undriven_2;
  wire [1:0] counter_1_q;
  wire [2:0] counter_2_q;

  Clock clock_1 (.out(clock_1_out));
  Clock clock_2 (.out(clock_2_out));
  Clock clock_3 (.out(clock_3_out));
  Clock clock_4 (.out(clock_4_out));
  Clock clock_5 (.out(clock_5_out));
  Clock clock_6 (.out(clock_6_out));
  D_Flip_Flop d_ff_1 (.clk(clock_1_out), .D(D), .Q(d_ff_1_q), .reset(CLR));  // open: Qn, preset
  assign controlled_buffer_1_out = not_12_out ? clock_4_out : 1'bz;  // Controlled_Buffer controlled_buffer_1
  assign controlled_buffer_2_out = not_13_out ? clock_5_out : 1'bz;  // Controlled_Buffer controlled_buffer_2
  or or_1 (or_1_out, CLR_5, d_ff_6_q);
  assign controlled_buffer_3_out = not_21_out ? clock_6_out : 1'bz;  // Controlled_Buffer controlled_buffer_3
  assign controlled_buffer_4_out = not_18_out ? clock_7_out : 1'bz;  // Controlled_Buffer controlled_buffer_4
  Clock clock_7 (.out(clock_7_out));
  assign controlled_buffer_5_out = not_11_out ? clock_8_out : 1'bz;  // Controlled_Buffer controlled_buffer_5
  Clock clock_8 (.out(clock_8_out));
  D_Flip_Flop d_ff_2 (.clk(clock_2_out), .D(D_2), .Q(d_ff_2_q), .reset(CLR_2));  // open: Qn, preset
  D_Flip_Flop d_ff_3 (.clk(clock_3_out), .D(D_3), .Q(d_ff_3_q), .reset(CLR_3));  // open: Qn, preset
  D_Flip_Flop d_ff_4 (.clk(controlled_buffer_1_out), .D(D_4), .Q(d_ff_4_q), .reset(CLR_4));  // open: Qn, preset
  D_Flip_Flop d_ff_5 (.clk(controlled_buffer_2_out), .D(D_5), .Q(d_ff_5_q), .reset(or_1_out));  // open: Qn, preset
  D_Flip_Flop d_ff_6 (
    .clk(controlled_buffer_2_out), .D(\Saída_do_Mealy_a_cada_sequência ), .Q(d_ff_6_q), .reset(and_1_out));  // open: Qn, preset
  D_Flip_Flop d_ff_7 (.clk(controlled_buffer_3_out), .D(D_6), .Q(d_ff_7_q), .reset(CLR_6));  // open: Qn, preset
  D_Flip_Flop d_ff_8 (.clk(controlled_buffer_4_out), .D(D_7), .Q(d_ff_8_q), .reset(CLR_7));  // open: Qn, preset
  D_Flip_Flop d_ff_9 (.clk(controlled_buffer_5_out), .D(D_8), .Q(d_ff_9_q), .reset(CLR_8));  // open: Qn, preset
  D_Flip_Flop d_ff_10 (.clk(clock_1_out), .D(d_ff_1_q), .Q(d_ff_10_q), .reset(CLR));  // open: Qn, preset
  D_Flip_Flop d_ff_11 (.clk(clock_2_out), .D(d_ff_2_q), .Q(d_ff_11_q), .reset(CLR_2));  // open: Qn, preset
  D_Flip_Flop d_ff_12 (.clk(clock_3_out), .D(d_ff_3_q), .Q(d_ff_12_q), .reset(CLR_3));  // open: Qn, preset
  D_Flip_Flop d_ff_13 (.clk(controlled_buffer_1_out), .D(d_ff_4_q), .Q(d_ff_13_q), .reset(CLR_4));  // open: Qn, preset
  D_Flip_Flop d_ff_14 (
    .clk(controlled_buffer_2_out), .D(d_ff_5_q), .Q(d_ff_14_q), .reset(or_1_out));  // open: Qn, preset
  and and_1 (and_1_out, controlled_buffer_2_out, d_ff_6_q);
  D_Flip_Flop d_ff_15 (.clk(controlled_buffer_3_out), .D(d_ff_7_q), .Q(d_ff_15_q), .reset(CLR_6));  // open: Qn, preset
  D_Flip_Flop d_ff_16 (.clk(controlled_buffer_4_out), .D(d_ff_8_q), .Q(d_ff_16_q), .reset(CLR_7));  // open: Qn, preset
  D_Flip_Flop d_ff_17 (.clk(controlled_buffer_5_out), .D(d_ff_9_q), .Q(d_ff_17_q), .reset(CLR_8));  // open: Qn, preset
  D_Flip_Flop d_ff_18 (.clk(clock_1_out), .D(d_ff_10_q), .Q(d_ff_18_q), .reset(CLR));  // open: Qn, preset
  D_Flip_Flop d_ff_19 (.clk(clock_2_out), .D(d_ff_11_q), .Q(d_ff_19_q), .reset(CLR_2));  // open: Qn, preset
  D_Flip_Flop d_ff_20 (.clk(clock_3_out), .D(d_ff_12_q), .Q(d_ff_20_q), .reset(CLR_3));  // open: Qn, preset
  D_Flip_Flop d_ff_21 (.clk(controlled_buffer_1_out), .D(d_ff_13_q), .Q(d_ff_21_q), .reset(CLR_4));  // open: Qn, preset
  D_Flip_Flop d_ff_22 (
    .clk(controlled_buffer_2_out), .D(d_ff_14_q), .Q(d_ff_22_q), .reset(or_1_out));  // open: Qn, preset
  D_Flip_Flop d_ff_23 (.clk(controlled_buffer_3_out), .D(d_ff_15_q), .Q(d_ff_23_q), .reset(CLR_6));  // open: Qn, preset
  D_Flip_Flop d_ff_24 (.clk(controlled_buffer_4_out), .D(d_ff_16_q), .Q(d_ff_24_q), .reset(CLR_7));  // open: Qn, preset
  D_Flip_Flop d_ff_25 (.clk(controlled_buffer_5_out), .D(d_ff_17_q), .Q(d_ff_25_q), .reset(CLR_8));  // open: Qn, preset
  D_Flip_Flop d_ff_26 (.clk(clock_1_out), .D(d_ff_18_q), .Q(d_ff_26_q), .reset(CLR));  // open: Qn, preset
  not not_1 (not_1_out, d_ff_10_q);
  D_Flip_Flop d_ff_27 (.clk(clock_2_out), .D(d_ff_19_q), .Q(d_ff_27_q), .reset(CLR_2));  // open: Qn, preset
  not not_2 (not_2_out, d_ff_11_q);
  not not_3 (not_3_out, d_ff_12_q);
  not not_4 (not_4_out, d_ff_21_q);
  not not_5 (not_5_out, d_ff_4_q);
  not not_6 (not_6_out, d_ff_22_q);
  not not_7 (not_7_out, d_ff_5_q);
  not not_8 (not_8_out, d_ff_23_q);
  not not_9 (not_9_out, d_ff_7_q);
  not not_10 (not_10_out, d_ff_17_q);
  and and_2 (and_2_out, d_ff_25_q, not_10_out, d_ff_9_q);
  or or_2 (or_2_out, and_2_out, and_10_out);
  not not_11 (not_11_out, \Saída_do_FSM_3 );
  and and_3 (\Saída , d_ff_26_q, d_ff_18_q, not_1_out, d_ff_1_q);
  and and_4 (and_4_out, d_ff_27_q, d_ff_19_q, not_2_out, d_ff_2_q);
  D_Flip_Flop d_ff_28 (.clk(clock_3_out), .D(d_ff_20_q), .Q(d_ff_28_q), .reset(CLR_3));  // open: Qn, preset
  and and_5 (\Saída_do_Mealy , d_ff_28_q, d_ff_20_q, not_3_out, d_ff_3_q);
  D_Flip_Flop d_ff_29 (.clk(controlled_buffer_1_out), .D(d_ff_21_q), .Q(d_ff_29_q), .reset(CLR_4));  // open: Qn, preset
  and and_6 (\Saída_do_FSM , d_ff_29_q, not_4_out, d_ff_13_q, not_5_out);
  not not_12 (not_12_out, \Saída_do_FSM );
  D_Flip_Flop d_ff_30 (
    .clk(controlled_buffer_2_out), .D(d_ff_22_q), .Q(d_ff_30_q), .reset(or_1_out));  // open: Qn, preset
  and and_7 (\Saída_do_Mealy_a_cada_sequência , d_ff_30_q, not_6_out, d_ff_14_q, not_7_out);
  not not_13 (not_13_out, \Saída_do_Mealy_com_2_sequências );
  D_Flip_Flop d_ff_31 (.clk(controlled_buffer_3_out), .D(d_ff_23_q), .Q(d_ff_31_q), .reset(CLR_6));  // open: Qn, preset
  and and_8 (and_8_out, d_ff_31_q, not_8_out, d_ff_15_q, not_9_out);
  D_Flip_Flop d_ff_32 (.clk(controlled_buffer_4_out), .D(d_ff_24_q), .Q(d_ff_32_q), .reset(CLR_7));  // open: Qn, preset
  not not_14 (not_14_out, d_ff_32_q);
  or or_3 (or_3_out, d_ff_32_q, not_14_out);
  and and_9 (and_9_out, or_3_out, or_5_out);
  not not_15 (not_15_out, d_ff_24_q);
  not not_16 (not_16_out, d_ff_16_q);
  not not_17 (not_17_out, d_ff_8_q);
  not not_18 (not_18_out, \Saída_do_FSM_2 );
  Counter #(.width(2), .max('h3)) counter_1 (
    .D(2'b01), .count(undriven), .Q(counter_1_q), .carry(counter_1_carry), .clk(controlled_buffer_5_out),
    .clr(CLR_8));  // open: load, preset, down
  not not_19 (not_19_out, d_ff_25_q);
  not not_20 (not_20_out, d_ff_9_q);
  and and_10 (and_10_out, not_19_out, d_ff_17_q, not_20_out);
  and and_11 (\Saída_do_FSM_3 , or_2_out, or_4_out);
  D_Flip_Flop d_ff_33 (.clk(clock_2_out), .D(and_4_out), .Q(\Saída_2 ), .reset(CLR_2));  // open: Qn, preset
  D_Flip_Flop d_ff_34 (
    .clk(clock_3_out), .D(\Saída_do_Mealy ), .Q(\Saída_do_Moore ), .reset(CLR_3));  // open: Qn, preset
  T_Flip_Flop t_ff_1 (
    .clk(controlled_buffer_2_out), .T(\Saída_do_Mealy_a_cada_sequência ), .Q(t_ff_1_q), .reset(CLR_5));  // open: Qn, preset
  D_Flip_Flop d_ff_35 (
    .clk(controlled_buffer_3_out), .D(and_8_out), .Q(\Saída_do_Moore_a_cada_sequência ), .reset(CLR_6));  // open: Qn, preset
  and and_12 (\Saída_do_FSM_2 , and_9_out, not_15_out, not_16_out, not_17_out);
  // Probe on counter_1_q
  or or_4 (or_4_out, counter_1_carry, t_ff_2_q);
  // Probe on counter_2_q
  Counter #(.width(3), .max('h4)) counter_2 (
    .D(3'b001), .count(undriven_2), .Q(counter_2_q), .carry(counter_2_carry), .clk(controlled_buffer_4_out),
    .clr(CLR_7));  // open: load, preset, down
  T_Flip_Flop t_ff_2 (
    .clk(controlled_buffer_5_out), .T(counter_1_carry), .Q(t_ff_2_q), .reset(CLR_8));  // open: Qn, preset
  and and_13 (\Saída_do_Mealy_com_2_sequências , t_ff_1_q, \Saída_do_Mealy_a_cada_sequência );
  T_Flip_Flop t_ff_3 (
    .clk(controlled_buffer_3_out), .T(\Saída_do_Moore_a_cada_sequência ), .Q(t_ff_3_q), .reset(CLR_6));  // open: Qn, preset
  or or_5 (or_5_out, counter_2_carry, t_ff_4_q);
  and and_14 (and_14_out, t_ff_3_q, \Saída_do_Moore_a_cada_sequência );
  T_Flip_Flop t_ff_4 (
    .clk(controlled_buffer_4_out), .T(counter_2_carry), .Q(t_ff_4_q), .reset(CLR_7));  // open: Qn, preset
  T_Flip_Flop t_ff_5 (.clk(controlled_buffer_3_out), .T(and_14_out), .Q(t_ff_5_q), .reset(CLR_6));  // open: Qn, preset
  and and_15 (and_15_out, t_ff_5_q, \Saída_do_Moore_a_cada_sequência );
  T_Flip_Flop t_ff_6 (
    .clk(controlled_buffer_3_out), .T(and_15_out), .Q(\Saída_do_Moore_com_3_sequências ), .reset(CLR_6));  // open: Qn, preset
  not not_21 (not_21_out, \Saída_do_Moore_com_3_sequências );

  // Notes on the sheet:
  //   Matrícula: 723185
  //   Autor: Danielle Dias Vieira
  //   Exercício 04 - Máquina de Estados Finitos para reconhecer a sequência 1010
  //   Exercício 01 - Máquina de Estados Finitos segundo a abordagem de Mealy para sequência 1101
  //   Exercício 02 - Máquina de Estados Finitos segundo a abordagem de Moore para sequência 1101
  //   Exercício 03 - Máquina de Estados Finitos segundo a abordagem de Mealy e Moore para sequência 1101
  //   Exercício 06 - Moore para reconhecer apenas 3 sequencias de 1010 com interseção
  //   Exercício 07 - Máquina de Estados Finitos para sequencias 0000 ou 1000
  //   Exercício 08 - Máquina de Estados Finitos para sequências 101 ou 010
  //   Exercício 05 - Máquina de Estados Finitos segundo abordagem de Mealy sem interseção para reconhecer 2 vezes a sequência 1010
endmodule
