// Logisim project Exercicio1302.circ as structural Verilog: 1 circuit, main circuit main
module main (
  input  IN,
  input  CLR,
  input  pulse
);

  wire j_k_ff_1_qn, j_k_ff_2_q, j_k_ff_2_qn, j_k_ff_3_q, j_k_ff_3_qn, j_k_ff_4_q, j_k_ff_4_qn, j_k_ff_5_q,
       j_k_ff_5_qn;

  // Probe on j_k_ff_1_qn
  J_K_Flip_Flop j_k_ff_1 (.J(IN), .clk(j_k_ff_2_q), .K(IN), .Qn(j_k_ff_1_qn), .reset(CLR));  // open: Q, preset
  J_K_Flip_Flop j_k_ff_2 (
    .J(IN), .clk(j_k_ff_3_q), .K(IN), .Q(j_k_ff_2_q), .Qn(j_k_ff_2_qn), .reset(CLR));  // open: preset
  // Probe on j_k_ff_2_qn
  // Probe on j_k_ff_3_qn
  J_K_Flip_Flop j_k_ff_3 (
    .J(IN), .clk(j_k_ff_4_q), .K(IN), .Q(j_k_ff_3_q), .Qn(j_k_ff_3_qn), .reset(CLR));  // open: preset
  // Probe on j_k_ff_4_qn
  J_K_Flip_Flop j_k_ff_4 (
    .J(IN), .clk(j_k_ff_5_q), .K(IN), .Q(j_k_ff_4_q), .Qn(j_k_ff_4_qn), .reset(CLR));  // open: preset
  // Probe on j_k_ff_5_qn
  J_K_Flip_Flop j_k_ff_5 (.J(IN), .clk(pulse), .K(IN), .Q(j_k_ff_5_q), .Qn(j_k_ff_5_qn), .reset(CLR));  // open: preset
endmodule
