// Logisim project Exercicio1303.circ as structural Verilog: 1 circuit, main circuit main
module main (
  input  IN,
  input  pulse,
  input  CLR
);

  wire and_1_out, j_k_ff_1_q, j_k_ff_1_qn, j_k_ff_2_q, j_k_ff_2_qn, j_k_ff_3_q, j_k_ff_3_qn, j_k_ff_4_q,
       not_1_out, not_2_out, or_1_out;

  and and_1 (and_1_out, not_1_out, j_k_ff_2_q, not_2_out, j_k_ff_4_q);
  J_K_Flip_Flop j_k_ff_1 (
    .J(IN), .clk(pulse), .K(IN), .Q(j_k_ff_1_q), .Qn(j_k_ff_1_qn), .reset(or_1_out));  // open: preset
  or or_1 (or_1_out, CLR, and_1_out);
  not not_1 (not_1_out, j_k_ff_1_q);
  not not_2 (not_2_out, j_k_ff_3_q);
  J_K_Flip_Flop j_k_ff_2 (
    .J(IN), .clk(j_k_ff_1_qn), .K(IN), .Q(j_k_ff_2_q), .Qn(j_k_ff_2_qn), .reset(or_1_out));  // open: preset
  // Probe on j_k_ff_4_q
  J_K_Flip_Flop #(.trigger("falling")) j_k_ff_3 (
    .J(IN), .clk(j_k_ff_2_qn), .K(IN), .Q(j_k_ff_3_q), .Qn(j_k_ff_3_qn), .reset(or_1_out));  // open: preset
  // Probe on j_k_ff_3_q
  // Probe on j_k_ff_2_q
  // Probe on j_k_ff_1_q
  J_K_Flip_Flop j_k_ff_4 (.J(IN), .clk(j_k_ff_3_qn), .K(IN), .Q(j_k_ff_4_q), .reset(or_1_out));  // open: Qn, preset
endmodule
