// Logisim project Exercicio1304.circ as structural Verilog: 1 circuit, main circuit main
module main (
  input  IN,
  input  pulse
);

  wire and_1_out, j_k_ff_1_q, j_k_ff_1_qn, j_k_ff_2_q, j_k_ff_2_qn, j_k_ff_3_q, j_k_ff_3_qn, j_k_ff_4_q,
       j_k_ff_4_qn, not_1_out, not_2_out, not_3_out, or_1_out;

  not not_1 (not_1_out, IN);
  or or_1 (or_1_out, not_1_out, and_1_out);
  not not_2 (not_2_out, j_k_ff_1_qn);
  and and_1 (and_1_out, not_2_out, j_k_ff_2_qn, not_3_out, j_k_ff_4_qn);
  not not_3 (not_3_out, j_k_ff_3_qn);
  J_K_Flip_Flop #(.Pre_Clr_Positions("BELOW_ABOVE")) j_k_ff_1 (
    .J(IN), .clk(pulse), .K(IN), .Q(j_k_ff_1_q), .Qn(j_k_ff_1_qn), .preset(or_1_out));  // open: reset
  J_K_Flip_Flop #(.Pre_Clr_Positions("BELOW_ABOVE")) j_k_ff_2 (
    .J(IN), .clk(j_k_ff_1_q), .K(IN), .Q(j_k_ff_2_q), .Qn(j_k_ff_2_qn), .preset(or_1_out));  // open: reset
  // Probe on j_k_ff_4_q
  // Probe on j_k_ff_3_q
  J_K_Flip_Flop #(.trigger("falling"), .Pre_Clr_Positions("BELOW_ABOVE")) j_k_ff_3 (
    .J(IN), .clk(j_k_ff_2_q), .K(IN), .Q(j_k_ff_3_q), .Qn(j_k_ff_3_qn), .preset(or_1_out));  // open: reset
  // Probe on j_k_ff_2_q
  J_K_Flip_Flop #(.Pre_Clr_Positions("BELOW_ABOVE")) j_k_ff_4 (
    .J(IN), .clk(j_k_ff_3_q), .K(IN), .Q(j_k_ff_4_q), .Qn(j_k_ff_4_qn), .preset(or_1_out));  // open: reset
  // Probe on j_k_ff_1_q
endmodule
