// Logisim project Exercicio1305.circ as structural Verilog: 1 circuit, main circuit main
module main (
  input  pulso,
  input  CLR
);

  wire and_1_out, or_1_out, t_ff_1_q, t_ff_2_q, t_ff_2_qn, t_ff_3_q, t_ff_3_qn;

  // Probe on t_ff_1_q
  T_Flip_Flop t_ff_1 (.clk(t_ff_2_qn), .T(t_ff_2_qn), .Q(t_ff_1_q));  // open: Qn, preset, reset
  or or_1 (or_1_out, CLR, and_1_out);
  and and_1 (and_1_out, t_ff_1_q, t_ff_2_q, t_ff_3_q);
  // Probe on t_ff_2_q
  T_Flip_Flop t_ff_2 (.clk(t_ff_3_qn), .T(t_ff_3_qn), .Q(t_ff_2_q), .Qn(t_ff_2_qn));  // open: preset, reset
  // Probe on t_ff_3_q
  T_Flip_Flop t_ff_3 (.clk(pulso), .T(pulso), .Q(t_ff_3_q), .Qn(t_ff_3_qn), .reset(or_1_out));  // open: preset
endmodule
