// Logisim project questao01.circ as structural Verilog: 1 circuit, main circuit main
module main (
  input  in_1,
  input  in_2,
  output out_3,
  output out_4,
  output out_5,
  output out_6,
  output out_7
);

  wire clock_1_out;

  Clock clock_1 (.out(clock_1_out));
  J_K_Flip_Flop #(.Pre_Clr_Positions("LEGACY"), .enable("true"), .NewFFLayout("false")) j_k_ff_1 (
    .J(in_1), .clk(out_4), .K(in_1), .Qn(out_3));  // open: Q, preset, en, reset
  J_K_Flip_Flop #(.Pre_Clr_Positions("LEGACY"), .enable("true"), .NewFFLayout("false")) j_k_ff_2 (
    .J(in_1), .clk(out_5), .K(in_1), .Qn(out_4));  // open: Q, preset, en, reset
  J_K_Flip_Flop #(.Pre_Clr_Positions("LEGACY"), .enable("true"), .NewFFLayout("false")) j_k_ff_3 (
    .J(in_1), .clk(out_6), .K(in_1), .Qn(out_5));  // open: Q, preset, en, reset
  J_K_Flip_Flop #(.Pre_Clr_Positions("LEGACY"), .enable("true"), .NewFFLayout("false")) j_k_ff_4 (
    .J(in_1), .clk(out_7), .K(in_1), .Qn(out_6));  // open: Q, preset, en, reset
  J_K_Flip_Flop #(.Pre_Clr_Positions("LEGACY"), .enable("true"), .NewFFLayout("false")) j_k_ff_5 (
    .J(in_1), .clk(clock_1_out), .K(in_1), .Qn(out_7), .reset(in_2));  // open: Q, preset, en
endmodule
