// Logisim project questao04.circ as structural Verilog: 1 circuit, main circuit main
module main (
  input  in_1,
  output out_2,
  output out_3,
  output out_4,
  output out_5
);

  wire and_1_out, clock_1_out, j_k_ff_1_qn, j_k_ff_2_qn, j_k_ff_3_qn, j_k_ff_4_qn, not_1_out, not_2_out,
       not_3_out, or_1_out;

  Clock clock_1 (.out(clock_1_out));
  not not_1 (not_1_out, in_1);
  or or_1 (or_1_out, not_1_out, and_1_out);
  not not_2 (not_2_out, j_k_ff_1_qn);
  and and_1 (and_1_out, not_2_out, j_k_ff_2_qn, not_3_out, j_k_ff_4_qn);
  not not_3 (not_3_out, j_k_ff_3_qn);
  J_K_Flip_Flop #(.Pre_Clr_Positions("LEGACY"), .enable("true"), .NewFFLayout("false")) j_k_ff_1 (
    .J(in_1), .clk(clock_1_out), .K(in_1), .Q(out_5), .Qn(j_k_ff_1_qn), .preset(or_1_out));  // open: en, reset
  J_K_Flip_Flop #(.Pre_Clr_Positions("LEGACY"), .enable("true"), .NewFFLayout("false")) j_k_ff_2 (
    .J(in_1), .clk(out_5), .K(in_1), .Q(out_4), .Qn(j_k_ff_2_qn), .preset(or_1_out));  // open: en, reset
  J_K_Flip_Flop #(.Pre_Clr_Positions("LEGACY"), .enable("true"), .NewFFLayout("false")) j_k_ff_3 (
    .J(in_1), .clk(out_4), .K(in_1), .Q(out_3), .Qn(j_k_ff_3_qn), .preset(or_1_out));  // open: en, reset
  J_K_Flip_Flop #(.Pre_Clr_Positions("LEGACY"), .enable("true"), .NewFFLayout("false")) j_k_ff_4 (
    .J(in_1), .clk(out_3), .K(in_1), .Q(out_2), .Qn(j_k_ff_4_qn), .preset(or_1_out));  // open: en, reset
endmodule
