// Logisim project questao05.circ as structural Verilog: 1 circuit, main circuit main
module main (
  input  in_1,
  output out_2,
  output out_3,
  output out_4
);

  wire and_1_out, and_2_out, and_3_out, and_4_out, and_5_out, clock_1_out, or_1_out, or_2_out, or_3_out,
       t_ff_3_qn;

  Clock clock_1 (.out(clock_1_out));
  T_Flip_Flop #(.Pre_Clr_Positions("LEGACY"), .enable("true"), .NewFFLayout("false")) t_ff_1 (
    .clk(clock_1_out), .T(in_1), .Q(out_2));  // open: Qn, preset, reset, en
  and and_1 (and_1_out, t_ff_3_qn, out_2);
  and and_2 (and_2_out, out_4, out_3);
  T_Flip_Flop #(.Pre_Clr_Positions("LEGACY"), .enable("true"), .NewFFLayout("false")) t_ff_2 (
    .clk(clock_1_out), .T(or_1_out), .Q(out_3));  // open: Qn, preset, reset, en
  or or_1 (or_1_out, and_1_out, and_2_out);
  and and_3 (and_3_out, out_2, out_3);
  and and_4 (and_4_out, out_2, out_4);
  and and_5 (and_5_out, out_4, out_3);
  or or_2 (or_2_out, and_3_out, and_4_out);
  T_Flip_Flop #(.Pre_Clr_Positions("LEGACY"), .enable("true"), .NewFFLayout("false")) t_ff_3 (
    .clk(clock_1_out), .T(or_3_out), .Q(out_4), .Qn(t_ff_3_qn));  // open: preset, reset, en
  or or_3 (or_3_out, or_2_out, and_5_out);
endmodule
